// Logisim project COMPUTER1.circ as structural Verilog: 15 circuits, main circuit main
module main (
  input  in_1,
  input  in_2,
  input  in_3,
  input  [7:0] in_4,
  input  in_5,
  input  in_6,
  input  in_7,
  input  in_8,
  input  in_9,
  input  in_10,
  input  in_11,
  input  in_12,
  input  in_13,
  input  in_14,
  input  in_15,
  output [7:0] out_16
);

  wire and_1_out, and_2_out, and_3_out, and_4_out, and_5_out, and_6_out, and_7_out, and_8_out, and_9_out,
       b_smallmemory_1_out_10, b_smallmemory_1_out_11, b_smallmemory_1_out_12, b_smallmemory_1_out_13,
       b_smallmemory_1_out_14, b_smallmemory_1_out_15, b_smallmemory_1_out_16, b_smallmemory_1_out_17,
       b_smallmemory_2_out_10, b_smallmemory_2_out_11, b_smallmemory_2_out_12, b_smallmemory_2_out_13,
       b_smallmemory_2_out_14, b_smallmemory_2_out_15, b_smallmemory_2_out_16, b_smallmemory_2_out_17,
       b_smallmemory_3_out_10, b_smallmemory_3_out_11, b_smallmemory_3_out_12, b_smallmemory_3_out_13,
       b_smallmemory_3_out_14, b_smallmemory_3_out_15, b_smallmemory_3_out_16, b_smallmemory_3_out_17;
  wire [7:0] controlled_buffer_1_out, e_andgroub_1_out_10, e_andgroub_2_out_10, e_andgroub_3_out_10;

  and and_1 (and_1_out, in_1, in_2);
  and and_2 (and_2_out, in_8, in_9);
  and and_3 (and_3_out, in_12, in_13);
  and and_4 (and_4_out, and_1_out, in_5);
  and and_5 (and_5_out, and_1_out, in_7);
  and and_6 (and_6_out, and_2_out, in_10);
  and and_7 (and_7_out, and_2_out, in_11);
  and and_8 (and_8_out, and_3_out, in_14);
  and and_9 (and_9_out, and_3_out, in_15);
  B_smallmemory b_smallmemory_1 (
    .in_1(controlled_buffer_1_out[0]), .in_2(controlled_buffer_1_out[1]), .in_3(controlled_buffer_1_out[2]),
    .in_4(controlled_buffer_1_out[3]), .in_5(controlled_buffer_1_out[4]), .in_6(controlled_buffer_1_out[5]),
    .in_7(controlled_buffer_1_out[6]), .in_8(controlled_buffer_1_out[7]), .S(and_4_out),
    .out_10(b_smallmemory_1_out_10), .out_11(b_smallmemory_1_out_11), .out_12(b_smallmemory_1_out_12),
    .out_13(b_smallmemory_1_out_13), .out_14(b_smallmemory_1_out_14), .out_15(b_smallmemory_1_out_15),
    .out_16(b_smallmemory_1_out_16), .out_17(b_smallmemory_1_out_17));
  B_smallmemory b_smallmemory_2 (
    .in_1(controlled_buffer_1_out[0]), .in_2(controlled_buffer_1_out[1]), .in_3(controlled_buffer_1_out[2]),
    .in_4(controlled_buffer_1_out[3]), .in_5(controlled_buffer_1_out[4]), .in_6(controlled_buffer_1_out[5]),
    .in_7(controlled_buffer_1_out[6]), .in_8(controlled_buffer_1_out[7]), .S(and_6_out),
    .out_10(b_smallmemory_2_out_10), .out_11(b_smallmemory_2_out_11), .out_12(b_smallmemory_2_out_12),
    .out_13(b_smallmemory_2_out_13), .out_14(b_smallmemory_2_out_14), .out_15(b_smallmemory_2_out_15),
    .out_16(b_smallmemory_2_out_16), .out_17(b_smallmemory_2_out_17));
  B_smallmemory b_smallmemory_3 (
    .in_1(controlled_buffer_1_out[0]), .in_2(controlled_buffer_1_out[1]), .in_3(controlled_buffer_1_out[2]),
    .in_4(controlled_buffer_1_out[3]), .in_5(controlled_buffer_1_out[4]), .in_6(controlled_buffer_1_out[5]),
    .in_7(controlled_buffer_1_out[6]), .in_8(controlled_buffer_1_out[7]), .S(and_8_out),
    .out_10(b_smallmemory_3_out_10), .out_11(b_smallmemory_3_out_11), .out_12(b_smallmemory_3_out_12),
    .out_13(b_smallmemory_3_out_13), .out_14(b_smallmemory_3_out_14), .out_15(b_smallmemory_3_out_15),
    .out_16(b_smallmemory_3_out_16), .out_17(b_smallmemory_3_out_17));
  E_andgroub e_andgroub_1 (
    .in_1(b_smallmemory_1_out_10), .in_2(b_smallmemory_1_out_11), .in_3(b_smallmemory_1_out_12),
    .in_4(b_smallmemory_1_out_13), .in_5(b_smallmemory_1_out_14), .in_6(b_smallmemory_1_out_15),
    .in_7(b_smallmemory_1_out_16), .in_8(b_smallmemory_1_out_17), .in_9(and_5_out),
    .out_10(e_andgroub_1_out_10[0]), .out_11(e_andgroub_1_out_10[1]), .out_12(e_andgroub_1_out_10[2]),
    .out_13(e_andgroub_1_out_10[3]), .out_14(e_andgroub_1_out_10[4]), .out_15(e_andgroub_1_out_10[5]),
    .out_16(e_andgroub_1_out_10[6]), .out_17(e_andgroub_1_out_10[7]));
  E_andgroub e_andgroub_2 (
    .in_1(b_smallmemory_2_out_10), .in_2(b_smallmemory_2_out_11), .in_3(b_smallmemory_2_out_12),
    .in_4(b_smallmemory_2_out_13), .in_5(b_smallmemory_2_out_14), .in_6(b_smallmemory_2_out_15),
    .in_7(b_smallmemory_2_out_16), .in_8(b_smallmemory_2_out_17), .in_9(and_7_out),
    .out_10(e_andgroub_2_out_10[0]), .out_11(e_andgroub_2_out_10[1]), .out_12(e_andgroub_2_out_10[2]),
    .out_13(e_andgroub_2_out_10[3]), .out_14(e_andgroub_2_out_10[4]), .out_15(e_andgroub_2_out_10[5]),
    .out_16(e_andgroub_2_out_10[6]), .out_17(e_andgroub_2_out_10[7]));
  E_andgroub e_andgroub_3 (
    .in_1(b_smallmemory_3_out_10), .in_2(b_smallmemory_3_out_11), .in_3(b_smallmemory_3_out_12),
    .in_4(b_smallmemory_3_out_13), .in_5(b_smallmemory_3_out_14), .in_6(b_smallmemory_3_out_15),
    .in_7(b_smallmemory_3_out_16), .in_8(b_smallmemory_3_out_17), .in_9(and_9_out),
    .out_10(e_andgroub_3_out_10[0]), .out_11(e_andgroub_3_out_10[1]), .out_12(e_andgroub_3_out_10[2]),
    .out_13(e_andgroub_3_out_10[3]), .out_14(e_andgroub_3_out_10[4]), .out_15(e_andgroub_3_out_10[5]),
    .out_16(e_andgroub_3_out_10[6]), .out_17(e_andgroub_3_out_10[7]));
  assign controlled_buffer_1_out = and_5_out ? e_andgroub_1_out_10 : 8'bz;  // Controlled_Buffer controlled_buffer_1
  assign controlled_buffer_1_out = and_7_out ? e_andgroub_2_out_10 : 8'bz;  // Controlled_Buffer controlled_buffer_2
  assign controlled_buffer_1_out = and_9_out ? e_andgroub_3_out_10 : 8'bz;  // Controlled_Buffer controlled_buffer_3
  assign out_16 = in_3 ? controlled_buffer_1_out : 8'bz;  // Controlled_Buffer controlled_buffer_4
  assign controlled_buffer_1_out = in_6 ? in_4 : 8'bz;  // Controlled_Buffer controlled_buffer_5
endmodule

module B_smallmemory (
  input  in_1,
  input  in_2,
  input  in_3,
  input  in_4,
  input  in_5,
  input  in_6,
  input  in_7,
  input  in_8,
  input  S,
  output out_10,
  output out_11,
  output out_12,
  output out_13,
  output out_14,
  output out_15,
  output out_16,
  output out_17
);

  D_Flip_Flop d_ff_1 (.clk(S), .D(in_1), .Q(out_10));  // open: Qn, preset, en, reset
  D_Flip_Flop d_ff_2 (.clk(S), .D(in_2), .Q(out_11));  // open: Qn, preset, en, reset
  D_Flip_Flop d_ff_3 (.clk(S), .D(in_3), .Q(out_12));  // open: Qn, preset, en, reset
  D_Flip_Flop d_ff_4 (.clk(S), .D(in_4), .Q(out_13));  // open: Qn, preset, en, reset
  D_Flip_Flop d_ff_5 (.clk(S), .D(in_5), .Q(out_14));  // open: Qn, preset, en, reset
  D_Flip_Flop d_ff_6 (.clk(S), .D(in_6), .Q(out_15));  // open: Qn, preset, en, reset
  D_Flip_Flop d_ff_7 (.clk(S), .D(in_7), .Q(out_16));  // open: Qn, preset, en, reset
  D_Flip_Flop d_ff_8 (.clk(S), .D(in_8), .Q(out_17));  // open: Qn, preset, en, reset
endmodule

module E_andgroub (
  input  in_1,
  input  in_2,
  input  in_3,
  input  in_4,
  input  in_5,
  input  in_6,
  input  in_7,
  input  in_8,
  input  in_9,
  output out_10,
  output out_11,
  output out_12,
  output out_13,
  output out_14,
  output out_15,
  output out_16,
  output out_17
);

  and and_1 (out_10, in_1, in_9);
  and and_2 (out_11, in_2, in_9);
  and and_3 (out_12, in_3, in_9);
  and and_4 (out_13, in_4, in_9);
  and and_5 (out_14, in_5, in_9);
  and and_6 (out_15, in_6, in_9);
  and and_7 (out_16, in_7, in_9);
  and and_8 (out_17, in_8, in_9);
endmodule

module R (
  input  [7:0] in_1,
  input  in_2,
  input  in_3,
  output [7:0] out_4
);

  wire b_smallmemory_1_out_10, b_smallmemory_1_out_11, b_smallmemory_1_out_12, b_smallmemory_1_out_13,
       b_smallmemory_1_out_14, b_smallmemory_1_out_15, b_smallmemory_1_out_16, b_smallmemory_1_out_17;

  B_smallmemory b_smallmemory_1 (
    .in_1(in_1[0]), .in_2(in_1[1]), .in_3(in_1[2]), .in_4(in_1[3]), .in_5(in_1[4]), .in_6(in_1[5]),
    .in_7(in_1[6]), .in_8(in_1[7]), .S(in_2), .out_10(b_smallmemory_1_out_10),
    .out_11(b_smallmemory_1_out_11), .out_12(b_smallmemory_1_out_12), .out_13(b_smallmemory_1_out_13),
    .out_14(b_smallmemory_1_out_14), .out_15(b_smallmemory_1_out_15), .out_16(b_smallmemory_1_out_16),
    .out_17(b_smallmemory_1_out_17));
  E_andgroub e_andgroub_1 (
    .in_1(b_smallmemory_1_out_10), .in_2(b_smallmemory_1_out_11), .in_3(b_smallmemory_1_out_12),
    .in_4(b_smallmemory_1_out_13), .in_5(b_smallmemory_1_out_14), .in_6(b_smallmemory_1_out_15),
    .in_7(b_smallmemory_1_out_16), .in_8(b_smallmemory_1_out_17), .in_9(in_3), .out_10(out_4[0]),
    .out_11(out_4[1]), .out_12(out_4[2]), .out_13(out_4[3]), .out_14(out_4[4]), .out_15(out_4[5]),
    .out_16(out_4[6]), .out_17(out_4[7]));
endmodule

module R1 (
  input  in_1,
  input  in_2,
  output [7:0] out_3
);

  wire b_smallmemory_1_out_10, b_smallmemory_1_out_11, b_smallmemory_1_out_12, b_smallmemory_1_out_13,
       b_smallmemory_1_out_14, b_smallmemory_1_out_15, b_smallmemory_1_out_16, b_smallmemory_1_out_17;
  wire [7:0] e_andgroub_1_out_10;

  B_smallmemory b_smallmemory_1 (
    .in_1(out_3[0]), .in_2(out_3[1]), .in_3(out_3[2]), .in_4(out_3[3]), .in_5(out_3[4]), .in_6(out_3[5]),
    .in_7(out_3[6]), .in_8(out_3[7]), .S(in_1), .out_10(b_smallmemory_1_out_10),
    .out_11(b_smallmemory_1_out_11), .out_12(b_smallmemory_1_out_12), .out_13(b_smallmemory_1_out_13),
    .out_14(b_smallmemory_1_out_14), .out_15(b_smallmemory_1_out_15), .out_16(b_smallmemory_1_out_16),
    .out_17(b_smallmemory_1_out_17));
  E_andgroub e_andgroub_1 (
    .in_1(b_smallmemory_1_out_10), .in_2(b_smallmemory_1_out_11), .in_3(b_smallmemory_1_out_12),
    .in_4(b_smallmemory_1_out_13), .in_5(b_smallmemory_1_out_14), .in_6(b_smallmemory_1_out_15),
    .in_7(b_smallmemory_1_out_16), .in_8(b_smallmemory_1_out_17), .in_9(in_2),
    .out_10(e_andgroub_1_out_10[0]), .out_11(e_andgroub_1_out_10[1]), .out_12(e_andgroub_1_out_10[2]),
    .out_13(e_andgroub_1_out_10[3]), .out_14(e_andgroub_1_out_10[4]), .out_15(e_andgroub_1_out_10[5]),
    .out_16(e_andgroub_1_out_10[6]), .out_17(e_andgroub_1_out_10[7]));
  assign out_3 = in_2 ? e_andgroub_1_out_10 : 8'bz;  // Controlled_Buffer controlled_buffer_1
endmodule

module RAM (
  input  [7:0] in_1,
  input  [7:0] in_2,
  input  in_3,
  input  in_4,
  input  S,
  input  R,
  input  [7:0] in_7,
  input  in_8,
  input  in_9,
  output [7:0] out_10,
  output [7:0] out_11
);

  wire decoder_1_out0, decoder_1_out1, decoder_1_out2, decoder_1_out3, decoder_1_out4, decoder_1_out5,
       decoder_1_out6, decoder_1_out7, decoder_1_out8, decoder_1_out9, decoder_1_out10, decoder_1_out11,
       decoder_1_out12, decoder_1_out13, decoder_1_out14, decoder_1_out15, decoder_2_out0, decoder_2_out1,
       decoder_2_out2, decoder_2_out3, decoder_2_out4, decoder_2_out5, decoder_2_out6, decoder_2_out7,
       decoder_2_out8, decoder_2_out9, decoder_2_out10, decoder_2_out11, decoder_2_out12, decoder_2_out13,
       decoder_2_out14, decoder_2_out15, undriven, undriven_2, undriven_3, undriven_4, undriven_5,
       undriven_6, undriven_7, undriven_8, undriven_9, undriven_10, undriven_11, undriven_12, undriven_13,
       undriven_14, undriven_15, undriven_16, undriven_17, undriven_18, undriven_19, undriven_20,
       undriven_21, undriven_22, undriven_23, undriven_24, undriven_25, undriven_26, undriven_27,
       undriven_28, undriven_29, undriven_30, undriven_31, undriven_32, undriven_33, undriven_34,
       undriven_35, undriven_36, undriven_37, undriven_38, undriven_39, undriven_40, undriven_41,
       undriven_42, undriven_43, undriven_44, undriven_45, undriven_46, undriven_47, undriven_48,
       undriven_49, undriven_50, undriven_51, undriven_52, undriven_53, undriven_54, undriven_55,
       undriven_56, undriven_57, undriven_58, undriven_59, undriven_60, undriven_61, undriven_62,
       undriven_63, undriven_64, undriven_65, undriven_66, undriven_67, undriven_68, undriven_69,
       undriven_70, undriven_71, undriven_72, undriven_73, undriven_74, undriven_75, undriven_76,
       undriven_77, undriven_78, undriven_79, undriven_80, undriven_81, undriven_82, undriven_83,
       undriven_84, undriven_85, undriven_86, undriven_87, undriven_88, undriven_89, undriven_90,
       undriven_91, undriven_92, undriven_93, undriven_94, undriven_95, undriven_96, undriven_97,
       undriven_98, undriven_99, undriven_100, undriven_101, undriven_102, undriven_103, undriven_104,
       undriven_105, undriven_106, undriven_107, undriven_108, undriven_109, undriven_110, undriven_111,
       undriven_112, undriven_113, undriven_114, undriven_115, undriven_116, undriven_117, undriven_118,
       undriven_119, undriven_120, undriven_121, undriven_122, undriven_123, undriven_124, undriven_125,
       undriven_126, undriven_127, undriven_128, undriven_129, undriven_130, undriven_131, undriven_132,
       undriven_133, undriven_134, undriven_135, undriven_136, undriven_137, undriven_138, undriven_139,
       undriven_140, undriven_141, undriven_142, undriven_143, undriven_144, undriven_145, undriven_146,
       undriven_147, undriven_148, undriven_149, undriven_150, undriven_151, undriven_152, undriven_153,
       undriven_154, undriven_155, undriven_156, undriven_157, undriven_158, undriven_159, undriven_160,
       undriven_161, undriven_162, undriven_163, undriven_164, undriven_165, undriven_166, undriven_167,
       undriven_168, undriven_169, undriven_170, undriven_171, undriven_172, undriven_173, undriven_174,
       undriven_175, undriven_176, undriven_177, undriven_178, undriven_179, undriven_180, undriven_181,
       undriven_182, undriven_183, undriven_184, undriven_185, undriven_186, undriven_187, undriven_188,
       undriven_189, undriven_190, undriven_191, undriven_192, undriven_193, undriven_194, undriven_195,
       undriven_196, undriven_197, undriven_198, undriven_199, undriven_200, undriven_201, undriven_202,
       undriven_203, undriven_204, undriven_205, undriven_206, undriven_207, undriven_208, undriven_209,
       undriven_210, undriven_211, undriven_212, undriven_213, undriven_214;
  wire [7:0] r_for_ram_1_out_6;

  R r_1 (.in_1(in_2), .in_2(in_3), .in_3(in_4), .out_4(out_10));
  Decoder #(.select(4)) decoder_1 (
    .out0(decoder_1_out0), .out1(decoder_1_out1), .out2(decoder_1_out2), .out3(decoder_1_out3),
    .out4(decoder_1_out4), .out5(decoder_1_out5), .out6(decoder_1_out6), .out7(decoder_1_out7),
    .out8(decoder_1_out8), .out9(decoder_1_out9), .out10(decoder_1_out10), .out11(decoder_1_out11),
    .out12(decoder_1_out12), .out13(decoder_1_out13), .out14(decoder_1_out14), .out15(decoder_1_out15),
    .sel(out_10[7:4]));  // open: en
  R_for_RAM r_for_ram_1 (
    .in_2(decoder_1_out0), .in_3(decoder_2_out0), .in_4(S), .in_5(R), .out_6(r_for_ram_1_out_6), .in_1(in_1));
  R_for_RAM r_for_ram_2 (
    .in_2(decoder_1_out1), .in_3(decoder_2_out0), .in_4(S), .out_6(r_for_ram_1_out_6), .in_1(in_1));  // open: in_5
  R_for_RAM r_for_ram_3 (
    .in_2(decoder_1_out2), .in_3(decoder_2_out0), .in_4(S), .out_6(r_for_ram_1_out_6));  // open: in_5, in_1
  R_for_RAM r_for_ram_4 (
    .in_2(decoder_1_out3), .in_3(decoder_2_out0), .in_4(S), .out_6(r_for_ram_1_out_6));  // open: in_5, in_1
  R_for_RAM r_for_ram_5 (
    .in_2(decoder_1_out4), .in_3(decoder_2_out0), .in_4(S), .out_6(r_for_ram_1_out_6));  // open: in_5, in_1
  R_for_RAM r_for_ram_6 (
    .in_2(decoder_1_out5), .in_3(decoder_2_out0), .in_4(S), .out_6(r_for_ram_1_out_6));  // open: in_5, in_1
  R_for_RAM r_for_ram_7 (
    .in_2(decoder_1_out6), .in_3(decoder_2_out0), .in_4(S), .out_6(r_for_ram_1_out_6));  // open: in_5, in_1
  R_for_RAM r_for_ram_8 (
    .in_2(decoder_1_out7), .in_3(decoder_2_out0), .in_4(S), .out_6(r_for_ram_1_out_6));  // open: in_5, in_1
  R_for_RAM r_for_ram_9 (
    .in_2(decoder_1_out8), .in_3(decoder_2_out0), .in_4(S), .out_6(r_for_ram_1_out_6));  // open: in_5, in_1
  R_for_RAM r_for_ram_10 (
    .in_2(decoder_1_out9), .in_3(decoder_2_out0), .in_4(S), .out_6(r_for_ram_1_out_6));  // open: in_5, in_1
  R_for_RAM r_for_ram_11 (
    .in_2(decoder_1_out10), .in_3(decoder_2_out0), .in_4(S), .out_6(r_for_ram_1_out_6));  // open: in_5, in_1
  R_for_RAM r_for_ram_12 (
    .in_2(decoder_1_out11), .in_3(decoder_2_out0), .in_4(S), .out_6(r_for_ram_1_out_6));  // open: in_5, in_1
  R_for_RAM r_for_ram_13 (
    .in_2(decoder_1_out12), .in_3(decoder_2_out0), .in_4(S), .out_6(r_for_ram_1_out_6));  // open: in_5, in_1
  R_for_RAM r_for_ram_14 (
    .in_2(decoder_1_out13), .in_3(decoder_2_out0), .in_4(S), .out_6(r_for_ram_1_out_6));  // open: in_5, in_1
  R_for_RAM r_for_ram_15 (
    .in_2(decoder_1_out14), .in_3(decoder_2_out0), .in_4(S), .out_6(r_for_ram_1_out_6));  // open: in_5, in_1
  R_for_RAM r_for_ram_16 (
    .in_2(decoder_1_out15), .in_3(decoder_2_out0), .in_4(S), .out_6(r_for_ram_1_out_6));  // open: in_5, in_1
  Decoder #(.select(4)) decoder_2 (
    .out0(decoder_2_out0), .out1(decoder_2_out1), .out2(decoder_2_out2), .out3(decoder_2_out3),
    .out4(decoder_2_out4), .out5(decoder_2_out5), .out6(decoder_2_out6), .out7(decoder_2_out7),
    .out8(decoder_2_out8), .out9(decoder_2_out9), .out10(decoder_2_out10), .out11(decoder_2_out11),
    .out12(decoder_2_out12), .out13(decoder_2_out13), .out14(decoder_2_out14), .out15(decoder_2_out15),
    .sel(out_10[3:0]));  // open: en
  R_for_RAM r_for_ram_17 (
    .in_2(decoder_1_out0), .in_3(decoder_2_out1), .in_4(S), .in_5(R), .out_6(r_for_ram_1_out_6), .in_1(in_1));
  R_for_RAM r_for_ram_18 (
    .in_2(decoder_1_out1), .in_3(decoder_2_out1), .in_4(S), .in_5(R), .out_6(r_for_ram_1_out_6), .in_1(in_1));
  R_for_RAM r_for_ram_19 (
    .in_2(decoder_1_out2), .in_3(decoder_2_out1), .in_4(undriven), .out_6(r_for_ram_1_out_6));  // open: in_5, in_1
  R_for_RAM r_for_ram_20 (
    .in_2(decoder_1_out3), .in_3(decoder_2_out1), .in_4(undriven_2), .out_6(r_for_ram_1_out_6));  // open: in_5, in_1
  R_for_RAM r_for_ram_21 (
    .in_2(decoder_1_out4), .in_3(decoder_2_out1), .in_4(undriven_3), .out_6(r_for_ram_1_out_6));  // open: in_5, in_1
  R_for_RAM r_for_ram_22 (
    .in_2(decoder_1_out5), .in_3(decoder_2_out1), .in_4(undriven_4), .out_6(r_for_ram_1_out_6));  // open: in_5, in_1
  R_for_RAM r_for_ram_23 (
    .in_2(decoder_1_out6), .in_3(decoder_2_out1), .in_4(undriven_5), .out_6(r_for_ram_1_out_6));  // open: in_5, in_1
  R_for_RAM r_for_ram_24 (
    .in_2(decoder_1_out7), .in_3(decoder_2_out1), .in_4(undriven_6), .out_6(r_for_ram_1_out_6));  // open: in_5, in_1
  R_for_RAM r_for_ram_25 (
    .in_2(decoder_1_out8), .in_3(decoder_2_out1), .in_4(undriven_7), .out_6(r_for_ram_1_out_6));  // open: in_5, in_1
  R_for_RAM r_for_ram_26 (
    .in_2(decoder_1_out9), .in_3(decoder_2_out1), .in_4(undriven_8), .out_6(r_for_ram_1_out_6));  // open: in_5, in_1
  R_for_RAM r_for_ram_27 (
    .in_2(decoder_1_out10), .in_3(decoder_2_out1), .in_4(undriven_9), .out_6(r_for_ram_1_out_6));  // open: in_5, in_1
  R_for_RAM r_for_ram_28 (
    .in_2(decoder_1_out11), .in_3(decoder_2_out1), .in_4(undriven_10), .out_6(r_for_ram_1_out_6));  // open: in_5, in_1
  R_for_RAM r_for_ram_29 (
    .in_2(decoder_1_out12), .in_3(decoder_2_out1), .in_4(undriven_11), .out_6(r_for_ram_1_out_6));  // open: in_5, in_1
  R_for_RAM r_for_ram_30 (
    .in_2(decoder_1_out13), .in_3(decoder_2_out1), .in_4(undriven_12), .out_6(r_for_ram_1_out_6));  // open: in_5, in_1
  R_for_RAM r_for_ram_31 (
    .in_2(decoder_1_out14), .in_3(decoder_2_out1), .in_4(undriven_13), .out_6(r_for_ram_1_out_6));  // open: in_5, in_1
  R_for_RAM r_for_ram_32 (
    .in_2(decoder_1_out15), .in_3(decoder_2_out1), .in_4(undriven_14), .out_6(r_for_ram_1_out_6));  // open: in_5, in_1
  R_for_RAM r_for_ram_33 (
    .in_2(decoder_1_out0), .in_3(decoder_2_out2), .in_4(S), .in_5(R), .out_6(r_for_ram_1_out_6), .in_1(in_1));
  R_for_RAM r_for_ram_34 (
    .in_2(decoder_1_out1), .in_3(decoder_2_out2), .in_4(S), .in_5(R), .out_6(r_for_ram_1_out_6), .in_1(in_1));
  R_for_RAM r_for_ram_35 (
    .in_2(decoder_1_out2), .in_3(decoder_2_out2), .in_4(undriven_15), .out_6(r_for_ram_1_out_6));  // open: in_5, in_1
  R_for_RAM r_for_ram_36 (
    .in_2(decoder_1_out3), .in_3(decoder_2_out2), .in_4(undriven_16), .out_6(r_for_ram_1_out_6));  // open: in_5, in_1
  R_for_RAM r_for_ram_37 (
    .in_2(decoder_1_out4), .in_3(decoder_2_out2), .in_4(undriven_17), .out_6(r_for_ram_1_out_6));  // open: in_5, in_1
  R_for_RAM r_for_ram_38 (
    .in_2(decoder_1_out5), .in_3(decoder_2_out2), .in_4(undriven_18), .out_6(r_for_ram_1_out_6));  // open: in_5, in_1
  R_for_RAM r_for_ram_39 (
    .in_2(decoder_1_out6), .in_3(decoder_2_out2), .in_4(undriven_19), .out_6(r_for_ram_1_out_6));  // open: in_5, in_1
  R_for_RAM r_for_ram_40 (
    .in_2(decoder_1_out7), .in_3(decoder_2_out2), .in_4(undriven_20), .out_6(r_for_ram_1_out_6));  // open: in_5, in_1
  R_for_RAM r_for_ram_41 (
    .in_2(decoder_1_out8), .in_3(decoder_2_out2), .in_4(undriven_21), .out_6(r_for_ram_1_out_6));  // open: in_5, in_1
  R_for_RAM r_for_ram_42 (
    .in_2(decoder_1_out9), .in_3(decoder_2_out2), .in_4(undriven_22), .out_6(r_for_ram_1_out_6));  // open: in_5, in_1
  R_for_RAM r_for_ram_43 (
    .in_2(decoder_1_out10), .in_3(decoder_2_out2), .in_4(undriven_23), .out_6(r_for_ram_1_out_6));  // open: in_5, in_1
  R_for_RAM r_for_ram_44 (
    .in_2(decoder_1_out11), .in_3(decoder_2_out2), .in_4(undriven_24), .out_6(r_for_ram_1_out_6));  // open: in_5, in_1
  R_for_RAM r_for_ram_45 (
    .in_2(decoder_1_out12), .in_3(decoder_2_out2), .in_4(undriven_25), .out_6(r_for_ram_1_out_6));  // open: in_5, in_1
  R_for_RAM r_for_ram_46 (
    .in_2(decoder_1_out13), .in_3(decoder_2_out2), .in_4(undriven_26), .out_6(r_for_ram_1_out_6));  // open: in_5, in_1
  R_for_RAM r_for_ram_47 (
    .in_2(decoder_1_out14), .in_3(decoder_2_out2), .in_4(undriven_27), .out_6(r_for_ram_1_out_6));  // open: in_5, in_1
  R_for_RAM r_for_ram_48 (
    .in_2(decoder_1_out15), .in_3(decoder_2_out2), .in_4(undriven_28), .out_6(r_for_ram_1_out_6));  // open: in_5, in_1
  R_for_RAM r_for_ram_49 (
    .in_2(decoder_1_out0), .in_3(decoder_2_out3), .in_4(undriven_29), .out_6(r_for_ram_1_out_6), .in_1(in_1));  // open: in_5
  R_for_RAM r_for_ram_50 (
    .in_2(decoder_1_out1), .in_3(decoder_2_out3), .in_4(S), .in_5(R), .out_6(r_for_ram_1_out_6), .in_1(in_1));
  R_for_RAM r_for_ram_51 (
    .in_2(decoder_1_out2), .in_3(decoder_2_out3), .in_4(undriven_30), .out_6(r_for_ram_1_out_6));  // open: in_5, in_1
  R_for_RAM r_for_ram_52 (
    .in_2(decoder_1_out3), .in_3(decoder_2_out3), .in_4(undriven_31), .out_6(r_for_ram_1_out_6));  // open: in_5, in_1
  R_for_RAM r_for_ram_53 (
    .in_2(decoder_1_out4), .in_3(decoder_2_out3), .in_4(undriven_32), .out_6(r_for_ram_1_out_6));  // open: in_5, in_1
  R_for_RAM r_for_ram_54 (
    .in_2(decoder_1_out5), .in_3(decoder_2_out3), .in_4(undriven_33), .out_6(r_for_ram_1_out_6));  // open: in_5, in_1
  R_for_RAM r_for_ram_55 (
    .in_2(decoder_1_out6), .in_3(decoder_2_out3), .in_4(undriven_34), .out_6(r_for_ram_1_out_6));  // open: in_5, in_1
  R_for_RAM r_for_ram_56 (
    .in_2(decoder_1_out7), .in_3(decoder_2_out3), .in_4(undriven_35), .out_6(r_for_ram_1_out_6));  // open: in_5, in_1
  R_for_RAM r_for_ram_57 (
    .in_2(decoder_1_out8), .in_3(decoder_2_out3), .in_4(undriven_36), .out_6(r_for_ram_1_out_6));  // open: in_5, in_1
  R_for_RAM r_for_ram_58 (
    .in_2(decoder_1_out9), .in_3(decoder_2_out3), .in_4(undriven_37), .out_6(r_for_ram_1_out_6));  // open: in_5, in_1
  R_for_RAM r_for_ram_59 (
    .in_2(decoder_1_out10), .in_3(decoder_2_out3), .in_4(undriven_38), .out_6(r_for_ram_1_out_6));  // open: in_5, in_1
  R_for_RAM r_for_ram_60 (
    .in_2(decoder_1_out11), .in_3(decoder_2_out3), .in_4(undriven_39), .out_6(r_for_ram_1_out_6));  // open: in_5, in_1
  R_for_RAM r_for_ram_61 (
    .in_2(decoder_1_out12), .in_3(decoder_2_out3), .in_4(undriven_40), .out_6(r_for_ram_1_out_6));  // open: in_5, in_1
  R_for_RAM r_for_ram_62 (
    .in_2(decoder_1_out13), .in_3(decoder_2_out3), .in_4(undriven_41), .out_6(r_for_ram_1_out_6));  // open: in_5, in_1
  R_for_RAM r_for_ram_63 (
    .in_2(decoder_1_out14), .in_3(decoder_2_out3), .in_4(undriven_42), .out_6(r_for_ram_1_out_6));  // open: in_5, in_1
  R_for_RAM r_for_ram_64 (
    .in_2(decoder_1_out15), .in_3(decoder_2_out3), .in_4(undriven_43), .out_6(r_for_ram_1_out_6));  // open: in_5, in_1
  R_for_RAM r_for_ram_65 (
    .in_2(decoder_1_out0), .in_3(decoder_2_out4), .in_4(undriven_44), .out_6(r_for_ram_1_out_6), .in_1(in_1));  // open: in_5
  R_for_RAM r_for_ram_66 (
    .in_2(decoder_1_out1), .in_3(decoder_2_out4), .in_4(S), .in_5(R), .out_6(r_for_ram_1_out_6), .in_1(in_1));
  R_for_RAM r_for_ram_67 (
    .in_2(decoder_1_out2), .in_3(decoder_2_out4), .in_4(undriven_45), .out_6(r_for_ram_1_out_6));  // open: in_5, in_1
  R_for_RAM r_for_ram_68 (
    .in_2(decoder_1_out3), .in_3(decoder_2_out4), .in_4(undriven_46), .out_6(r_for_ram_1_out_6));  // open: in_5, in_1
  R_for_RAM r_for_ram_69 (
    .in_2(decoder_1_out4), .in_3(decoder_2_out4), .in_4(undriven_47), .out_6(r_for_ram_1_out_6));  // open: in_5, in_1
  R_for_RAM r_for_ram_70 (
    .in_2(decoder_1_out5), .in_3(decoder_2_out4), .in_4(undriven_48), .out_6(r_for_ram_1_out_6));  // open: in_5, in_1
  R_for_RAM r_for_ram_71 (
    .in_2(decoder_1_out6), .in_3(decoder_2_out4), .in_4(undriven_49), .out_6(r_for_ram_1_out_6));  // open: in_5, in_1
  R_for_RAM r_for_ram_72 (
    .in_2(decoder_1_out7), .in_3(decoder_2_out4), .in_4(undriven_50), .out_6(r_for_ram_1_out_6));  // open: in_5, in_1
  R_for_RAM r_for_ram_73 (
    .in_2(decoder_1_out8), .in_3(decoder_2_out4), .in_4(undriven_51), .out_6(r_for_ram_1_out_6));  // open: in_5, in_1
  R_for_RAM r_for_ram_74 (
    .in_2(decoder_1_out9), .in_3(decoder_2_out4), .in_4(undriven_52), .out_6(r_for_ram_1_out_6));  // open: in_5, in_1
  R_for_RAM r_for_ram_75 (
    .in_2(decoder_1_out10), .in_3(decoder_2_out4), .in_4(undriven_53), .out_6(r_for_ram_1_out_6));  // open: in_5, in_1
  R_for_RAM r_for_ram_76 (
    .in_2(decoder_1_out11), .in_3(decoder_2_out4), .in_4(undriven_54), .out_6(r_for_ram_1_out_6));  // open: in_5, in_1
  R_for_RAM r_for_ram_77 (
    .in_2(decoder_1_out12), .in_3(decoder_2_out4), .in_4(undriven_55), .out_6(r_for_ram_1_out_6));  // open: in_5, in_1
  R_for_RAM r_for_ram_78 (
    .in_2(decoder_1_out13), .in_3(decoder_2_out4), .in_4(undriven_56), .out_6(r_for_ram_1_out_6));  // open: in_5, in_1
  R_for_RAM r_for_ram_79 (
    .in_2(decoder_1_out14), .in_3(decoder_2_out4), .in_4(undriven_57), .out_6(r_for_ram_1_out_6));  // open: in_5, in_1
  R_for_RAM r_for_ram_80 (
    .in_2(decoder_1_out15), .in_3(decoder_2_out4), .in_4(undriven_58), .out_6(r_for_ram_1_out_6));  // open: in_5, in_1
  R_for_RAM r_for_ram_81 (
    .in_2(decoder_1_out0), .in_3(decoder_2_out5), .in_4(undriven_59), .out_6(r_for_ram_1_out_6), .in_1(in_1));  // open: in_5
  R_for_RAM r_for_ram_82 (
    .in_2(decoder_1_out1), .in_3(decoder_2_out5), .in_4(S), .in_5(R), .out_6(r_for_ram_1_out_6), .in_1(in_1));
  R_for_RAM r_for_ram_83 (
    .in_2(decoder_1_out2), .in_3(decoder_2_out5), .in_4(undriven_60), .out_6(r_for_ram_1_out_6));  // open: in_5, in_1
  R_for_RAM r_for_ram_84 (
    .in_2(decoder_1_out3), .in_3(decoder_2_out5), .in_4(undriven_61), .out_6(r_for_ram_1_out_6));  // open: in_5, in_1
  R_for_RAM r_for_ram_85 (
    .in_2(decoder_1_out4), .in_3(decoder_2_out5), .in_4(undriven_62), .out_6(r_for_ram_1_out_6));  // open: in_5, in_1
  R_for_RAM r_for_ram_86 (
    .in_2(decoder_1_out5), .in_3(decoder_2_out5), .in_4(undriven_63), .out_6(r_for_ram_1_out_6));  // open: in_5, in_1
  R_for_RAM r_for_ram_87 (
    .in_2(decoder_1_out6), .in_3(decoder_2_out5), .in_4(undriven_64), .out_6(r_for_ram_1_out_6));  // open: in_5, in_1
  R_for_RAM r_for_ram_88 (
    .in_2(decoder_1_out7), .in_3(decoder_2_out5), .in_4(undriven_65), .out_6(r_for_ram_1_out_6));  // open: in_5, in_1
  R_for_RAM r_for_ram_89 (
    .in_2(decoder_1_out8), .in_3(decoder_2_out5), .in_4(undriven_66), .out_6(r_for_ram_1_out_6));  // open: in_5, in_1
  R_for_RAM r_for_ram_90 (
    .in_2(decoder_1_out9), .in_3(decoder_2_out5), .in_4(undriven_67), .out_6(r_for_ram_1_out_6));  // open: in_5, in_1
  R_for_RAM r_for_ram_91 (
    .in_2(decoder_1_out10), .in_3(decoder_2_out5), .in_4(undriven_68), .out_6(r_for_ram_1_out_6));  // open: in_5, in_1
  R_for_RAM r_for_ram_92 (
    .in_2(decoder_1_out11), .in_3(decoder_2_out5), .in_4(undriven_69), .out_6(r_for_ram_1_out_6));  // open: in_5, in_1
  R_for_RAM r_for_ram_93 (
    .in_2(decoder_1_out12), .in_3(decoder_2_out5), .in_4(undriven_70), .out_6(r_for_ram_1_out_6));  // open: in_5, in_1
  R_for_RAM r_for_ram_94 (
    .in_2(decoder_1_out13), .in_3(decoder_2_out5), .in_4(undriven_71), .out_6(r_for_ram_1_out_6));  // open: in_5, in_1
  R_for_RAM r_for_ram_95 (
    .in_2(decoder_1_out14), .in_3(decoder_2_out5), .in_4(undriven_72), .out_6(r_for_ram_1_out_6));  // open: in_5, in_1
  R_for_RAM r_for_ram_96 (
    .in_2(decoder_1_out15), .in_3(decoder_2_out5), .in_4(undriven_73), .out_6(r_for_ram_1_out_6));  // open: in_5, in_1
  R_for_RAM r_for_ram_97 (
    .in_2(decoder_1_out0), .in_3(decoder_2_out6), .in_4(undriven_102), .in_5(R), .out_6(r_for_ram_1_out_6),
    .in_1(in_1));
  R_for_RAM r_for_ram_98 (
    .in_2(decoder_1_out1), .in_3(decoder_2_out6), .in_4(S), .in_5(R), .out_6(r_for_ram_1_out_6), .in_1(in_1));
  R_for_RAM r_for_ram_99 (
    .in_2(decoder_1_out2), .in_3(decoder_2_out6), .in_4(undriven_74), .out_6(r_for_ram_1_out_6));  // open: in_5, in_1
  R_for_RAM r_for_ram_100 (
    .in_2(decoder_1_out3), .in_3(decoder_2_out6), .in_4(undriven_75), .out_6(r_for_ram_1_out_6));  // open: in_5, in_1
  R_for_RAM r_for_ram_101 (
    .in_2(decoder_1_out4), .in_3(decoder_2_out6), .in_4(undriven_76), .out_6(r_for_ram_1_out_6));  // open: in_5, in_1
  R_for_RAM r_for_ram_102 (
    .in_2(decoder_1_out5), .in_3(decoder_2_out6), .in_4(undriven_77), .out_6(r_for_ram_1_out_6));  // open: in_5, in_1
  R_for_RAM r_for_ram_103 (
    .in_2(decoder_1_out6), .in_3(decoder_2_out6), .in_4(undriven_78), .out_6(r_for_ram_1_out_6));  // open: in_5, in_1
  R_for_RAM r_for_ram_104 (
    .in_2(decoder_1_out7), .in_3(decoder_2_out6), .in_4(undriven_79), .out_6(r_for_ram_1_out_6));  // open: in_5, in_1
  R_for_RAM r_for_ram_105 (
    .in_2(decoder_1_out8), .in_3(decoder_2_out6), .in_4(undriven_80), .out_6(r_for_ram_1_out_6));  // open: in_5, in_1
  R_for_RAM r_for_ram_106 (
    .in_2(decoder_1_out9), .in_3(decoder_2_out6), .in_4(undriven_81), .out_6(r_for_ram_1_out_6));  // open: in_5, in_1
  R_for_RAM r_for_ram_107 (
    .in_2(decoder_1_out10), .in_3(decoder_2_out6), .in_4(undriven_82), .out_6(r_for_ram_1_out_6));  // open: in_5, in_1
  R_for_RAM r_for_ram_108 (
    .in_2(decoder_1_out11), .in_3(decoder_2_out6), .in_4(undriven_83), .out_6(r_for_ram_1_out_6));  // open: in_5, in_1
  R_for_RAM r_for_ram_109 (
    .in_2(decoder_1_out12), .in_3(decoder_2_out6), .in_4(undriven_84), .out_6(r_for_ram_1_out_6));  // open: in_5, in_1
  R_for_RAM r_for_ram_110 (
    .in_2(decoder_1_out13), .in_3(decoder_2_out6), .in_4(undriven_85), .out_6(r_for_ram_1_out_6));  // open: in_5, in_1
  R_for_RAM r_for_ram_111 (
    .in_2(decoder_1_out14), .in_3(decoder_2_out6), .in_4(undriven_86), .out_6(r_for_ram_1_out_6));  // open: in_5, in_1
  R_for_RAM r_for_ram_112 (
    .in_2(decoder_1_out15), .in_3(decoder_2_out6), .in_4(undriven_87), .out_6(r_for_ram_1_out_6));  // open: in_5, in_1
  R_for_RAM r_for_ram_113 (
    .in_2(decoder_1_out0), .in_3(decoder_2_out7), .in_4(undriven_102), .in_5(R), .out_6(r_for_ram_1_out_6),
    .in_1(in_1));
  R_for_RAM r_for_ram_114 (
    .in_2(decoder_1_out1), .in_3(decoder_2_out7), .in_4(S), .in_5(R), .out_6(r_for_ram_1_out_6), .in_1(in_1));
  R_for_RAM r_for_ram_115 (
    .in_2(decoder_1_out2), .in_3(decoder_2_out7), .in_4(undriven_88), .out_6(r_for_ram_1_out_6));  // open: in_5, in_1
  R_for_RAM r_for_ram_116 (
    .in_2(decoder_1_out3), .in_3(decoder_2_out7), .in_4(undriven_89), .out_6(r_for_ram_1_out_6));  // open: in_5, in_1
  R_for_RAM r_for_ram_117 (
    .in_2(decoder_1_out4), .in_3(decoder_2_out7), .in_4(undriven_90), .out_6(r_for_ram_1_out_6));  // open: in_5, in_1
  R_for_RAM r_for_ram_118 (
    .in_2(decoder_1_out5), .in_3(decoder_2_out7), .in_4(undriven_91), .out_6(r_for_ram_1_out_6));  // open: in_5, in_1
  R_for_RAM r_for_ram_119 (
    .in_2(decoder_1_out6), .in_3(decoder_2_out7), .in_4(undriven_92), .out_6(r_for_ram_1_out_6));  // open: in_5, in_1
  R_for_RAM r_for_ram_120 (
    .in_2(decoder_1_out7), .in_3(decoder_2_out7), .in_4(undriven_93), .out_6(r_for_ram_1_out_6));  // open: in_5, in_1
  R_for_RAM r_for_ram_121 (
    .in_2(decoder_1_out8), .in_3(decoder_2_out7), .in_4(undriven_94), .out_6(r_for_ram_1_out_6));  // open: in_5, in_1
  R_for_RAM r_for_ram_122 (
    .in_2(decoder_1_out9), .in_3(decoder_2_out7), .in_4(undriven_95), .out_6(r_for_ram_1_out_6));  // open: in_5, in_1
  R_for_RAM r_for_ram_123 (
    .in_2(decoder_1_out10), .in_3(decoder_2_out7), .in_4(undriven_96), .out_6(r_for_ram_1_out_6));  // open: in_5, in_1
  R_for_RAM r_for_ram_124 (
    .in_2(decoder_1_out11), .in_3(decoder_2_out7), .in_4(undriven_97), .out_6(r_for_ram_1_out_6));  // open: in_5, in_1
  R_for_RAM r_for_ram_125 (
    .in_2(decoder_1_out12), .in_3(decoder_2_out7), .in_4(undriven_98), .out_6(r_for_ram_1_out_6));  // open: in_5, in_1
  R_for_RAM r_for_ram_126 (
    .in_2(decoder_1_out13), .in_3(decoder_2_out7), .in_4(undriven_99), .out_6(r_for_ram_1_out_6));  // open: in_5, in_1
  R_for_RAM r_for_ram_127 (
    .in_2(decoder_1_out14), .in_3(decoder_2_out7), .in_4(undriven_100), .out_6(r_for_ram_1_out_6));  // open: in_5, in_1
  R_for_RAM r_for_ram_128 (
    .in_2(decoder_1_out15), .in_3(decoder_2_out7), .in_4(undriven_101), .out_6(r_for_ram_1_out_6));  // open: in_5, in_1
  R_for_RAM r_for_ram_129 (
    .in_2(decoder_1_out0), .in_3(decoder_2_out8), .in_4(undriven_102), .in_5(R), .out_6(r_for_ram_1_out_6),
    .in_1(in_1));
  R_for_RAM r_for_ram_130 (
    .in_2(decoder_1_out1), .in_3(decoder_2_out8), .in_4(S), .in_5(R), .out_6(r_for_ram_1_out_6), .in_1(in_1));
  R_for_RAM r_for_ram_131 (
    .in_2(decoder_1_out2), .in_3(decoder_2_out8), .in_4(undriven_103), .out_6(r_for_ram_1_out_6));  // open: in_5, in_1
  R_for_RAM r_for_ram_132 (
    .in_2(decoder_1_out3), .in_3(decoder_2_out8), .in_4(undriven_104), .out_6(r_for_ram_1_out_6));  // open: in_5, in_1
  R_for_RAM r_for_ram_133 (
    .in_2(decoder_1_out4), .in_3(decoder_2_out8), .in_4(undriven_105), .out_6(r_for_ram_1_out_6));  // open: in_5, in_1
  R_for_RAM r_for_ram_134 (
    .in_2(decoder_1_out5), .in_3(decoder_2_out8), .in_4(undriven_106), .out_6(r_for_ram_1_out_6));  // open: in_5, in_1
  R_for_RAM r_for_ram_135 (
    .in_2(decoder_1_out6), .in_3(decoder_2_out8), .in_4(undriven_107), .out_6(r_for_ram_1_out_6));  // open: in_5, in_1
  R_for_RAM r_for_ram_136 (
    .in_2(decoder_1_out7), .in_3(decoder_2_out8), .in_4(undriven_108), .out_6(r_for_ram_1_out_6));  // open: in_5, in_1
  R_for_RAM r_for_ram_137 (
    .in_2(decoder_1_out8), .in_3(decoder_2_out8), .in_4(undriven_109), .out_6(r_for_ram_1_out_6));  // open: in_5, in_1
  R_for_RAM r_for_ram_138 (
    .in_2(decoder_1_out9), .in_3(decoder_2_out8), .in_4(undriven_110), .out_6(r_for_ram_1_out_6));  // open: in_5, in_1
  R_for_RAM r_for_ram_139 (
    .in_2(decoder_1_out10), .in_3(decoder_2_out8), .in_4(undriven_111), .out_6(r_for_ram_1_out_6));  // open: in_5, in_1
  R_for_RAM r_for_ram_140 (
    .in_2(decoder_1_out11), .in_3(decoder_2_out8), .in_4(undriven_112), .out_6(r_for_ram_1_out_6));  // open: in_5, in_1
  R_for_RAM r_for_ram_141 (
    .in_2(decoder_1_out12), .in_3(decoder_2_out8), .in_4(undriven_113), .out_6(r_for_ram_1_out_6));  // open: in_5, in_1
  R_for_RAM r_for_ram_142 (
    .in_2(decoder_1_out13), .in_3(decoder_2_out8), .in_4(undriven_114), .out_6(r_for_ram_1_out_6));  // open: in_5, in_1
  R_for_RAM r_for_ram_143 (
    .in_2(decoder_1_out14), .in_3(decoder_2_out8), .in_4(undriven_115), .out_6(r_for_ram_1_out_6));  // open: in_5, in_1
  R_for_RAM r_for_ram_144 (
    .in_2(decoder_1_out15), .in_3(decoder_2_out8), .in_4(undriven_116), .out_6(r_for_ram_1_out_6));  // open: in_5, in_1
  R_for_RAM r_for_ram_145 (
    .in_2(decoder_1_out0), .in_3(decoder_2_out9), .in_4(undriven_102), .in_5(R), .out_6(r_for_ram_1_out_6),
    .in_1(in_1));
  R_for_RAM r_for_ram_146 (
    .in_2(decoder_1_out1), .in_3(decoder_2_out9), .in_4(S), .in_5(R), .out_6(r_for_ram_1_out_6), .in_1(in_1));
  R_for_RAM r_for_ram_147 (
    .in_2(decoder_1_out2), .in_3(decoder_2_out9), .in_4(undriven_117), .out_6(r_for_ram_1_out_6));  // open: in_5, in_1
  R_for_RAM r_for_ram_148 (
    .in_2(decoder_1_out3), .in_3(decoder_2_out9), .in_4(undriven_118), .out_6(r_for_ram_1_out_6));  // open: in_5, in_1
  R_for_RAM r_for_ram_149 (
    .in_2(decoder_1_out4), .in_3(decoder_2_out9), .in_4(undriven_119), .out_6(r_for_ram_1_out_6));  // open: in_5, in_1
  R_for_RAM r_for_ram_150 (
    .in_2(decoder_1_out5), .in_3(decoder_2_out9), .in_4(undriven_120), .out_6(r_for_ram_1_out_6));  // open: in_5, in_1
  R_for_RAM r_for_ram_151 (
    .in_2(decoder_1_out6), .in_3(decoder_2_out9), .in_4(undriven_121), .out_6(r_for_ram_1_out_6));  // open: in_5, in_1
  R_for_RAM r_for_ram_152 (
    .in_2(decoder_1_out7), .in_3(decoder_2_out9), .in_4(undriven_122), .out_6(r_for_ram_1_out_6));  // open: in_5, in_1
  R_for_RAM r_for_ram_153 (
    .in_2(decoder_1_out8), .in_3(decoder_2_out9), .in_4(undriven_123), .out_6(r_for_ram_1_out_6));  // open: in_5, in_1
  R_for_RAM r_for_ram_154 (
    .in_2(decoder_1_out9), .in_3(decoder_2_out9), .in_4(undriven_124), .out_6(r_for_ram_1_out_6));  // open: in_5, in_1
  R_for_RAM r_for_ram_155 (
    .in_2(decoder_1_out10), .in_3(decoder_2_out9), .in_4(undriven_125), .out_6(r_for_ram_1_out_6));  // open: in_5, in_1
  R_for_RAM r_for_ram_156 (
    .in_2(decoder_1_out11), .in_3(decoder_2_out9), .in_4(undriven_126), .out_6(r_for_ram_1_out_6));  // open: in_5, in_1
  R_for_RAM r_for_ram_157 (
    .in_2(decoder_1_out12), .in_3(decoder_2_out9), .in_4(undriven_127), .out_6(r_for_ram_1_out_6));  // open: in_5, in_1
  R_for_RAM r_for_ram_158 (
    .in_2(decoder_1_out13), .in_3(decoder_2_out9), .in_4(undriven_128), .out_6(r_for_ram_1_out_6));  // open: in_5, in_1
  R_for_RAM r_for_ram_159 (
    .in_2(decoder_1_out14), .in_3(decoder_2_out9), .in_4(undriven_129), .out_6(r_for_ram_1_out_6));  // open: in_5, in_1
  R_for_RAM r_for_ram_160 (
    .in_2(decoder_1_out15), .in_3(decoder_2_out9), .in_4(undriven_130), .out_6(r_for_ram_1_out_6));  // open: in_5, in_1
  R_for_RAM r_for_ram_161 (
    .in_2(decoder_1_out0), .in_3(decoder_2_out10), .in_4(undriven_102), .in_5(R), .out_6(r_for_ram_1_out_6),
    .in_1(in_1));
  R_for_RAM r_for_ram_162 (
    .in_2(decoder_1_out1), .in_3(decoder_2_out10), .in_4(S), .in_5(R), .out_6(r_for_ram_1_out_6), .in_1(in_1));
  R_for_RAM r_for_ram_163 (
    .in_2(decoder_1_out2), .in_3(decoder_2_out10), .in_4(undriven_131), .out_6(r_for_ram_1_out_6));  // open: in_5, in_1
  R_for_RAM r_for_ram_164 (
    .in_2(decoder_1_out3), .in_3(decoder_2_out10), .in_4(undriven_132), .out_6(r_for_ram_1_out_6));  // open: in_5, in_1
  R_for_RAM r_for_ram_165 (
    .in_2(decoder_1_out4), .in_3(decoder_2_out10), .in_4(undriven_133), .out_6(r_for_ram_1_out_6));  // open: in_5, in_1
  R_for_RAM r_for_ram_166 (
    .in_2(decoder_1_out5), .in_3(decoder_2_out10), .in_4(undriven_134), .out_6(r_for_ram_1_out_6));  // open: in_5, in_1
  R_for_RAM r_for_ram_167 (
    .in_2(decoder_1_out6), .in_3(decoder_2_out10), .in_4(undriven_135), .out_6(r_for_ram_1_out_6));  // open: in_5, in_1
  R_for_RAM r_for_ram_168 (
    .in_2(decoder_1_out7), .in_3(decoder_2_out10), .in_4(undriven_136), .out_6(r_for_ram_1_out_6));  // open: in_5, in_1
  R_for_RAM r_for_ram_169 (
    .in_2(decoder_1_out8), .in_3(decoder_2_out10), .in_4(undriven_137), .out_6(r_for_ram_1_out_6));  // open: in_5, in_1
  R_for_RAM r_for_ram_170 (
    .in_2(decoder_1_out9), .in_3(decoder_2_out10), .in_4(undriven_138), .out_6(r_for_ram_1_out_6));  // open: in_5, in_1
  R_for_RAM r_for_ram_171 (
    .in_2(decoder_1_out10), .in_3(decoder_2_out10), .in_4(undriven_139), .out_6(r_for_ram_1_out_6));  // open: in_5, in_1
  R_for_RAM r_for_ram_172 (
    .in_2(decoder_1_out11), .in_3(decoder_2_out10), .in_4(undriven_140), .out_6(r_for_ram_1_out_6));  // open: in_5, in_1
  R_for_RAM r_for_ram_173 (
    .in_2(decoder_1_out12), .in_3(decoder_2_out10), .in_4(undriven_141), .out_6(r_for_ram_1_out_6));  // open: in_5, in_1
  R_for_RAM r_for_ram_174 (
    .in_2(decoder_1_out13), .in_3(decoder_2_out10), .in_4(undriven_142), .out_6(r_for_ram_1_out_6));  // open: in_5, in_1
  R_for_RAM r_for_ram_175 (
    .in_2(decoder_1_out14), .in_3(decoder_2_out10), .in_4(undriven_143), .out_6(r_for_ram_1_out_6));  // open: in_5, in_1
  R_for_RAM r_for_ram_176 (
    .in_2(decoder_1_out15), .in_3(decoder_2_out10), .in_4(undriven_144), .out_6(r_for_ram_1_out_6));  // open: in_5, in_1
  R_for_RAM r_for_ram_177 (
    .in_2(decoder_1_out0), .in_3(decoder_2_out11), .in_4(undriven_102), .in_5(R), .out_6(r_for_ram_1_out_6),
    .in_1(in_1));
  R_for_RAM r_for_ram_178 (
    .in_2(decoder_1_out1), .in_3(decoder_2_out11), .in_4(S), .in_5(R), .out_6(r_for_ram_1_out_6), .in_1(in_1));
  R_for_RAM r_for_ram_179 (
    .in_2(decoder_1_out2), .in_3(decoder_2_out11), .in_4(undriven_145), .out_6(r_for_ram_1_out_6));  // open: in_5, in_1
  R_for_RAM r_for_ram_180 (
    .in_2(decoder_1_out3), .in_3(decoder_2_out11), .in_4(undriven_146), .out_6(r_for_ram_1_out_6));  // open: in_5, in_1
  R_for_RAM r_for_ram_181 (
    .in_2(decoder_1_out4), .in_3(decoder_2_out11), .in_4(undriven_147), .out_6(r_for_ram_1_out_6));  // open: in_5, in_1
  R_for_RAM r_for_ram_182 (
    .in_2(decoder_1_out5), .in_3(decoder_2_out11), .in_4(undriven_148), .out_6(r_for_ram_1_out_6));  // open: in_5, in_1
  R_for_RAM r_for_ram_183 (
    .in_2(decoder_1_out6), .in_3(decoder_2_out11), .in_4(undriven_149), .out_6(r_for_ram_1_out_6));  // open: in_5, in_1
  R_for_RAM r_for_ram_184 (
    .in_2(decoder_1_out7), .in_3(decoder_2_out11), .in_4(undriven_150), .out_6(r_for_ram_1_out_6));  // open: in_5, in_1
  R_for_RAM r_for_ram_185 (
    .in_2(decoder_1_out8), .in_3(decoder_2_out11), .in_4(undriven_151), .out_6(r_for_ram_1_out_6));  // open: in_5, in_1
  R_for_RAM r_for_ram_186 (
    .in_2(decoder_1_out9), .in_3(decoder_2_out11), .in_4(undriven_152), .out_6(r_for_ram_1_out_6));  // open: in_5, in_1
  R_for_RAM r_for_ram_187 (
    .in_2(decoder_1_out10), .in_3(decoder_2_out11), .in_4(undriven_153), .out_6(r_for_ram_1_out_6));  // open: in_5, in_1
  R_for_RAM r_for_ram_188 (
    .in_2(decoder_1_out11), .in_3(decoder_2_out11), .in_4(undriven_154), .out_6(r_for_ram_1_out_6));  // open: in_5, in_1
  R_for_RAM r_for_ram_189 (
    .in_2(decoder_1_out12), .in_3(decoder_2_out11), .in_4(undriven_155), .out_6(r_for_ram_1_out_6));  // open: in_5, in_1
  R_for_RAM r_for_ram_190 (
    .in_2(decoder_1_out13), .in_3(decoder_2_out11), .in_4(undriven_156), .out_6(r_for_ram_1_out_6));  // open: in_5, in_1
  R_for_RAM r_for_ram_191 (
    .in_2(decoder_1_out14), .in_3(decoder_2_out11), .in_4(undriven_157), .out_6(r_for_ram_1_out_6));  // open: in_5, in_1
  R_for_RAM r_for_ram_192 (
    .in_2(decoder_1_out15), .in_3(decoder_2_out11), .in_4(undriven_158), .out_6(r_for_ram_1_out_6));  // open: in_5, in_1
  R_for_RAM r_for_ram_193 (
    .in_2(decoder_1_out0), .in_3(decoder_2_out12), .in_4(undriven_102), .in_5(R), .out_6(r_for_ram_1_out_6),
    .in_1(in_1));
  R_for_RAM r_for_ram_194 (
    .in_2(decoder_1_out1), .in_3(decoder_2_out12), .in_4(S), .in_5(R), .out_6(r_for_ram_1_out_6), .in_1(in_1));
  R_for_RAM r_for_ram_195 (
    .in_2(decoder_1_out2), .in_3(decoder_2_out12), .in_4(undriven_159), .out_6(r_for_ram_1_out_6));  // open: in_5, in_1
  R_for_RAM r_for_ram_196 (
    .in_2(decoder_1_out3), .in_3(decoder_2_out12), .in_4(undriven_160), .out_6(r_for_ram_1_out_6));  // open: in_5, in_1
  R_for_RAM r_for_ram_197 (
    .in_2(decoder_1_out4), .in_3(decoder_2_out12), .in_4(undriven_161), .out_6(r_for_ram_1_out_6));  // open: in_5, in_1
  R_for_RAM r_for_ram_198 (
    .in_2(decoder_1_out5), .in_3(decoder_2_out12), .in_4(undriven_162), .out_6(r_for_ram_1_out_6));  // open: in_5, in_1
  R_for_RAM r_for_ram_199 (
    .in_2(decoder_1_out6), .in_3(decoder_2_out12), .in_4(undriven_163), .out_6(r_for_ram_1_out_6));  // open: in_5, in_1
  R_for_RAM r_for_ram_200 (
    .in_2(decoder_1_out7), .in_3(decoder_2_out12), .in_4(undriven_164), .out_6(r_for_ram_1_out_6));  // open: in_5, in_1
  R_for_RAM r_for_ram_201 (
    .in_2(decoder_1_out8), .in_3(decoder_2_out12), .in_4(undriven_165), .out_6(r_for_ram_1_out_6));  // open: in_5, in_1
  R_for_RAM r_for_ram_202 (
    .in_2(decoder_1_out9), .in_3(decoder_2_out12), .in_4(undriven_166), .out_6(r_for_ram_1_out_6));  // open: in_5, in_1
  R_for_RAM r_for_ram_203 (
    .in_2(decoder_1_out10), .in_3(decoder_2_out12), .in_4(undriven_167), .out_6(r_for_ram_1_out_6));  // open: in_5, in_1
  R_for_RAM r_for_ram_204 (
    .in_2(decoder_1_out11), .in_3(decoder_2_out12), .in_4(undriven_168), .out_6(r_for_ram_1_out_6));  // open: in_5, in_1
  R_for_RAM r_for_ram_205 (
    .in_2(decoder_1_out12), .in_3(decoder_2_out12), .in_4(undriven_169), .out_6(r_for_ram_1_out_6));  // open: in_5, in_1
  R_for_RAM r_for_ram_206 (
    .in_2(decoder_1_out13), .in_3(decoder_2_out12), .in_4(undriven_170), .out_6(r_for_ram_1_out_6));  // open: in_5, in_1
  R_for_RAM r_for_ram_207 (
    .in_2(decoder_1_out14), .in_3(decoder_2_out12), .in_4(undriven_171), .out_6(r_for_ram_1_out_6));  // open: in_5, in_1
  R_for_RAM r_for_ram_208 (
    .in_2(decoder_1_out15), .in_3(decoder_2_out12), .in_4(undriven_172), .out_6(r_for_ram_1_out_6));  // open: in_5, in_1
  R_for_RAM r_for_ram_209 (
    .in_2(decoder_1_out0), .in_3(decoder_2_out13), .in_4(undriven_102), .in_5(R), .out_6(r_for_ram_1_out_6),
    .in_1(in_1));
  R_for_RAM r_for_ram_210 (
    .in_2(decoder_1_out1), .in_3(decoder_2_out13), .in_4(S), .in_5(R), .out_6(r_for_ram_1_out_6), .in_1(in_1));
  R_for_RAM r_for_ram_211 (
    .in_2(decoder_1_out2), .in_3(decoder_2_out13), .in_4(undriven_173), .out_6(r_for_ram_1_out_6));  // open: in_5, in_1
  R_for_RAM r_for_ram_212 (
    .in_2(decoder_1_out3), .in_3(decoder_2_out13), .in_4(undriven_174), .out_6(r_for_ram_1_out_6));  // open: in_5, in_1
  R_for_RAM r_for_ram_213 (
    .in_2(decoder_1_out4), .in_3(decoder_2_out13), .in_4(undriven_175), .out_6(r_for_ram_1_out_6));  // open: in_5, in_1
  R_for_RAM r_for_ram_214 (
    .in_2(decoder_1_out5), .in_3(decoder_2_out13), .in_4(undriven_176), .out_6(r_for_ram_1_out_6));  // open: in_5, in_1
  R_for_RAM r_for_ram_215 (
    .in_2(decoder_1_out6), .in_3(decoder_2_out13), .in_4(undriven_177), .out_6(r_for_ram_1_out_6));  // open: in_5, in_1
  R_for_RAM r_for_ram_216 (
    .in_2(decoder_1_out7), .in_3(decoder_2_out13), .in_4(undriven_178), .out_6(r_for_ram_1_out_6));  // open: in_5, in_1
  R_for_RAM r_for_ram_217 (
    .in_2(decoder_1_out8), .in_3(decoder_2_out13), .in_4(undriven_179), .out_6(r_for_ram_1_out_6));  // open: in_5, in_1
  R_for_RAM r_for_ram_218 (
    .in_2(decoder_1_out9), .in_3(decoder_2_out13), .in_4(undriven_180), .out_6(r_for_ram_1_out_6));  // open: in_5, in_1
  R_for_RAM r_for_ram_219 (
    .in_2(decoder_1_out10), .in_3(decoder_2_out13), .in_4(undriven_181), .out_6(r_for_ram_1_out_6));  // open: in_5, in_1
  R_for_RAM r_for_ram_220 (
    .in_2(decoder_1_out11), .in_3(decoder_2_out13), .in_4(undriven_182), .out_6(r_for_ram_1_out_6));  // open: in_5, in_1
  R_for_RAM r_for_ram_221 (
    .in_2(decoder_1_out12), .in_3(decoder_2_out13), .in_4(undriven_183), .out_6(r_for_ram_1_out_6));  // open: in_5, in_1
  R_for_RAM r_for_ram_222 (
    .in_2(decoder_1_out13), .in_3(decoder_2_out13), .in_4(undriven_184), .out_6(r_for_ram_1_out_6));  // open: in_5, in_1
  R_for_RAM r_for_ram_223 (
    .in_2(decoder_1_out14), .in_3(decoder_2_out13), .in_4(undriven_185), .out_6(r_for_ram_1_out_6));  // open: in_5, in_1
  R_for_RAM r_for_ram_224 (
    .in_2(decoder_1_out15), .in_3(decoder_2_out13), .in_4(undriven_186), .out_6(r_for_ram_1_out_6));  // open: in_5, in_1
  R_for_RAM r_for_ram_225 (
    .in_2(decoder_1_out0), .in_3(decoder_2_out14), .in_4(undriven_102), .in_5(R), .out_6(r_for_ram_1_out_6),
    .in_1(in_1));
  R_for_RAM r_for_ram_226 (
    .in_2(decoder_1_out1), .in_3(decoder_2_out14), .in_4(S), .in_5(R), .out_6(r_for_ram_1_out_6), .in_1(in_1));
  R_for_RAM r_for_ram_227 (
    .in_2(decoder_1_out2), .in_3(decoder_2_out14), .in_4(undriven_187), .out_6(r_for_ram_1_out_6));  // open: in_5, in_1
  R_for_RAM r_for_ram_228 (
    .in_2(decoder_1_out3), .in_3(decoder_2_out14), .in_4(undriven_188), .out_6(r_for_ram_1_out_6));  // open: in_5, in_1
  R_for_RAM r_for_ram_229 (
    .in_2(decoder_1_out4), .in_3(decoder_2_out14), .in_4(undriven_189), .out_6(r_for_ram_1_out_6));  // open: in_5, in_1
  R_for_RAM r_for_ram_230 (
    .in_2(decoder_1_out5), .in_3(decoder_2_out14), .in_4(undriven_190), .out_6(r_for_ram_1_out_6));  // open: in_5, in_1
  R_for_RAM r_for_ram_231 (
    .in_2(decoder_1_out6), .in_3(decoder_2_out14), .in_4(undriven_191), .out_6(r_for_ram_1_out_6));  // open: in_5, in_1
  R_for_RAM r_for_ram_232 (
    .in_2(decoder_1_out7), .in_3(decoder_2_out14), .in_4(undriven_192), .out_6(r_for_ram_1_out_6));  // open: in_5, in_1
  R_for_RAM r_for_ram_233 (
    .in_2(decoder_1_out8), .in_3(decoder_2_out14), .in_4(undriven_193), .out_6(r_for_ram_1_out_6));  // open: in_5, in_1
  R_for_RAM r_for_ram_234 (
    .in_2(decoder_1_out9), .in_3(decoder_2_out14), .in_4(undriven_194), .out_6(r_for_ram_1_out_6));  // open: in_5, in_1
  R_for_RAM r_for_ram_235 (
    .in_2(decoder_1_out10), .in_3(decoder_2_out14), .in_4(undriven_195), .out_6(r_for_ram_1_out_6));  // open: in_5, in_1
  R_for_RAM r_for_ram_236 (
    .in_2(decoder_1_out11), .in_3(decoder_2_out14), .in_4(undriven_196), .out_6(r_for_ram_1_out_6));  // open: in_5, in_1
  R_for_RAM r_for_ram_237 (
    .in_2(decoder_1_out12), .in_3(decoder_2_out14), .in_4(undriven_197), .out_6(r_for_ram_1_out_6));  // open: in_5, in_1
  R_for_RAM r_for_ram_238 (
    .in_2(decoder_1_out13), .in_3(decoder_2_out14), .in_4(undriven_198), .out_6(r_for_ram_1_out_6));  // open: in_5, in_1
  R_for_RAM r_for_ram_239 (
    .in_2(decoder_1_out14), .in_3(decoder_2_out14), .in_4(undriven_199), .out_6(r_for_ram_1_out_6));  // open: in_5, in_1
  R_for_RAM r_for_ram_240 (
    .in_2(decoder_1_out15), .in_3(decoder_2_out14), .in_4(undriven_200), .out_6(r_for_ram_1_out_6));  // open: in_5, in_1
  R_for_RAM r_for_ram_241 (
    .in_2(decoder_1_out0), .in_3(decoder_2_out15), .in_4(undriven_102), .in_5(R), .out_6(r_for_ram_1_out_6),
    .in_1(in_1));
  R_for_RAM r_for_ram_242 (
    .in_2(decoder_1_out1), .in_3(decoder_2_out15), .in_4(S), .in_5(R), .out_6(r_for_ram_1_out_6), .in_1(in_1));
  R_for_RAM r_for_ram_243 (
    .in_2(decoder_1_out2), .in_3(decoder_2_out15), .in_4(undriven_201), .in_5(R), .out_6(r_for_ram_1_out_6));  // open: in_1
  R_for_RAM r_for_ram_244 (
    .in_2(decoder_1_out3), .in_3(decoder_2_out15), .in_4(undriven_202), .in_5(R), .out_6(r_for_ram_1_out_6));  // open: in_1
  R_for_RAM r_for_ram_245 (
    .in_2(decoder_1_out4), .in_3(decoder_2_out15), .in_4(undriven_203), .in_5(R), .out_6(r_for_ram_1_out_6));  // open: in_1
  R_for_RAM r_for_ram_246 (
    .in_2(decoder_1_out5), .in_3(decoder_2_out15), .in_4(undriven_204), .in_5(R), .out_6(r_for_ram_1_out_6));  // open: in_1
  R_for_RAM r_for_ram_247 (
    .in_2(decoder_1_out6), .in_3(decoder_2_out15), .in_4(undriven_205), .in_5(R), .out_6(r_for_ram_1_out_6));  // open: in_1
  R_for_RAM r_for_ram_248 (
    .in_2(decoder_1_out7), .in_3(decoder_2_out15), .in_4(undriven_206), .in_5(R), .out_6(r_for_ram_1_out_6));  // open: in_1
  R_for_RAM r_for_ram_249 (
    .in_2(decoder_1_out8), .in_3(decoder_2_out15), .in_4(undriven_207), .in_5(R), .out_6(r_for_ram_1_out_6));  // open: in_1
  R_for_RAM r_for_ram_250 (
    .in_2(decoder_1_out9), .in_3(decoder_2_out15), .in_4(undriven_208), .in_5(R), .out_6(r_for_ram_1_out_6));  // open: in_1
  R_for_RAM r_for_ram_251 (
    .in_2(decoder_1_out10), .in_3(decoder_2_out15), .in_4(undriven_209), .in_5(R), .out_6(r_for_ram_1_out_6));  // open: in_1
  R_for_RAM r_for_ram_252 (
    .in_2(decoder_1_out11), .in_3(decoder_2_out15), .in_4(undriven_210), .in_5(R), .out_6(r_for_ram_1_out_6));  // open: in_1
  R_for_RAM r_for_ram_253 (
    .in_2(decoder_1_out12), .in_3(decoder_2_out15), .in_4(undriven_211), .in_5(R), .out_6(r_for_ram_1_out_6));  // open: in_1
  R_for_RAM r_for_ram_254 (
    .in_2(decoder_1_out13), .in_3(decoder_2_out15), .in_4(undriven_212), .in_5(R), .out_6(r_for_ram_1_out_6));  // open: in_1
  R_for_RAM r_for_ram_255 (
    .in_2(decoder_1_out14), .in_3(decoder_2_out15), .in_4(undriven_213), .in_5(R), .out_6(r_for_ram_1_out_6));  // open: in_1
  R_for_RAM r_for_ram_256 (
    .in_2(decoder_1_out15), .in_3(decoder_2_out15), .in_4(undriven_214), .in_5(R), .out_6(r_for_ram_1_out_6));  // open: in_1
  assign r_for_ram_1_out_6 = in_9 ? in_7 : 8'bz;  // Controlled_Buffer controlled_buffer_1
  assign out_11 = in_8 ? r_for_ram_1_out_6 : 8'bz;  // Controlled_Buffer controlled_buffer_2
endmodule

module R_for_RAM (
  input  [7:0] in_1,
  input  in_2,
  input  in_3,
  input  in_4,
  input  in_5,
  output [7:0] out_6
);

  wire and_1_out, and_2_out, and_3_out, b_smallmemory_1_out_10, b_smallmemory_1_out_11,
       b_smallmemory_1_out_12, b_smallmemory_1_out_13, b_smallmemory_1_out_14, b_smallmemory_1_out_15,
       b_smallmemory_1_out_16, b_smallmemory_1_out_17;
  wire [7:0] e_andgroub_1_out_10;

  and and_1 (and_1_out, in_2, in_3);
  and and_2 (and_2_out, and_1_out, in_4);
  and and_3 (and_3_out, and_1_out, in_5);
  B_smallmemory b_smallmemory_1 (
    .in_1(in_1[0]), .in_2(in_1[1]), .in_3(in_1[2]), .in_4(in_1[3]), .in_5(in_1[4]), .in_6(in_1[5]),
    .in_7(in_1[6]), .in_8(in_1[7]), .S(and_2_out), .out_10(b_smallmemory_1_out_10),
    .out_11(b_smallmemory_1_out_11), .out_12(b_smallmemory_1_out_12), .out_13(b_smallmemory_1_out_13),
    .out_14(b_smallmemory_1_out_14), .out_15(b_smallmemory_1_out_15), .out_16(b_smallmemory_1_out_16),
    .out_17(b_smallmemory_1_out_17));
  E_andgroub e_andgroub_1 (
    .in_1(b_smallmemory_1_out_10), .in_2(b_smallmemory_1_out_11), .in_3(b_smallmemory_1_out_12),
    .in_4(b_smallmemory_1_out_13), .in_5(b_smallmemory_1_out_14), .in_6(b_smallmemory_1_out_15),
    .in_7(b_smallmemory_1_out_16), .in_8(b_smallmemory_1_out_17), .in_9(and_3_out),
    .out_10(e_andgroub_1_out_10[0]), .out_11(e_andgroub_1_out_10[1]), .out_12(e_andgroub_1_out_10[2]),
    .out_13(e_andgroub_1_out_10[3]), .out_14(e_andgroub_1_out_10[4]), .out_15(e_andgroub_1_out_10[5]),
    .out_16(e_andgroub_1_out_10[6]), .out_17(e_andgroub_1_out_10[7]));
  assign out_6 = and_3_out ? e_andgroub_1_out_10 : 8'bz;  // Controlled_Buffer controlled_buffer_1
endmodule

module RAM_2 (
  input  [8:0] in_1,
  input  in_2,
  input  [7:0] in_3,
  input  s,
  input  e,
  output [7:0] out_6
);

  wire [8:0] controlled_buffer_1_out;

  assign controlled_buffer_1_out = in_2 ? in_1 : 9'bz;  // Controlled_Buffer controlled_buffer_1
  RAM_part #(.addrWidth(9), .bus("separate")) ram_1 (
    .addr(controlled_buffer_1_out), .din(in_3), .data(out_6), .str(1'b1), .clk(s), .ld(e));  // open: sel, clr
endmodule

module test (
);

  RAM_2 ram_2_1 ();  // open: in_1, in_3, s, e, out_6, in_2
endmodule

module shirft_right (
  input  in_1,
  input  [7:0] in_2,
  output [7:0] out_3,
  output out_4
);


  assign out_3 = {in_2[6:0], in_1};
  assign out_4 = in_2[7];
endmodule

module shift_left (
  input  in_1,
  input  [7:0] in_2,
  output [7:0] out_3,
  output out_4
);


  assign in_2[0] = in_1;
  assign out_3[6:0] = in_2[7:1];
  assign out_4 = out_3[7];
endmodule

module small_COMPARATOR (
  input  in_1,
  input  in_2,
  input  in_3,
  input  in_4,
  output out_5,
  output out_6,
  output out_7
);

  wire and_2_out, not_1_out;

  xor xor_1 (out_5, in_3, in_4);
  not not_1 (not_1_out, out_5);
  and and_1 (out_7, not_1_out, in_1);
  and and_2 (and_2_out, in_1, in_3, out_5);
  or or_1 (out_6, and_2_out, in_2);
endmodule

module _8bitcomparator (
  input  [7:0] in_1,
  input  [7:0] in_2,
  output [7:0] out_3,
  output out_4,
  output out_5
);

  wire small_comparator_1_out_6, small_comparator_1_out_7, small_comparator_2_out_6,
       small_comparator_2_out_7, small_comparator_3_out_6, small_comparator_3_out_7,
       small_comparator_4_out_6, small_comparator_4_out_7, small_comparator_5_out_6,
       small_comparator_5_out_7, small_comparator_6_out_6, small_comparator_6_out_7,
       small_comparator_7_out_6, small_comparator_7_out_7;

  small_COMPARATOR small_comparator_1 (
    .in_3(in_1[0]), .in_4(in_2[0]), .out_5(out_3[0]), .out_6(small_comparator_1_out_6),
    .out_7(small_comparator_1_out_7), .in_1(1'b1), .in_2(1'b0));
  small_COMPARATOR small_comparator_2 (
    .in_3(in_1[1]), .in_4(in_2[1]), .out_5(out_3[1]), .out_6(small_comparator_2_out_6),
    .out_7(small_comparator_2_out_7), .in_1(small_comparator_1_out_7), .in_2(small_comparator_1_out_6));
  small_COMPARATOR small_comparator_3 (
    .in_3(in_1[2]), .in_4(in_2[2]), .out_5(out_3[2]), .out_6(small_comparator_3_out_6),
    .out_7(small_comparator_3_out_7), .in_1(small_comparator_2_out_7), .in_2(small_comparator_2_out_6));
  small_COMPARATOR small_comparator_4 (
    .in_3(in_1[3]), .in_4(in_2[3]), .out_5(out_3[3]), .out_6(small_comparator_4_out_6),
    .out_7(small_comparator_4_out_7), .in_1(small_comparator_3_out_7), .in_2(small_comparator_3_out_6));
  small_COMPARATOR small_comparator_5 (
    .in_3(in_1[4]), .in_4(in_2[4]), .out_5(out_3[4]), .out_6(small_comparator_5_out_6),
    .out_7(small_comparator_5_out_7), .in_1(small_comparator_4_out_7), .in_2(small_comparator_4_out_6));
  small_COMPARATOR small_comparator_6 (
    .in_3(in_1[5]), .in_4(in_2[5]), .out_5(out_3[5]), .out_6(small_comparator_6_out_6),
    .out_7(small_comparator_6_out_7), .in_1(small_comparator_5_out_7), .in_2(small_comparator_5_out_6));
  small_COMPARATOR small_comparator_7 (
    .in_3(in_1[6]), .in_4(in_2[6]), .out_5(out_3[6]), .out_6(small_comparator_7_out_6),
    .out_7(small_comparator_7_out_7), .in_1(small_comparator_6_out_7), .in_2(small_comparator_6_out_6));
  small_COMPARATOR small_comparator_8 (
    .in_3(in_1[7]), .in_4(in_2[7]), .out_5(out_3[7]), .out_6(out_4), .out_7(out_5),
    .in_1(small_comparator_7_out_7), .in_2(small_comparator_7_out_6));
endmodule

module ALU (
  input  [7:0] in_1,
  input  [7:0] in_2,
  input  in_3,
  input  [2:0] in_4,
  output out_5,
  output out_6,
  output out_7,
  output [7:0] out_8,
  output out_9
);

  wire adder_1_cout, and_2_out, and_3_out, and_4_out, decoder_1_out0, decoder_1_out1, decoder_1_out2,
       decoder_1_out3, decoder_1_out4, decoder_1_out5, decoder_1_out6, decoder_1_out7, or_3_out,
       shirft_right_1_out_4, undriven;
  wire [7:0] adder_1_out, and_1_out, n8bitcomparator_1_out_3, not_1_out, or_1_out, shift_left_1_out_3,
       shirft_right_1_out_3, xor_1_out;

  assign not_1_out = ~in_1;  // NOT_Gate not_1, 8 bits wide
  shift_left shift_left_1 (.in_1(undriven), .in_2(in_1), .out_3(shift_left_1_out_3), .out_4(in_3));
  shirft_right shirft_right_1 (.in_1(in_3), .in_2(in_1), .out_3(shirft_right_1_out_3), .out_4(shirft_right_1_out_4));
  Adder adder_1 (.a(in_1), .b(in_2), .out(adder_1_out), .cin(in_3), .cout(adder_1_cout));
  Decoder #(.select(3)) decoder_1 (
    .out0(decoder_1_out0), .out1(decoder_1_out1), .out2(decoder_1_out2), .out3(decoder_1_out3),
    .out4(decoder_1_out4), .out5(decoder_1_out5), .out6(decoder_1_out6), .out7(decoder_1_out7), .sel(in_4));  // open: en
  _8bitcomparator u_8bitcomparator_1 (
    .in_1(in_1), .in_2(in_2), .out_3(n8bitcomparator_1_out_3), .out_4(out_5), .out_5(out_6));
  assign xor_1_out = in_1 ^ in_2;  // XOR_Gate xor_1, 8 bits wide
  assign or_1_out = in_1 | in_2;  // OR_Gate or_1, 8 bits wide
  assign and_1_out = in_1 & in_2;  // AND_Gate and_1, 8 bits wide
  assign out_8 = decoder_1_out0 ? adder_1_out : 8'bz;  // Controlled_Buffer controlled_buffer_1
  assign out_8 = decoder_1_out6 ? xor_1_out : 8'bz;  // Controlled_Buffer controlled_buffer_2
  assign out_8 = decoder_1_out5 ? or_1_out : 8'bz;  // Controlled_Buffer controlled_buffer_3
  assign out_8 = decoder_1_out4 ? and_1_out : 8'bz;  // Controlled_Buffer controlled_buffer_4
  assign out_8 = decoder_1_out3 ? not_1_out : 8'bz;  // Controlled_Buffer controlled_buffer_5
  and and_2 (and_2_out, undriven, decoder_1_out2);
  assign out_8 = decoder_1_out2 ? shift_left_1_out_3 : 8'bz;  // Controlled_Buffer controlled_buffer_6
  and and_3 (and_3_out, shirft_right_1_out_4, decoder_1_out1);
  assign out_8 = decoder_1_out1 ? shirft_right_1_out_3 : 8'bz;  // Controlled_Buffer controlled_buffer_7
  and and_4 (and_4_out, adder_1_cout, decoder_1_out0);
  assign out_8 = decoder_1_out7 ? n8bitcomparator_1_out_3 : 8'bz;  // Controlled_Buffer controlled_buffer_8
  or or_2 (out_9, and_2_out, and_3_out, and_4_out);
  or or_3 (or_3_out, out_8[0], out_8[1], out_8[2], out_8[3], out_8[4], out_8[5], out_8[6], out_8[7]);
  not not_2 (out_7, or_3_out);
endmodule

module E_onepin (
  input  [7:0] in_1,
  input  in_2,
  output [7:0] out_3
);

  and and_1 (out_3[0], in_1[0], in_2);
  and and_2 (out_3[1], in_1[1], in_2);
  and and_3 (out_3[2], in_1[2], in_2);
  and and_4 (out_3[3], in_1[3], in_2);
  and and_5 (out_3[4], in_1[4], in_2);
  and and_6 (out_3[5], in_1[5], in_2);
  and and_7 (out_3[6], in_1[6], in_2);
  and and_8 (out_3[7], in_1[7], in_2);
endmodule
