// Logisim project COMPUTER3.circ as structural Verilog
module main (
  input  in_1,
  input  in_2,
  input  in_3,
  input  [7:0] in_4,
  input  in_5,
  input  in_6,
  input  in_7,
  input  in_8,
  input  in_9,
  input  in_10,
  input  in_11,
  input  in_12,
  input  in_13,
  input  in_14,
  input  in_15,
  output [7:0] out_16
);

  wire and_1_out, and_2_out, and_3_out, and_4_out, and_5_out, and_6_out, and_7_out, and_8_out, and_9_out,
       b_smallmemory_1_out_10, b_smallmemory_1_out_11, b_smallmemory_1_out_12, b_smallmemory_1_out_13,
       b_smallmemory_1_out_14, b_smallmemory_1_out_15, b_smallmemory_1_out_16, b_smallmemory_1_out_17,
       b_smallmemory_2_out_10, b_smallmemory_2_out_11, b_smallmemory_2_out_12, b_smallmemory_2_out_13,
       b_smallmemory_2_out_14, b_smallmemory_2_out_15, b_smallmemory_2_out_16, b_smallmemory_2_out_17,
       b_smallmemory_3_out_10, b_smallmemory_3_out_11, b_smallmemory_3_out_12, b_smallmemory_3_out_13,
       b_smallmemory_3_out_14, b_smallmemory_3_out_15, b_smallmemory_3_out_16, b_smallmemory_3_out_17;
  wire [7:0] controlled_buffer_1_out, e_andgroub_1_out_10, e_andgroub_2_out_10, e_andgroub_3_out_10;

  and and_1 (and_1_out, in_1, in_2);
  and and_2 (and_2_out, in_8, in_9);
  and and_3 (and_3_out, in_12, in_13);
  and and_4 (and_4_out, and_1_out, in_5);
  and and_5 (and_5_out, and_1_out, in_7);
  and and_6 (and_6_out, and_2_out, in_10);
  and and_7 (and_7_out, and_2_out, in_11);
  and and_8 (and_8_out, and_3_out, in_14);
  and and_9 (and_9_out, and_3_out, in_15);
  B_smallmemory b_smallmemory_1 (
    .in_1(controlled_buffer_1_out[0]), .in_2(controlled_buffer_1_out[1]), .in_3(controlled_buffer_1_out[2]),
    .in_4(controlled_buffer_1_out[3]), .in_5(controlled_buffer_1_out[4]), .in_6(controlled_buffer_1_out[5]),
    .in_7(controlled_buffer_1_out[6]), .in_8(controlled_buffer_1_out[7]), .S(and_4_out),
    .out_10(b_smallmemory_1_out_10), .out_11(b_smallmemory_1_out_11), .out_12(b_smallmemory_1_out_12),
    .out_13(b_smallmemory_1_out_13), .out_14(b_smallmemory_1_out_14), .out_15(b_smallmemory_1_out_15),
    .out_16(b_smallmemory_1_out_16), .out_17(b_smallmemory_1_out_17));
  B_smallmemory b_smallmemory_2 (
    .in_1(controlled_buffer_1_out[0]), .in_2(controlled_buffer_1_out[1]), .in_3(controlled_buffer_1_out[2]),
    .in_4(controlled_buffer_1_out[3]), .in_5(controlled_buffer_1_out[4]), .in_6(controlled_buffer_1_out[5]),
    .in_7(controlled_buffer_1_out[6]), .in_8(controlled_buffer_1_out[7]), .S(and_6_out),
    .out_10(b_smallmemory_2_out_10), .out_11(b_smallmemory_2_out_11), .out_12(b_smallmemory_2_out_12),
    .out_13(b_smallmemory_2_out_13), .out_14(b_smallmemory_2_out_14), .out_15(b_smallmemory_2_out_15),
    .out_16(b_smallmemory_2_out_16), .out_17(b_smallmemory_2_out_17));
  B_smallmemory b_smallmemory_3 (
    .in_1(controlled_buffer_1_out[0]), .in_2(controlled_buffer_1_out[1]), .in_3(controlled_buffer_1_out[2]),
    .in_4(controlled_buffer_1_out[3]), .in_5(controlled_buffer_1_out[4]), .in_6(controlled_buffer_1_out[5]),
    .in_7(controlled_buffer_1_out[6]), .in_8(controlled_buffer_1_out[7]), .S(and_8_out),
    .out_10(b_smallmemory_3_out_10), .out_11(b_smallmemory_3_out_11), .out_12(b_smallmemory_3_out_12),
    .out_13(b_smallmemory_3_out_13), .out_14(b_smallmemory_3_out_14), .out_15(b_smallmemory_3_out_15),
    .out_16(b_smallmemory_3_out_16), .out_17(b_smallmemory_3_out_17));
  E_andgroub e_andgroub_1 (
    .in_1(b_smallmemory_1_out_10), .in_2(b_smallmemory_1_out_11), .in_3(b_smallmemory_1_out_12),
    .in_4(b_smallmemory_1_out_13), .in_5(b_smallmemory_1_out_14), .in_6(b_smallmemory_1_out_15),
    .in_7(b_smallmemory_1_out_16), .in_8(b_smallmemory_1_out_17), .in_9(and_5_out),
    .out_10(e_andgroub_1_out_10[0]), .out_11(e_andgroub_1_out_10[1]), .out_12(e_andgroub_1_out_10[2]),
    .out_13(e_andgroub_1_out_10[3]), .out_14(e_andgroub_1_out_10[4]), .out_15(e_andgroub_1_out_10[5]),
    .out_16(e_andgroub_1_out_10[6]), .out_17(e_andgroub_1_out_10[7]));
  E_andgroub e_andgroub_2 (
    .in_1(b_smallmemory_2_out_10), .in_2(b_smallmemory_2_out_11), .in_3(b_smallmemory_2_out_12),
    .in_4(b_smallmemory_2_out_13), .in_5(b_smallmemory_2_out_14), .in_6(b_smallmemory_2_out_15),
    .in_7(b_smallmemory_2_out_16), .in_8(b_smallmemory_2_out_17), .in_9(and_7_out),
    .out_10(e_andgroub_2_out_10[0]), .out_11(e_andgroub_2_out_10[1]), .out_12(e_andgroub_2_out_10[2]),
    .out_13(e_andgroub_2_out_10[3]), .out_14(e_andgroub_2_out_10[4]), .out_15(e_andgroub_2_out_10[5]),
    .out_16(e_andgroub_2_out_10[6]), .out_17(e_andgroub_2_out_10[7]));
  E_andgroub e_andgroub_3 (
    .in_1(b_smallmemory_3_out_10), .in_2(b_smallmemory_3_out_11), .in_3(b_smallmemory_3_out_12),
    .in_4(b_smallmemory_3_out_13), .in_5(b_smallmemory_3_out_14), .in_6(b_smallmemory_3_out_15),
    .in_7(b_smallmemory_3_out_16), .in_8(b_smallmemory_3_out_17), .in_9(and_9_out),
    .out_10(e_andgroub_3_out_10[0]), .out_11(e_andgroub_3_out_10[1]), .out_12(e_andgroub_3_out_10[2]),
    .out_13(e_andgroub_3_out_10[3]), .out_14(e_andgroub_3_out_10[4]), .out_15(e_andgroub_3_out_10[5]),
    .out_16(e_andgroub_3_out_10[6]), .out_17(e_andgroub_3_out_10[7]));
  assign controlled_buffer_1_out = and_5_out ? e_andgroub_1_out_10 : 8'bz;  // Controlled_Buffer controlled_buffer_1
  assign controlled_buffer_1_out = and_7_out ? e_andgroub_2_out_10 : 8'bz;  // Controlled_Buffer controlled_buffer_2
  assign controlled_buffer_1_out = and_9_out ? e_andgroub_3_out_10 : 8'bz;  // Controlled_Buffer controlled_buffer_3
  assign out_16 = in_3 ? controlled_buffer_1_out : 8'bz;  // Controlled_Buffer controlled_buffer_4
  assign controlled_buffer_1_out = in_6 ? in_4 : 8'bz;  // Controlled_Buffer controlled_buffer_5
endmodule

module B_smallmemory (
  input  in_1,
  input  in_2,
  input  in_3,
  input  in_4,
  input  in_5,
  input  in_6,
  input  in_7,
  input  in_8,
  input  S,
  output out_10,
  output out_11,
  output out_12,
  output out_13,
  output out_14,
  output out_15,
  output out_16,
  output out_17
);

  D_Flip_Flop d_ff_1 (.clk(S), .D(in_1), .Q(out_10));  // open: Qn, preset, en, reset
  D_Flip_Flop d_ff_2 (.clk(S), .D(in_2), .Q(out_11));  // open: Qn, preset, en, reset
  D_Flip_Flop d_ff_3 (.clk(S), .D(in_3), .Q(out_12));  // open: Qn, preset, en, reset
  D_Flip_Flop d_ff_4 (.clk(S), .D(in_4), .Q(out_13));  // open: Qn, preset, en, reset
  D_Flip_Flop d_ff_5 (.clk(S), .D(in_5), .Q(out_14));  // open: Qn, preset, en, reset
  D_Flip_Flop d_ff_6 (.clk(S), .D(in_6), .Q(out_15));  // open: Qn, preset, en, reset
  D_Flip_Flop d_ff_7 (.clk(S), .D(in_7), .Q(out_16));  // open: Qn, preset, en, reset
  D_Flip_Flop d_ff_8 (.clk(S), .D(in_8), .Q(out_17));  // open: Qn, preset, en, reset
endmodule

module E_andgroub (
  input  in_1,
  input  in_2,
  input  in_3,
  input  in_4,
  input  in_5,
  input  in_6,
  input  in_7,
  input  in_8,
  input  in_9,
  output out_10,
  output out_11,
  output out_12,
  output out_13,
  output out_14,
  output out_15,
  output out_16,
  output out_17
);

  and and_1 (out_10, in_1, in_9);
  and and_2 (out_11, in_2, in_9);
  and and_3 (out_12, in_3, in_9);
  and and_4 (out_13, in_4, in_9);
  and and_5 (out_14, in_5, in_9);
  and and_6 (out_15, in_6, in_9);
  and and_7 (out_16, in_7, in_9);
  and and_8 (out_17, in_8, in_9);
endmodule

module R (
  input  [7:0] in_1,
  input  in_2,
  input  in_3,
  output [7:0] out_4
);

  wire b_smallmemory_1_out_10, b_smallmemory_1_out_11, b_smallmemory_1_out_12, b_smallmemory_1_out_13,
       b_smallmemory_1_out_14, b_smallmemory_1_out_15, b_smallmemory_1_out_16, b_smallmemory_1_out_17;

  B_smallmemory b_smallmemory_1 (
    .in_1(in_1[0]), .in_2(in_1[1]), .in_3(in_1[2]), .in_4(in_1[3]), .in_5(in_1[4]), .in_6(in_1[5]),
    .in_7(in_1[6]), .in_8(in_1[7]), .S(in_2), .out_10(b_smallmemory_1_out_10),
    .out_11(b_smallmemory_1_out_11), .out_12(b_smallmemory_1_out_12), .out_13(b_smallmemory_1_out_13),
    .out_14(b_smallmemory_1_out_14), .out_15(b_smallmemory_1_out_15), .out_16(b_smallmemory_1_out_16),
    .out_17(b_smallmemory_1_out_17));
  E_andgroub e_andgroub_1 (
    .in_1(b_smallmemory_1_out_10), .in_2(b_smallmemory_1_out_11), .in_3(b_smallmemory_1_out_12),
    .in_4(b_smallmemory_1_out_13), .in_5(b_smallmemory_1_out_14), .in_6(b_smallmemory_1_out_15),
    .in_7(b_smallmemory_1_out_16), .in_8(b_smallmemory_1_out_17), .in_9(in_3), .out_10(out_4[0]),
    .out_11(out_4[1]), .out_12(out_4[2]), .out_13(out_4[3]), .out_14(out_4[4]), .out_15(out_4[5]),
    .out_16(out_4[6]), .out_17(out_4[7]));
endmodule

module R1 (
  input  in_1,
  input  in_2,
  output [7:0] out_3
);

  wire b_smallmemory_1_out_10, b_smallmemory_1_out_11, b_smallmemory_1_out_12, b_smallmemory_1_out_13,
       b_smallmemory_1_out_14, b_smallmemory_1_out_15, b_smallmemory_1_out_16, b_smallmemory_1_out_17;
  wire [7:0] e_andgroub_1_out_10;

  B_smallmemory b_smallmemory_1 (
    .in_1(out_3[0]), .in_2(out_3[1]), .in_3(out_3[2]), .in_4(out_3[3]), .in_5(out_3[4]), .in_6(out_3[5]),
    .in_7(out_3[6]), .in_8(out_3[7]), .S(in_1), .out_10(b_smallmemory_1_out_10),
    .out_11(b_smallmemory_1_out_11), .out_12(b_smallmemory_1_out_12), .out_13(b_smallmemory_1_out_13),
    .out_14(b_smallmemory_1_out_14), .out_15(b_smallmemory_1_out_15), .out_16(b_smallmemory_1_out_16),
    .out_17(b_smallmemory_1_out_17));
  E_andgroub e_andgroub_1 (
    .in_1(b_smallmemory_1_out_10), .in_2(b_smallmemory_1_out_11), .in_3(b_smallmemory_1_out_12),
    .in_4(b_smallmemory_1_out_13), .in_5(b_smallmemory_1_out_14), .in_6(b_smallmemory_1_out_15),
    .in_7(b_smallmemory_1_out_16), .in_8(b_smallmemory_1_out_17), .in_9(in_2),
    .out_10(e_andgroub_1_out_10[0]), .out_11(e_andgroub_1_out_10[1]), .out_12(e_andgroub_1_out_10[2]),
    .out_13(e_andgroub_1_out_10[3]), .out_14(e_andgroub_1_out_10[4]), .out_15(e_andgroub_1_out_10[5]),
    .out_16(e_andgroub_1_out_10[6]), .out_17(e_andgroub_1_out_10[7]));
  assign out_3 = in_2 ? e_andgroub_1_out_10 : 8'bz;  // Controlled_Buffer controlled_buffer_1
endmodule

module RAM (
  input  [7:0] in_1,
  input  [7:0] in_2,
  input  in_3,
  input  S,
  input  R,
  output [7:0] out_6
);

  wire decoder_1_out0, decoder_1_out1, decoder_1_out2, decoder_1_out3, decoder_1_out4, decoder_1_out5,
       decoder_1_out6, decoder_1_out7, decoder_1_out8, decoder_1_out9, decoder_1_out10, decoder_1_out11,
       decoder_1_out12, decoder_1_out13, decoder_1_out14, decoder_1_out15, decoder_2_out0, decoder_2_out1,
       decoder_2_out2, decoder_2_out3, decoder_2_out4, decoder_2_out5, decoder_2_out6, decoder_2_out7,
       decoder_2_out8, decoder_2_out9, decoder_2_out10, decoder_2_out11, decoder_2_out12, decoder_2_out13,
       decoder_2_out14, decoder_2_out15;
  wire [7:0] e_onepin_1_out_3;

  E_onepin e_onepin_1 (.in_2(in_3), .out_3(e_onepin_1_out_3), .in_1(in_2));
  Decoder #(.select(4)) decoder_1 (
    .out0(decoder_1_out0), .out1(decoder_1_out1), .out2(decoder_1_out2), .out3(decoder_1_out3),
    .out4(decoder_1_out4), .out5(decoder_1_out5), .out6(decoder_1_out6), .out7(decoder_1_out7),
    .out8(decoder_1_out8), .out9(decoder_1_out9), .out10(decoder_1_out10), .out11(decoder_1_out11),
    .out12(decoder_1_out12), .out13(decoder_1_out13), .out14(decoder_1_out14), .out15(decoder_1_out15),
    .sel(e_onepin_1_out_3[7:4]));  // open: en
  R_for_RAM r_for_ram_1 (.in_2(decoder_1_out0), .in_3(decoder_2_out0), .in_4(S), .in_5(R), .out_6(out_6), .in_1(in_1));
  R_for_RAM r_for_ram_2 (
    .in_2(decoder_1_out1), .in_3(decoder_2_out0), .in_4(S), .out_6(out_6), .in_1(in_1));  // open: in_5
  R_for_RAM r_for_ram_3 (.in_2(decoder_1_out2), .in_3(decoder_2_out0), .in_4(S), .in_5(R), .out_6(out_6), .in_1(in_1));
  R_for_RAM r_for_ram_4 (.in_2(decoder_1_out3), .in_3(decoder_2_out0), .in_4(S), .in_5(R), .out_6(out_6), .in_1(in_1));
  R_for_RAM r_for_ram_5 (.in_2(decoder_1_out4), .in_3(decoder_2_out0), .in_4(S), .in_5(R), .out_6(out_6), .in_1(in_1));
  R_for_RAM r_for_ram_6 (.in_2(decoder_1_out5), .in_3(decoder_2_out0), .in_4(S), .in_5(R), .out_6(out_6), .in_1(in_1));
  R_for_RAM r_for_ram_7 (.in_2(decoder_1_out6), .in_3(decoder_2_out0), .in_4(S), .in_5(R), .out_6(out_6), .in_1(in_1));
  R_for_RAM r_for_ram_8 (.in_2(decoder_1_out7), .in_3(decoder_2_out0), .in_4(S), .in_5(R), .out_6(out_6), .in_1(in_1));
  R_for_RAM r_for_ram_9 (.in_2(decoder_1_out8), .in_3(decoder_2_out0), .in_4(S), .in_5(R), .out_6(out_6), .in_1(in_1));
  R_for_RAM r_for_ram_10 (.in_2(decoder_1_out9), .in_3(decoder_2_out0), .in_4(S), .in_5(R), .out_6(out_6), .in_1(in_1));
  R_for_RAM r_for_ram_11 (
    .in_2(decoder_1_out10), .in_3(decoder_2_out0), .in_4(S), .in_5(R), .out_6(out_6), .in_1(in_1));
  R_for_RAM r_for_ram_12 (
    .in_2(decoder_1_out11), .in_3(decoder_2_out0), .in_4(S), .in_5(R), .out_6(out_6), .in_1(in_1));
  R_for_RAM r_for_ram_13 (
    .in_2(decoder_1_out12), .in_3(decoder_2_out0), .in_4(S), .in_5(R), .out_6(out_6), .in_1(in_1));
  R_for_RAM r_for_ram_14 (
    .in_2(decoder_1_out13), .in_3(decoder_2_out0), .in_4(S), .in_5(R), .out_6(out_6), .in_1(in_1));
  R_for_RAM r_for_ram_15 (
    .in_2(decoder_1_out14), .in_3(decoder_2_out0), .in_4(S), .in_5(R), .out_6(out_6), .in_1(in_1));
  R_for_RAM r_for_ram_16 (
    .in_2(decoder_1_out15), .in_3(decoder_2_out0), .in_4(S), .in_5(R), .out_6(out_6), .in_1(in_1));
  Decoder #(.select(4)) decoder_2 (
    .out0(decoder_2_out0), .out1(decoder_2_out1), .out2(decoder_2_out2), .out3(decoder_2_out3),
    .out4(decoder_2_out4), .out5(decoder_2_out5), .out6(decoder_2_out6), .out7(decoder_2_out7),
    .out8(decoder_2_out8), .out9(decoder_2_out9), .out10(decoder_2_out10), .out11(decoder_2_out11),
    .out12(decoder_2_out12), .out13(decoder_2_out13), .out14(decoder_2_out14), .out15(decoder_2_out15),
    .sel(e_onepin_1_out_3[3:0]));  // open: en
  R_for_RAM r_for_ram_17 (.in_2(decoder_1_out0), .in_3(decoder_2_out1), .in_4(S), .in_5(R), .out_6(out_6), .in_1(in_1));
  R_for_RAM r_for_ram_18 (.in_2(decoder_1_out1), .in_3(decoder_2_out1), .in_4(S), .in_5(R), .out_6(out_6), .in_1(in_1));
  R_for_RAM r_for_ram_19 (.in_2(decoder_1_out2), .in_3(decoder_2_out1), .in_4(S), .in_5(R), .out_6(out_6), .in_1(in_1));
  R_for_RAM r_for_ram_20 (.in_2(decoder_1_out3), .in_3(decoder_2_out1), .in_4(S), .in_5(R), .out_6(out_6), .in_1(in_1));
  R_for_RAM r_for_ram_21 (.in_2(decoder_1_out4), .in_3(decoder_2_out1), .in_4(S), .in_5(R), .out_6(out_6), .in_1(in_1));
  R_for_RAM r_for_ram_22 (.in_2(decoder_1_out5), .in_3(decoder_2_out1), .in_4(S), .in_5(R), .out_6(out_6), .in_1(in_1));
  R_for_RAM r_for_ram_23 (.in_2(decoder_1_out6), .in_3(decoder_2_out1), .in_4(S), .in_5(R), .out_6(out_6), .in_1(in_1));
  R_for_RAM r_for_ram_24 (.in_2(decoder_1_out7), .in_3(decoder_2_out1), .in_4(S), .in_5(R), .out_6(out_6), .in_1(in_1));
  R_for_RAM r_for_ram_25 (.in_2(decoder_1_out8), .in_3(decoder_2_out1), .in_4(S), .in_5(R), .out_6(out_6), .in_1(in_1));
  R_for_RAM r_for_ram_26 (.in_2(decoder_1_out9), .in_3(decoder_2_out1), .in_4(S), .in_5(R), .out_6(out_6), .in_1(in_1));
  R_for_RAM r_for_ram_27 (
    .in_2(decoder_1_out10), .in_3(decoder_2_out1), .in_4(S), .in_5(R), .out_6(out_6), .in_1(in_1));
  R_for_RAM r_for_ram_28 (
    .in_2(decoder_1_out11), .in_3(decoder_2_out1), .in_4(S), .in_5(R), .out_6(out_6), .in_1(in_1));
  R_for_RAM r_for_ram_29 (
    .in_2(decoder_1_out12), .in_3(decoder_2_out1), .in_4(S), .in_5(R), .out_6(out_6), .in_1(in_1));
  R_for_RAM r_for_ram_30 (
    .in_2(decoder_1_out13), .in_3(decoder_2_out1), .in_4(S), .in_5(R), .out_6(out_6), .in_1(in_1));
  R_for_RAM r_for_ram_31 (
    .in_2(decoder_1_out14), .in_3(decoder_2_out1), .in_4(S), .in_5(R), .out_6(out_6), .in_1(in_1));
  R_for_RAM r_for_ram_32 (
    .in_2(decoder_1_out15), .in_3(decoder_2_out1), .in_4(S), .in_5(R), .out_6(out_6), .in_1(in_1));
  R_for_RAM r_for_ram_33 (.in_2(decoder_1_out0), .in_3(decoder_2_out2), .in_4(S), .in_5(R), .out_6(out_6), .in_1(in_1));
  R_for_RAM r_for_ram_34 (.in_2(decoder_1_out1), .in_3(decoder_2_out2), .in_4(S), .in_5(R), .out_6(out_6), .in_1(in_1));
  R_for_RAM r_for_ram_35 (.in_2(decoder_1_out2), .in_3(decoder_2_out2), .in_4(S), .in_5(R), .out_6(out_6), .in_1(in_1));
  R_for_RAM r_for_ram_36 (.in_2(decoder_1_out3), .in_3(decoder_2_out2), .in_4(S), .in_5(R), .out_6(out_6), .in_1(in_1));
  R_for_RAM r_for_ram_37 (.in_2(decoder_1_out4), .in_3(decoder_2_out2), .in_4(S), .in_5(R), .out_6(out_6), .in_1(in_1));
  R_for_RAM r_for_ram_38 (.in_2(decoder_1_out5), .in_3(decoder_2_out2), .in_4(S), .in_5(R), .out_6(out_6), .in_1(in_1));
  R_for_RAM r_for_ram_39 (.in_2(decoder_1_out6), .in_3(decoder_2_out2), .in_4(S), .in_5(R), .out_6(out_6), .in_1(in_1));
  R_for_RAM r_for_ram_40 (.in_2(decoder_1_out7), .in_3(decoder_2_out2), .in_4(S), .in_5(R), .out_6(out_6), .in_1(in_1));
  R_for_RAM r_for_ram_41 (.in_2(decoder_1_out8), .in_3(decoder_2_out2), .in_4(S), .in_5(R), .out_6(out_6), .in_1(in_1));
  R_for_RAM r_for_ram_42 (.in_2(decoder_1_out9), .in_3(decoder_2_out2), .in_4(S), .in_5(R), .out_6(out_6), .in_1(in_1));
  R_for_RAM r_for_ram_43 (
    .in_2(decoder_1_out10), .in_3(decoder_2_out2), .in_4(S), .in_5(R), .out_6(out_6), .in_1(in_1));
  R_for_RAM r_for_ram_44 (
    .in_2(decoder_1_out11), .in_3(decoder_2_out2), .in_4(S), .in_5(R), .out_6(out_6), .in_1(in_1));
  R_for_RAM r_for_ram_45 (
    .in_2(decoder_1_out12), .in_3(decoder_2_out2), .in_4(S), .in_5(R), .out_6(out_6), .in_1(in_1));
  R_for_RAM r_for_ram_46 (
    .in_2(decoder_1_out13), .in_3(decoder_2_out2), .in_4(S), .in_5(R), .out_6(out_6), .in_1(in_1));
  R_for_RAM r_for_ram_47 (
    .in_2(decoder_1_out14), .in_3(decoder_2_out2), .in_4(S), .in_5(R), .out_6(out_6), .in_1(in_1));
  R_for_RAM r_for_ram_48 (
    .in_2(decoder_1_out15), .in_3(decoder_2_out2), .in_4(S), .in_5(R), .out_6(out_6), .in_1(in_1));
  R_for_RAM r_for_ram_49 (.in_2(decoder_1_out0), .in_3(decoder_2_out3), .in_4(S), .in_5(R), .out_6(out_6), .in_1(in_1));
  R_for_RAM r_for_ram_50 (.in_2(decoder_1_out1), .in_3(decoder_2_out3), .in_4(S), .in_5(R), .out_6(out_6), .in_1(in_1));
  R_for_RAM r_for_ram_51 (.in_2(decoder_1_out2), .in_3(decoder_2_out3), .in_4(S), .in_5(R), .out_6(out_6), .in_1(in_1));
  R_for_RAM r_for_ram_52 (.in_2(decoder_1_out3), .in_3(decoder_2_out3), .in_4(S), .in_5(R), .out_6(out_6), .in_1(in_1));
  R_for_RAM r_for_ram_53 (.in_2(decoder_1_out4), .in_3(decoder_2_out3), .in_4(S), .in_5(R), .out_6(out_6), .in_1(in_1));
  R_for_RAM r_for_ram_54 (.in_2(decoder_1_out5), .in_3(decoder_2_out3), .in_4(S), .in_5(R), .out_6(out_6), .in_1(in_1));
  R_for_RAM r_for_ram_55 (.in_2(decoder_1_out6), .in_3(decoder_2_out3), .in_4(S), .in_5(R), .out_6(out_6), .in_1(in_1));
  R_for_RAM r_for_ram_56 (.in_2(decoder_1_out7), .in_3(decoder_2_out3), .in_4(S), .in_5(R), .out_6(out_6), .in_1(in_1));
  R_for_RAM r_for_ram_57 (.in_2(decoder_1_out8), .in_3(decoder_2_out3), .in_4(S), .in_5(R), .out_6(out_6), .in_1(in_1));
  R_for_RAM r_for_ram_58 (.in_2(decoder_1_out9), .in_3(decoder_2_out3), .in_4(S), .in_5(R), .out_6(out_6), .in_1(in_1));
  R_for_RAM r_for_ram_59 (
    .in_2(decoder_1_out10), .in_3(decoder_2_out3), .in_4(S), .in_5(R), .out_6(out_6), .in_1(in_1));
  R_for_RAM r_for_ram_60 (
    .in_2(decoder_1_out11), .in_3(decoder_2_out3), .in_4(S), .in_5(R), .out_6(out_6), .in_1(in_1));
  R_for_RAM r_for_ram_61 (
    .in_2(decoder_1_out12), .in_3(decoder_2_out3), .in_4(S), .in_5(R), .out_6(out_6), .in_1(in_1));
  R_for_RAM r_for_ram_62 (
    .in_2(decoder_1_out13), .in_3(decoder_2_out3), .in_4(S), .in_5(R), .out_6(out_6), .in_1(in_1));
  R_for_RAM r_for_ram_63 (
    .in_2(decoder_1_out14), .in_3(decoder_2_out3), .in_4(S), .in_5(R), .out_6(out_6), .in_1(in_1));
  R_for_RAM r_for_ram_64 (
    .in_2(decoder_1_out15), .in_3(decoder_2_out3), .in_4(S), .in_5(R), .out_6(out_6), .in_1(in_1));
  R_for_RAM r_for_ram_65 (.in_2(decoder_1_out0), .in_3(decoder_2_out4), .in_4(S), .in_5(R), .out_6(out_6), .in_1(in_1));
  R_for_RAM r_for_ram_66 (.in_2(decoder_1_out1), .in_3(decoder_2_out4), .in_4(S), .in_5(R), .out_6(out_6), .in_1(in_1));
  R_for_RAM r_for_ram_67 (.in_2(decoder_1_out2), .in_3(decoder_2_out4), .in_4(S), .in_5(R), .out_6(out_6), .in_1(in_1));
  R_for_RAM r_for_ram_68 (.in_2(decoder_1_out3), .in_3(decoder_2_out4), .in_4(S), .in_5(R), .out_6(out_6), .in_1(in_1));
  R_for_RAM r_for_ram_69 (.in_2(decoder_1_out4), .in_3(decoder_2_out4), .in_4(S), .in_5(R), .out_6(out_6), .in_1(in_1));
  R_for_RAM r_for_ram_70 (.in_2(decoder_1_out5), .in_3(decoder_2_out4), .in_4(S), .in_5(R), .out_6(out_6), .in_1(in_1));
  R_for_RAM r_for_ram_71 (.in_2(decoder_1_out6), .in_3(decoder_2_out4), .in_4(S), .in_5(R), .out_6(out_6), .in_1(in_1));
  R_for_RAM r_for_ram_72 (.in_2(decoder_1_out7), .in_3(decoder_2_out4), .in_4(S), .in_5(R), .out_6(out_6), .in_1(in_1));
  R_for_RAM r_for_ram_73 (.in_2(decoder_1_out8), .in_3(decoder_2_out4), .in_4(S), .in_5(R), .out_6(out_6), .in_1(in_1));
  R_for_RAM r_for_ram_74 (.in_2(decoder_1_out9), .in_3(decoder_2_out4), .in_4(S), .in_5(R), .out_6(out_6), .in_1(in_1));
  R_for_RAM r_for_ram_75 (
    .in_2(decoder_1_out10), .in_3(decoder_2_out4), .in_4(S), .in_5(R), .out_6(out_6), .in_1(in_1));
  R_for_RAM r_for_ram_76 (
    .in_2(decoder_1_out11), .in_3(decoder_2_out4), .in_4(S), .in_5(R), .out_6(out_6), .in_1(in_1));
  R_for_RAM r_for_ram_77 (
    .in_2(decoder_1_out12), .in_3(decoder_2_out4), .in_4(S), .in_5(R), .out_6(out_6), .in_1(in_1));
  R_for_RAM r_for_ram_78 (
    .in_2(decoder_1_out13), .in_3(decoder_2_out4), .in_4(S), .in_5(R), .out_6(out_6), .in_1(in_1));
  R_for_RAM r_for_ram_79 (
    .in_2(decoder_1_out14), .in_3(decoder_2_out4), .in_4(S), .in_5(R), .out_6(out_6), .in_1(in_1));
  R_for_RAM r_for_ram_80 (
    .in_2(decoder_1_out15), .in_3(decoder_2_out4), .in_4(S), .in_5(R), .out_6(out_6), .in_1(in_1));
  R_for_RAM r_for_ram_81 (.in_2(decoder_1_out0), .in_3(decoder_2_out5), .in_4(S), .in_5(R), .out_6(out_6), .in_1(in_1));
  R_for_RAM r_for_ram_82 (.in_2(decoder_1_out1), .in_3(decoder_2_out5), .in_4(S), .in_5(R), .out_6(out_6), .in_1(in_1));
  R_for_RAM r_for_ram_83 (.in_2(decoder_1_out2), .in_3(decoder_2_out5), .in_4(S), .in_5(R), .out_6(out_6), .in_1(in_1));
  R_for_RAM r_for_ram_84 (.in_2(decoder_1_out3), .in_3(decoder_2_out5), .in_4(S), .in_5(R), .out_6(out_6), .in_1(in_1));
  R_for_RAM r_for_ram_85 (.in_2(decoder_1_out4), .in_3(decoder_2_out5), .in_4(S), .in_5(R), .out_6(out_6), .in_1(in_1));
  R_for_RAM r_for_ram_86 (.in_2(decoder_1_out5), .in_3(decoder_2_out5), .in_4(S), .in_5(R), .out_6(out_6), .in_1(in_1));
  R_for_RAM r_for_ram_87 (.in_2(decoder_1_out6), .in_3(decoder_2_out5), .in_4(S), .in_5(R), .out_6(out_6), .in_1(in_1));
  R_for_RAM r_for_ram_88 (.in_2(decoder_1_out7), .in_3(decoder_2_out5), .in_4(S), .in_5(R), .out_6(out_6), .in_1(in_1));
  R_for_RAM r_for_ram_89 (.in_2(decoder_1_out8), .in_3(decoder_2_out5), .in_4(S), .in_5(R), .out_6(out_6), .in_1(in_1));
  R_for_RAM r_for_ram_90 (.in_2(decoder_1_out9), .in_3(decoder_2_out5), .in_4(S), .in_5(R), .out_6(out_6), .in_1(in_1));
  R_for_RAM r_for_ram_91 (
    .in_2(decoder_1_out10), .in_3(decoder_2_out5), .in_4(S), .in_5(R), .out_6(out_6), .in_1(in_1));
  R_for_RAM r_for_ram_92 (
    .in_2(decoder_1_out11), .in_3(decoder_2_out5), .in_4(S), .in_5(R), .out_6(out_6), .in_1(in_1));
  R_for_RAM r_for_ram_93 (
    .in_2(decoder_1_out12), .in_3(decoder_2_out5), .in_4(S), .in_5(R), .out_6(out_6), .in_1(in_1));
  R_for_RAM r_for_ram_94 (
    .in_2(decoder_1_out13), .in_3(decoder_2_out5), .in_4(S), .in_5(R), .out_6(out_6), .in_1(in_1));
  R_for_RAM r_for_ram_95 (
    .in_2(decoder_1_out14), .in_3(decoder_2_out5), .in_4(S), .in_5(R), .out_6(out_6), .in_1(in_1));
  R_for_RAM r_for_ram_96 (
    .in_2(decoder_1_out15), .in_3(decoder_2_out5), .in_4(S), .in_5(R), .out_6(out_6), .in_1(in_1));
  R_for_RAM r_for_ram_97 (.in_2(decoder_1_out0), .in_3(decoder_2_out6), .in_4(S), .in_5(R), .out_6(out_6), .in_1(in_1));
  R_for_RAM r_for_ram_98 (.in_2(decoder_1_out1), .in_3(decoder_2_out6), .in_4(S), .in_5(R), .out_6(out_6), .in_1(in_1));
  R_for_RAM r_for_ram_99 (.in_2(decoder_1_out2), .in_3(decoder_2_out6), .in_4(S), .in_5(R), .out_6(out_6), .in_1(in_1));
  R_for_RAM r_for_ram_100 (
    .in_2(decoder_1_out3), .in_3(decoder_2_out6), .in_4(S), .in_5(R), .out_6(out_6), .in_1(in_1));
  R_for_RAM r_for_ram_101 (
    .in_2(decoder_1_out4), .in_3(decoder_2_out6), .in_4(S), .in_5(R), .out_6(out_6), .in_1(in_1));
  R_for_RAM r_for_ram_102 (
    .in_2(decoder_1_out5), .in_3(decoder_2_out6), .in_4(S), .in_5(R), .out_6(out_6));  // open: in_1
  R_for_RAM r_for_ram_103 (
    .in_2(decoder_1_out6), .in_3(decoder_2_out6), .in_4(S), .in_5(R), .out_6(out_6), .in_1(in_1));
  R_for_RAM r_for_ram_104 (
    .in_2(decoder_1_out7), .in_3(decoder_2_out6), .in_4(S), .in_5(R), .out_6(out_6), .in_1(in_1));
  R_for_RAM r_for_ram_105 (
    .in_2(decoder_1_out8), .in_3(decoder_2_out6), .in_4(S), .in_5(R), .out_6(out_6), .in_1(in_1));
  R_for_RAM r_for_ram_106 (
    .in_2(decoder_1_out9), .in_3(decoder_2_out6), .in_4(S), .in_5(R), .out_6(out_6), .in_1(in_1));
  R_for_RAM r_for_ram_107 (
    .in_2(decoder_1_out10), .in_3(decoder_2_out6), .in_4(S), .in_5(R), .out_6(out_6), .in_1(in_1));
  R_for_RAM r_for_ram_108 (
    .in_2(decoder_1_out11), .in_3(decoder_2_out6), .in_4(S), .in_5(R), .out_6(out_6), .in_1(in_1));
  R_for_RAM r_for_ram_109 (
    .in_2(decoder_1_out12), .in_3(decoder_2_out6), .in_4(S), .in_5(R), .out_6(out_6), .in_1(in_1));
  R_for_RAM r_for_ram_110 (
    .in_2(decoder_1_out13), .in_3(decoder_2_out6), .in_4(S), .in_5(R), .out_6(out_6), .in_1(in_1));
  R_for_RAM r_for_ram_111 (
    .in_2(decoder_1_out14), .in_3(decoder_2_out6), .in_4(S), .in_5(R), .out_6(out_6), .in_1(in_1));
  R_for_RAM r_for_ram_112 (
    .in_2(decoder_1_out15), .in_3(decoder_2_out6), .in_4(S), .in_5(R), .out_6(out_6), .in_1(in_1));
  R_for_RAM r_for_ram_113 (
    .in_2(decoder_1_out0), .in_3(decoder_2_out7), .in_4(S), .in_5(R), .out_6(out_6), .in_1(in_1));
  R_for_RAM r_for_ram_114 (
    .in_2(decoder_1_out1), .in_3(decoder_2_out7), .in_4(S), .in_5(R), .out_6(out_6), .in_1(in_1));
  R_for_RAM r_for_ram_115 (
    .in_2(decoder_1_out2), .in_3(decoder_2_out7), .in_4(S), .in_5(R), .out_6(out_6), .in_1(in_1));
  R_for_RAM r_for_ram_116 (
    .in_2(decoder_1_out3), .in_3(decoder_2_out7), .in_4(S), .in_5(R), .out_6(out_6), .in_1(in_1));
  R_for_RAM r_for_ram_117 (
    .in_2(decoder_1_out4), .in_3(decoder_2_out7), .in_4(S), .in_5(R), .out_6(out_6), .in_1(in_1));
  R_for_RAM r_for_ram_118 (
    .in_2(decoder_1_out5), .in_3(decoder_2_out7), .in_4(S), .in_5(R), .out_6(out_6));  // open: in_1
  R_for_RAM r_for_ram_119 (
    .in_2(decoder_1_out6), .in_3(decoder_2_out7), .in_4(S), .in_5(R), .out_6(out_6), .in_1(in_1));
  R_for_RAM r_for_ram_120 (
    .in_2(decoder_1_out7), .in_3(decoder_2_out7), .in_4(S), .in_5(R), .out_6(out_6), .in_1(in_1));
  R_for_RAM r_for_ram_121 (
    .in_2(decoder_1_out8), .in_3(decoder_2_out7), .in_4(S), .in_5(R), .out_6(out_6), .in_1(in_1));
  R_for_RAM r_for_ram_122 (
    .in_2(decoder_1_out9), .in_3(decoder_2_out7), .in_4(S), .in_5(R), .out_6(out_6), .in_1(in_1));
  R_for_RAM r_for_ram_123 (
    .in_2(decoder_1_out10), .in_3(decoder_2_out7), .in_4(S), .in_5(R), .out_6(out_6), .in_1(in_1));
  R_for_RAM r_for_ram_124 (
    .in_2(decoder_1_out11), .in_3(decoder_2_out7), .in_4(S), .in_5(R), .out_6(out_6), .in_1(in_1));
  R_for_RAM r_for_ram_125 (
    .in_2(decoder_1_out12), .in_3(decoder_2_out7), .in_4(S), .in_5(R), .out_6(out_6), .in_1(in_1));
  R_for_RAM r_for_ram_126 (
    .in_2(decoder_1_out13), .in_3(decoder_2_out7), .in_4(S), .in_5(R), .out_6(out_6), .in_1(in_1));
  R_for_RAM r_for_ram_127 (
    .in_2(decoder_1_out14), .in_3(decoder_2_out7), .in_4(S), .in_5(R), .out_6(out_6), .in_1(in_1));
  R_for_RAM r_for_ram_128 (
    .in_2(decoder_1_out15), .in_3(decoder_2_out7), .in_4(S), .in_5(R), .out_6(out_6), .in_1(in_1));
  R_for_RAM r_for_ram_129 (
    .in_2(decoder_1_out0), .in_3(decoder_2_out8), .in_4(S), .in_5(R), .out_6(out_6), .in_1(in_1));
  R_for_RAM r_for_ram_130 (
    .in_2(decoder_1_out1), .in_3(decoder_2_out8), .in_4(S), .in_5(R), .out_6(out_6), .in_1(in_1));
  R_for_RAM r_for_ram_131 (
    .in_2(decoder_1_out2), .in_3(decoder_2_out8), .in_4(S), .in_5(R), .out_6(out_6), .in_1(in_1));
  R_for_RAM r_for_ram_132 (
    .in_2(decoder_1_out3), .in_3(decoder_2_out8), .in_4(S), .in_5(R), .out_6(out_6), .in_1(in_1));
  R_for_RAM r_for_ram_133 (
    .in_2(decoder_1_out4), .in_3(decoder_2_out8), .in_4(S), .in_5(R), .out_6(out_6), .in_1(in_1));
  R_for_RAM r_for_ram_134 (
    .in_2(decoder_1_out5), .in_3(decoder_2_out8), .in_4(S), .in_5(R), .out_6(out_6));  // open: in_1
  R_for_RAM r_for_ram_135 (
    .in_2(decoder_1_out6), .in_3(decoder_2_out8), .in_4(S), .in_5(R), .out_6(out_6), .in_1(in_1));
  R_for_RAM r_for_ram_136 (
    .in_2(decoder_1_out7), .in_3(decoder_2_out8), .in_4(S), .in_5(R), .out_6(out_6), .in_1(in_1));
  R_for_RAM r_for_ram_137 (
    .in_2(decoder_1_out8), .in_3(decoder_2_out8), .in_4(S), .in_5(R), .out_6(out_6), .in_1(in_1));
  R_for_RAM r_for_ram_138 (
    .in_2(decoder_1_out9), .in_3(decoder_2_out8), .in_4(S), .in_5(R), .out_6(out_6), .in_1(in_1));
  R_for_RAM r_for_ram_139 (
    .in_2(decoder_1_out10), .in_3(decoder_2_out8), .in_4(S), .in_5(R), .out_6(out_6), .in_1(in_1));
  R_for_RAM r_for_ram_140 (
    .in_2(decoder_1_out11), .in_3(decoder_2_out8), .in_4(S), .in_5(R), .out_6(out_6), .in_1(in_1));
  R_for_RAM r_for_ram_141 (
    .in_2(decoder_1_out12), .in_3(decoder_2_out8), .in_4(S), .in_5(R), .out_6(out_6), .in_1(in_1));
  R_for_RAM r_for_ram_142 (
    .in_2(decoder_1_out13), .in_3(decoder_2_out8), .in_4(S), .in_5(R), .out_6(out_6), .in_1(in_1));
  R_for_RAM r_for_ram_143 (
    .in_2(decoder_1_out14), .in_3(decoder_2_out8), .in_4(S), .in_5(R), .out_6(out_6), .in_1(in_1));
  R_for_RAM r_for_ram_144 (
    .in_2(decoder_1_out15), .in_3(decoder_2_out8), .in_4(S), .in_5(R), .out_6(out_6), .in_1(in_1));
  R_for_RAM r_for_ram_145 (
    .in_2(decoder_1_out0), .in_3(decoder_2_out9), .in_4(S), .in_5(R), .out_6(out_6), .in_1(in_1));
  R_for_RAM r_for_ram_146 (
    .in_2(decoder_1_out1), .in_3(decoder_2_out9), .in_4(S), .in_5(R), .out_6(out_6), .in_1(in_1));
  R_for_RAM r_for_ram_147 (
    .in_2(decoder_1_out2), .in_3(decoder_2_out9), .in_4(S), .in_5(R), .out_6(out_6), .in_1(in_1));
  R_for_RAM r_for_ram_148 (
    .in_2(decoder_1_out3), .in_3(decoder_2_out9), .in_4(S), .in_5(R), .out_6(out_6), .in_1(in_1));
  R_for_RAM r_for_ram_149 (
    .in_2(decoder_1_out4), .in_3(decoder_2_out9), .in_4(S), .in_5(R), .out_6(out_6), .in_1(in_1));
  R_for_RAM r_for_ram_150 (
    .in_2(decoder_1_out5), .in_3(decoder_2_out9), .in_4(S), .in_5(R), .out_6(out_6));  // open: in_1
  R_for_RAM r_for_ram_151 (
    .in_2(decoder_1_out6), .in_3(decoder_2_out9), .in_4(S), .in_5(R), .out_6(out_6), .in_1(in_1));
  R_for_RAM r_for_ram_152 (
    .in_2(decoder_1_out7), .in_3(decoder_2_out9), .in_4(S), .in_5(R), .out_6(out_6), .in_1(in_1));
  R_for_RAM r_for_ram_153 (
    .in_2(decoder_1_out8), .in_3(decoder_2_out9), .in_4(S), .in_5(R), .out_6(out_6), .in_1(in_1));
  R_for_RAM r_for_ram_154 (
    .in_2(decoder_1_out9), .in_3(decoder_2_out9), .in_4(S), .in_5(R), .out_6(out_6), .in_1(in_1));
  R_for_RAM r_for_ram_155 (
    .in_2(decoder_1_out10), .in_3(decoder_2_out9), .in_4(S), .in_5(R), .out_6(out_6), .in_1(in_1));
  R_for_RAM r_for_ram_156 (
    .in_2(decoder_1_out11), .in_3(decoder_2_out9), .in_4(S), .in_5(R), .out_6(out_6), .in_1(in_1));
  R_for_RAM r_for_ram_157 (
    .in_2(decoder_1_out12), .in_3(decoder_2_out9), .in_4(S), .in_5(R), .out_6(out_6), .in_1(in_1));
  R_for_RAM r_for_ram_158 (
    .in_2(decoder_1_out13), .in_3(decoder_2_out9), .in_4(S), .in_5(R), .out_6(out_6), .in_1(in_1));
  R_for_RAM r_for_ram_159 (
    .in_2(decoder_1_out14), .in_3(decoder_2_out9), .in_4(S), .in_5(R), .out_6(out_6), .in_1(in_1));
  R_for_RAM r_for_ram_160 (
    .in_2(decoder_1_out15), .in_3(decoder_2_out9), .in_4(S), .in_5(R), .out_6(out_6), .in_1(in_1));
  R_for_RAM r_for_ram_161 (
    .in_2(decoder_1_out0), .in_3(decoder_2_out10), .in_4(S), .in_5(R), .out_6(out_6), .in_1(in_1));
  R_for_RAM r_for_ram_162 (
    .in_2(decoder_1_out1), .in_3(decoder_2_out10), .in_4(S), .in_5(R), .out_6(out_6), .in_1(in_1));
  R_for_RAM r_for_ram_163 (
    .in_2(decoder_1_out2), .in_3(decoder_2_out10), .in_4(S), .in_5(R), .out_6(out_6), .in_1(in_1));
  R_for_RAM r_for_ram_164 (
    .in_2(decoder_1_out3), .in_3(decoder_2_out10), .in_4(S), .in_5(R), .out_6(out_6), .in_1(in_1));
  R_for_RAM r_for_ram_165 (
    .in_2(decoder_1_out4), .in_3(decoder_2_out10), .in_4(S), .in_5(R), .out_6(out_6), .in_1(in_1));
  R_for_RAM r_for_ram_166 (
    .in_2(decoder_1_out5), .in_3(decoder_2_out10), .in_4(S), .in_5(R), .out_6(out_6));  // open: in_1
  R_for_RAM r_for_ram_167 (
    .in_2(decoder_1_out6), .in_3(decoder_2_out10), .in_4(S), .in_5(R), .out_6(out_6), .in_1(in_1));
  R_for_RAM r_for_ram_168 (
    .in_2(decoder_1_out7), .in_3(decoder_2_out10), .in_4(S), .in_5(R), .out_6(out_6), .in_1(in_1));
  R_for_RAM r_for_ram_169 (
    .in_2(decoder_1_out8), .in_3(decoder_2_out10), .in_4(S), .in_5(R), .out_6(out_6), .in_1(in_1));
  R_for_RAM r_for_ram_170 (
    .in_2(decoder_1_out9), .in_3(decoder_2_out10), .in_4(S), .in_5(R), .out_6(out_6), .in_1(in_1));
  R_for_RAM r_for_ram_171 (
    .in_2(decoder_1_out10), .in_3(decoder_2_out10), .in_4(S), .in_5(R), .out_6(out_6), .in_1(in_1));
  R_for_RAM r_for_ram_172 (
    .in_2(decoder_1_out11), .in_3(decoder_2_out10), .in_4(S), .in_5(R), .out_6(out_6), .in_1(in_1));
  R_for_RAM r_for_ram_173 (
    .in_2(decoder_1_out12), .in_3(decoder_2_out10), .in_4(S), .in_5(R), .out_6(out_6));  // open: in_1
  R_for_RAM r_for_ram_174 (
    .in_2(decoder_1_out13), .in_3(decoder_2_out10), .in_4(S), .in_5(R), .out_6(out_6), .in_1(in_1));
  R_for_RAM r_for_ram_175 (
    .in_2(decoder_1_out14), .in_3(decoder_2_out10), .in_4(S), .in_5(R), .out_6(out_6), .in_1(in_1));
  R_for_RAM r_for_ram_176 (
    .in_2(decoder_1_out15), .in_3(decoder_2_out10), .in_4(S), .in_5(R), .out_6(out_6), .in_1(in_1));
  R_for_RAM r_for_ram_177 (
    .in_2(decoder_1_out0), .in_3(decoder_2_out11), .in_4(S), .in_5(R), .out_6(out_6), .in_1(in_1));
  R_for_RAM r_for_ram_178 (
    .in_2(decoder_1_out1), .in_3(decoder_2_out11), .in_4(S), .in_5(R), .out_6(out_6), .in_1(in_1));
  R_for_RAM r_for_ram_179 (
    .in_2(decoder_1_out2), .in_3(decoder_2_out11), .in_4(S), .in_5(R), .out_6(out_6), .in_1(in_1));
  R_for_RAM r_for_ram_180 (
    .in_2(decoder_1_out3), .in_3(decoder_2_out11), .in_4(S), .in_5(R), .out_6(out_6), .in_1(in_1));
  R_for_RAM r_for_ram_181 (
    .in_2(decoder_1_out4), .in_3(decoder_2_out11), .in_4(S), .in_5(R), .out_6(out_6), .in_1(in_1));
  R_for_RAM r_for_ram_182 (
    .in_2(decoder_1_out5), .in_3(decoder_2_out11), .in_4(S), .in_5(R), .out_6(out_6));  // open: in_1
  R_for_RAM r_for_ram_183 (
    .in_2(decoder_1_out6), .in_3(decoder_2_out11), .in_4(S), .in_5(R), .out_6(out_6), .in_1(in_1));
  R_for_RAM r_for_ram_184 (
    .in_2(decoder_1_out7), .in_3(decoder_2_out11), .in_4(S), .in_5(R), .out_6(out_6), .in_1(in_1));
  R_for_RAM r_for_ram_185 (
    .in_2(decoder_1_out8), .in_3(decoder_2_out11), .in_4(S), .in_5(R), .out_6(out_6), .in_1(in_1));
  R_for_RAM r_for_ram_186 (
    .in_2(decoder_1_out9), .in_3(decoder_2_out11), .in_4(S), .in_5(R), .out_6(out_6), .in_1(in_1));
  R_for_RAM r_for_ram_187 (
    .in_2(decoder_1_out10), .in_3(decoder_2_out11), .in_4(S), .in_5(R), .out_6(out_6), .in_1(in_1));
  R_for_RAM r_for_ram_188 (
    .in_2(decoder_1_out11), .in_3(decoder_2_out11), .in_4(S), .in_5(R), .out_6(out_6), .in_1(in_1));
  R_for_RAM r_for_ram_189 (
    .in_2(decoder_1_out12), .in_3(decoder_2_out11), .in_4(S), .in_5(R), .out_6(out_6), .in_1(in_1));
  R_for_RAM r_for_ram_190 (
    .in_2(decoder_1_out13), .in_3(decoder_2_out11), .in_4(S), .in_5(R), .out_6(out_6), .in_1(in_1));
  R_for_RAM r_for_ram_191 (
    .in_2(decoder_1_out14), .in_3(decoder_2_out11), .in_4(S), .in_5(R), .out_6(out_6), .in_1(in_1));
  R_for_RAM r_for_ram_192 (
    .in_2(decoder_1_out15), .in_3(decoder_2_out11), .in_4(S), .in_5(R), .out_6(out_6), .in_1(in_1));
  R_for_RAM r_for_ram_193 (
    .in_2(decoder_1_out0), .in_3(decoder_2_out12), .in_4(S), .in_5(R), .out_6(out_6), .in_1(in_1));
  R_for_RAM r_for_ram_194 (
    .in_2(decoder_1_out1), .in_3(decoder_2_out12), .in_4(S), .in_5(R), .out_6(out_6), .in_1(in_1));
  R_for_RAM r_for_ram_195 (
    .in_2(decoder_1_out2), .in_3(decoder_2_out12), .in_4(S), .in_5(R), .out_6(out_6), .in_1(in_1));
  R_for_RAM r_for_ram_196 (
    .in_2(decoder_1_out3), .in_3(decoder_2_out12), .in_4(S), .in_5(R), .out_6(out_6), .in_1(in_1));
  R_for_RAM r_for_ram_197 (
    .in_2(decoder_1_out4), .in_3(decoder_2_out12), .in_4(S), .in_5(R), .out_6(out_6), .in_1(in_1));
  R_for_RAM r_for_ram_198 (
    .in_2(decoder_1_out5), .in_3(decoder_2_out12), .in_4(S), .in_5(R), .out_6(out_6));  // open: in_1
  R_for_RAM r_for_ram_199 (
    .in_2(decoder_1_out6), .in_3(decoder_2_out12), .in_4(S), .in_5(R), .out_6(out_6), .in_1(in_1));
  R_for_RAM r_for_ram_200 (
    .in_2(decoder_1_out7), .in_3(decoder_2_out12), .in_4(S), .in_5(R), .out_6(out_6), .in_1(in_1));
  R_for_RAM r_for_ram_201 (
    .in_2(decoder_1_out8), .in_3(decoder_2_out12), .in_4(S), .in_5(R), .out_6(out_6), .in_1(in_1));
  R_for_RAM r_for_ram_202 (
    .in_2(decoder_1_out9), .in_3(decoder_2_out12), .in_4(S), .in_5(R), .out_6(out_6), .in_1(in_1));
  R_for_RAM r_for_ram_203 (
    .in_2(decoder_1_out10), .in_3(decoder_2_out12), .in_4(S), .in_5(R), .out_6(out_6), .in_1(in_1));
  R_for_RAM r_for_ram_204 (
    .in_2(decoder_1_out11), .in_3(decoder_2_out12), .in_4(S), .in_5(R), .out_6(out_6), .in_1(in_1));
  R_for_RAM r_for_ram_205 (
    .in_2(decoder_1_out12), .in_3(decoder_2_out12), .in_4(S), .in_5(R), .out_6(out_6), .in_1(in_1));
  R_for_RAM r_for_ram_206 (
    .in_2(decoder_1_out13), .in_3(decoder_2_out12), .in_4(S), .in_5(R), .out_6(out_6), .in_1(in_1));
  R_for_RAM r_for_ram_207 (
    .in_2(decoder_1_out14), .in_3(decoder_2_out12), .in_4(S), .in_5(R), .out_6(out_6), .in_1(in_1));
  R_for_RAM r_for_ram_208 (
    .in_2(decoder_1_out15), .in_3(decoder_2_out12), .in_4(S), .in_5(R), .out_6(out_6), .in_1(in_1));
  R_for_RAM r_for_ram_209 (
    .in_2(decoder_1_out0), .in_3(decoder_2_out13), .in_4(S), .in_5(R), .out_6(out_6), .in_1(in_1));
  R_for_RAM r_for_ram_210 (
    .in_2(decoder_1_out1), .in_3(decoder_2_out13), .in_4(S), .in_5(R), .out_6(out_6), .in_1(in_1));
  R_for_RAM r_for_ram_211 (
    .in_2(decoder_1_out2), .in_3(decoder_2_out13), .in_4(S), .in_5(R), .out_6(out_6), .in_1(in_1));
  R_for_RAM r_for_ram_212 (
    .in_2(decoder_1_out3), .in_3(decoder_2_out13), .in_4(S), .in_5(R), .out_6(out_6), .in_1(in_1));
  R_for_RAM r_for_ram_213 (
    .in_2(decoder_1_out4), .in_3(decoder_2_out13), .in_4(S), .in_5(R), .out_6(out_6), .in_1(in_1));
  R_for_RAM r_for_ram_214 (
    .in_2(decoder_1_out5), .in_3(decoder_2_out13), .in_4(S), .in_5(R), .out_6(out_6));  // open: in_1
  R_for_RAM r_for_ram_215 (
    .in_2(decoder_1_out6), .in_3(decoder_2_out13), .in_4(S), .in_5(R), .out_6(out_6), .in_1(in_1));
  R_for_RAM r_for_ram_216 (
    .in_2(decoder_1_out7), .in_3(decoder_2_out13), .in_4(S), .in_5(R), .out_6(out_6), .in_1(in_1));
  R_for_RAM r_for_ram_217 (
    .in_2(decoder_1_out8), .in_3(decoder_2_out13), .in_4(S), .in_5(R), .out_6(out_6), .in_1(in_1));
  R_for_RAM r_for_ram_218 (
    .in_2(decoder_1_out9), .in_3(decoder_2_out13), .in_4(S), .in_5(R), .out_6(out_6), .in_1(in_1));
  R_for_RAM r_for_ram_219 (
    .in_2(decoder_1_out10), .in_3(decoder_2_out13), .in_4(S), .in_5(R), .out_6(out_6), .in_1(in_1));
  R_for_RAM r_for_ram_220 (
    .in_2(decoder_1_out11), .in_3(decoder_2_out13), .in_4(S), .in_5(R), .out_6(out_6), .in_1(in_1));
  R_for_RAM r_for_ram_221 (
    .in_2(decoder_1_out12), .in_3(decoder_2_out13), .in_4(S), .in_5(R), .out_6(out_6), .in_1(in_1));
  R_for_RAM r_for_ram_222 (
    .in_2(decoder_1_out13), .in_3(decoder_2_out13), .in_4(S), .in_5(R), .out_6(out_6), .in_1(in_1));
  R_for_RAM r_for_ram_223 (
    .in_2(decoder_1_out14), .in_3(decoder_2_out13), .in_4(S), .in_5(R), .out_6(out_6), .in_1(in_1));
  R_for_RAM r_for_ram_224 (
    .in_2(decoder_1_out15), .in_3(decoder_2_out13), .in_4(S), .in_5(R), .out_6(out_6), .in_1(in_1));
  R_for_RAM r_for_ram_225 (
    .in_2(decoder_1_out0), .in_3(decoder_2_out14), .in_4(S), .in_5(R), .out_6(out_6), .in_1(in_1));
  R_for_RAM r_for_ram_226 (
    .in_2(decoder_1_out1), .in_3(decoder_2_out14), .in_4(S), .in_5(R), .out_6(out_6), .in_1(in_1));
  R_for_RAM r_for_ram_227 (
    .in_2(decoder_1_out2), .in_3(decoder_2_out14), .in_4(S), .in_5(R), .out_6(out_6), .in_1(in_1));
  R_for_RAM r_for_ram_228 (
    .in_2(decoder_1_out3), .in_3(decoder_2_out14), .in_4(S), .in_5(R), .out_6(out_6), .in_1(in_1));
  R_for_RAM r_for_ram_229 (
    .in_2(decoder_1_out4), .in_3(decoder_2_out14), .in_4(S), .in_5(R), .out_6(out_6), .in_1(in_1));
  R_for_RAM r_for_ram_230 (
    .in_2(decoder_1_out5), .in_3(decoder_2_out14), .in_4(S), .in_5(R), .out_6(out_6));  // open: in_1
  R_for_RAM r_for_ram_231 (
    .in_2(decoder_1_out6), .in_3(decoder_2_out14), .in_4(S), .in_5(R), .out_6(out_6), .in_1(in_1));
  R_for_RAM r_for_ram_232 (
    .in_2(decoder_1_out7), .in_3(decoder_2_out14), .in_4(S), .in_5(R), .out_6(out_6), .in_1(in_1));
  R_for_RAM r_for_ram_233 (
    .in_2(decoder_1_out8), .in_3(decoder_2_out14), .in_4(S), .in_5(R), .out_6(out_6), .in_1(in_1));
  R_for_RAM r_for_ram_234 (
    .in_2(decoder_1_out9), .in_3(decoder_2_out14), .in_4(S), .in_5(R), .out_6(out_6), .in_1(in_1));
  R_for_RAM r_for_ram_235 (
    .in_2(decoder_1_out10), .in_3(decoder_2_out14), .in_4(S), .in_5(R), .out_6(out_6), .in_1(in_1));
  R_for_RAM r_for_ram_236 (
    .in_2(decoder_1_out11), .in_3(decoder_2_out14), .in_4(S), .in_5(R), .out_6(out_6), .in_1(in_1));
  R_for_RAM r_for_ram_237 (
    .in_2(decoder_1_out12), .in_3(decoder_2_out14), .in_4(S), .in_5(R), .out_6(out_6), .in_1(in_1));
  R_for_RAM r_for_ram_238 (
    .in_2(decoder_1_out13), .in_3(decoder_2_out14), .in_4(S), .in_5(R), .out_6(out_6), .in_1(in_1));
  R_for_RAM r_for_ram_239 (
    .in_2(decoder_1_out14), .in_3(decoder_2_out14), .in_4(S), .in_5(R), .out_6(out_6), .in_1(in_1));
  R_for_RAM r_for_ram_240 (
    .in_2(decoder_1_out15), .in_3(decoder_2_out14), .in_4(S), .in_5(R), .out_6(out_6), .in_1(in_1));
  R_for_RAM r_for_ram_241 (
    .in_2(decoder_1_out0), .in_3(decoder_2_out15), .in_4(S), .in_5(R), .out_6(out_6), .in_1(in_1));
  R_for_RAM r_for_ram_242 (
    .in_2(decoder_1_out1), .in_3(decoder_2_out15), .in_4(S), .in_5(R), .out_6(out_6), .in_1(in_1));
  R_for_RAM r_for_ram_243 (
    .in_2(decoder_1_out2), .in_3(decoder_2_out15), .in_4(S), .in_5(R), .out_6(out_6), .in_1(in_1));
  R_for_RAM r_for_ram_244 (
    .in_2(decoder_1_out3), .in_3(decoder_2_out15), .in_4(S), .in_5(R), .out_6(out_6), .in_1(in_1));
  R_for_RAM r_for_ram_245 (
    .in_2(decoder_1_out4), .in_3(decoder_2_out15), .in_4(S), .in_5(R), .out_6(out_6), .in_1(in_1));
  R_for_RAM r_for_ram_246 (
    .in_2(decoder_1_out5), .in_3(decoder_2_out15), .in_4(S), .in_5(R), .out_6(out_6), .in_1(in_1));
  R_for_RAM r_for_ram_247 (
    .in_2(decoder_1_out6), .in_3(decoder_2_out15), .in_4(S), .in_5(R), .out_6(out_6), .in_1(in_1));
  R_for_RAM r_for_ram_248 (
    .in_2(decoder_1_out7), .in_3(decoder_2_out15), .in_4(S), .in_5(R), .out_6(out_6), .in_1(in_1));
  R_for_RAM r_for_ram_249 (
    .in_2(decoder_1_out8), .in_3(decoder_2_out15), .in_4(S), .in_5(R), .out_6(out_6), .in_1(in_1));
  R_for_RAM r_for_ram_250 (
    .in_2(decoder_1_out9), .in_3(decoder_2_out15), .in_4(S), .in_5(R), .out_6(out_6), .in_1(in_1));
  R_for_RAM r_for_ram_251 (
    .in_2(decoder_1_out10), .in_3(decoder_2_out15), .in_4(S), .in_5(R), .out_6(out_6), .in_1(in_1));
  R_for_RAM r_for_ram_252 (
    .in_2(decoder_1_out11), .in_3(decoder_2_out15), .in_4(S), .in_5(R), .out_6(out_6), .in_1(in_1));
  R_for_RAM r_for_ram_253 (
    .in_2(decoder_1_out12), .in_3(decoder_2_out15), .in_4(S), .in_5(R), .out_6(out_6), .in_1(in_1));
  R_for_RAM r_for_ram_254 (
    .in_2(decoder_1_out13), .in_3(decoder_2_out15), .in_4(S), .in_5(R), .out_6(out_6), .in_1(in_1));
  R_for_RAM r_for_ram_255 (
    .in_2(decoder_1_out14), .in_3(decoder_2_out15), .in_4(S), .in_5(R), .out_6(out_6), .in_1(in_1));
  R_for_RAM r_for_ram_256 (
    .in_2(decoder_1_out15), .in_3(decoder_2_out15), .in_4(S), .in_5(R), .out_6(out_6), .in_1(in_1));
endmodule

module R_for_RAM (
  input  [7:0] in_1,
  input  in_2,
  input  in_3,
  input  in_4,
  input  in_5,
  output [7:0] out_6
);

  wire and_1_out, and_2_out, and_3_out, b_smallmemory_1_out_10, b_smallmemory_1_out_11,
       b_smallmemory_1_out_12, b_smallmemory_1_out_13, b_smallmemory_1_out_14, b_smallmemory_1_out_15,
       b_smallmemory_1_out_16, b_smallmemory_1_out_17;
  wire [7:0] e_andgroub_1_out_10;

  and and_1 (and_1_out, in_2, in_3);
  and and_2 (and_2_out, and_1_out, in_4);
  and and_3 (and_3_out, and_1_out, in_5);
  B_smallmemory b_smallmemory_1 (
    .in_1(in_1[0]), .in_2(in_1[1]), .in_3(in_1[2]), .in_4(in_1[3]), .in_5(in_1[4]), .in_6(in_1[5]),
    .in_7(in_1[6]), .in_8(in_1[7]), .S(and_2_out), .out_10(b_smallmemory_1_out_10),
    .out_11(b_smallmemory_1_out_11), .out_12(b_smallmemory_1_out_12), .out_13(b_smallmemory_1_out_13),
    .out_14(b_smallmemory_1_out_14), .out_15(b_smallmemory_1_out_15), .out_16(b_smallmemory_1_out_16),
    .out_17(b_smallmemory_1_out_17));
  E_andgroub e_andgroub_1 (
    .in_1(b_smallmemory_1_out_10), .in_2(b_smallmemory_1_out_11), .in_3(b_smallmemory_1_out_12),
    .in_4(b_smallmemory_1_out_13), .in_5(b_smallmemory_1_out_14), .in_6(b_smallmemory_1_out_15),
    .in_7(b_smallmemory_1_out_16), .in_8(b_smallmemory_1_out_17), .in_9(and_3_out),
    .out_10(e_andgroub_1_out_10[0]), .out_11(e_andgroub_1_out_10[1]), .out_12(e_andgroub_1_out_10[2]),
    .out_13(e_andgroub_1_out_10[3]), .out_14(e_andgroub_1_out_10[4]), .out_15(e_andgroub_1_out_10[5]),
    .out_16(e_andgroub_1_out_10[6]), .out_17(e_andgroub_1_out_10[7]));
  assign out_6 = and_3_out ? e_andgroub_1_out_10 : 8'bz;  // Controlled_Buffer controlled_buffer_1
endmodule

module RAM_2 (
  input  [8:0] in_1,
  input  in_2,
  input  [7:0] in_3,
  input  s,
  input  e,
  output [7:0] out_6
);

  wire [8:0] controlled_buffer_1_out;

  assign controlled_buffer_1_out = in_2 ? in_1 : 9'bz;  // Controlled_Buffer controlled_buffer_1
  RAM_part #(.addrWidth(9), .bus("separate")) ram_1 (
    .addr(controlled_buffer_1_out), .din(in_3), .data(out_6), .str(1'b1), .clk(s), .ld(e));  // open: sel, clr
endmodule

module test (
  input  in_1,
  output out_2,
  output out_3,
  output out_4,
  output out_5,
  output out_6,
  output out_7
);

  wire controlled_buffer_1_out, d_ff_7_q, not_1_out, or_1_out, or_2_out;

  D_Flip_Flop d_ff_1 (.clk(in_1), .D(or_1_out), .Q(out_2));  // open: Qn, preset, en, reset
  D_Flip_Flop d_ff_2 (.clk(in_1), .D(out_2), .Q(out_3));  // open: Qn, preset, en, reset
  assign controlled_buffer_1_out = not_1_out ? 1'b1 : 1'bz;  // Controlled_Buffer controlled_buffer_1
  Pull_Resistor pull_resistor_1 (.node(controlled_buffer_1_out));
  D_Flip_Flop d_ff_3 (.clk(in_1), .D(out_3), .Q(out_4));  // open: Qn, preset, en, reset
  D_Flip_Flop d_ff_4 (.clk(in_1), .D(out_4), .Q(out_5));  // open: Qn, preset, en, reset
  or or_1 (or_1_out, d_ff_7_q, controlled_buffer_1_out);
  D_Flip_Flop d_ff_5 (.clk(in_1), .D(out_5), .Q(out_6));  // open: Qn, preset, en, reset
  D_Flip_Flop d_ff_6 (.clk(in_1), .D(out_6), .Q(out_7));  // open: Qn, preset, en, reset
  D_Flip_Flop d_ff_7 (.clk(in_1), .D(out_7), .Q(d_ff_7_q));  // open: Qn, preset, en, reset
  or or_2 (or_2_out, out_2, out_3, out_4, out_5, out_7, d_ff_7_q, out_6);
  not not_1 (not_1_out, or_2_out);
endmodule

module shirft_right (
  input  in_1,
  input  [7:0] in_2,
  output [7:0] out_3,
  output out_4
);


  assign out_3 = {in_2[6:0], in_1};
  assign out_4 = in_2[7];
endmodule

module shift_left (
  input  in_1,
  input  [7:0] in_2,
  output [7:0] out_3,
  output out_4
);


  assign in_2[0] = in_1;
  assign out_3[6:0] = in_2[7:1];
  assign out_4 = out_3[7];
endmodule

module small_COMPARATOR (
  input  in_1,
  input  in_2,
  input  in_3,
  input  in_4,
  output out_5,
  output out_6,
  output out_7
);

  wire and_2_out, not_1_out;

  xor xor_1 (out_5, in_3, in_4);
  not not_1 (not_1_out, out_5);
  and and_1 (out_7, not_1_out, in_1);
  and and_2 (and_2_out, in_1, in_3, out_5);
  or or_1 (out_6, and_2_out, in_2);
endmodule

module _8bitcomparator (
  input  [7:0] in_1,
  input  [7:0] in_2,
  output [7:0] out_3,
  output out_4,
  output out_5
);

  wire small_comparator_1_out_6, small_comparator_1_out_7, small_comparator_2_out_6,
       small_comparator_2_out_7, small_comparator_3_out_6, small_comparator_3_out_7,
       small_comparator_4_out_6, small_comparator_4_out_7, small_comparator_5_out_6,
       small_comparator_5_out_7, small_comparator_6_out_6, small_comparator_6_out_7,
       small_comparator_7_out_6, small_comparator_7_out_7;

  small_COMPARATOR small_comparator_1 (
    .in_3(in_1[0]), .in_4(in_2[0]), .out_5(out_3[0]), .out_6(small_comparator_1_out_6),
    .out_7(small_comparator_1_out_7), .in_1(1'b1), .in_2(1'b0));
  small_COMPARATOR small_comparator_2 (
    .in_3(in_1[1]), .in_4(in_2[1]), .out_5(out_3[1]), .out_6(small_comparator_2_out_6),
    .out_7(small_comparator_2_out_7), .in_1(small_comparator_1_out_7), .in_2(small_comparator_1_out_6));
  small_COMPARATOR small_comparator_3 (
    .in_3(in_1[2]), .in_4(in_2[2]), .out_5(out_3[2]), .out_6(small_comparator_3_out_6),
    .out_7(small_comparator_3_out_7), .in_1(small_comparator_2_out_7), .in_2(small_comparator_2_out_6));
  small_COMPARATOR small_comparator_4 (
    .in_3(in_1[3]), .in_4(in_2[3]), .out_5(out_3[3]), .out_6(small_comparator_4_out_6),
    .out_7(small_comparator_4_out_7), .in_1(small_comparator_3_out_7), .in_2(small_comparator_3_out_6));
  small_COMPARATOR small_comparator_5 (
    .in_3(in_1[4]), .in_4(in_2[4]), .out_5(out_3[4]), .out_6(small_comparator_5_out_6),
    .out_7(small_comparator_5_out_7), .in_1(small_comparator_4_out_7), .in_2(small_comparator_4_out_6));
  small_COMPARATOR small_comparator_6 (
    .in_3(in_1[5]), .in_4(in_2[5]), .out_5(out_3[5]), .out_6(small_comparator_6_out_6),
    .out_7(small_comparator_6_out_7), .in_1(small_comparator_5_out_7), .in_2(small_comparator_5_out_6));
  small_COMPARATOR small_comparator_7 (
    .in_3(in_1[6]), .in_4(in_2[6]), .out_5(out_3[6]), .out_6(small_comparator_7_out_6),
    .out_7(small_comparator_7_out_7), .in_1(small_comparator_6_out_7), .in_2(small_comparator_6_out_6));
  small_COMPARATOR small_comparator_8 (
    .in_3(in_1[7]), .in_4(in_2[7]), .out_5(out_3[7]), .out_6(out_4), .out_7(out_5),
    .in_1(small_comparator_7_out_7), .in_2(small_comparator_7_out_6));
endmodule

module ALU (
  input  [7:0] in_1,
  input  [7:0] in_2,
  input  in_3,
  input  [2:0] in_4,
  output out_5,
  output out_6,
  output out_7,
  output [7:0] out_8,
  output out_9
);

  wire adder_1_cout, and_2_out, and_3_out, and_4_out, decoder_1_out0, decoder_1_out1, decoder_1_out2,
       decoder_1_out3, decoder_1_out4, decoder_1_out5, decoder_1_out6, decoder_1_out7, or_3_out,
       shirft_right_1_out_4, undriven;
  wire [7:0] adder_1_out, and_1_out, n8bitcomparator_1_out_3, not_1_out, or_1_out, shift_left_1_out_3,
       shirft_right_1_out_3, xor_1_out;

  assign not_1_out = ~in_1;  // NOT_Gate not_1, 8 bits wide
  shift_left shift_left_1 (.in_1(undriven), .in_2(in_1), .out_3(shift_left_1_out_3), .out_4(in_3));
  shirft_right shirft_right_1 (.in_1(in_3), .in_2(in_1), .out_3(shirft_right_1_out_3), .out_4(shirft_right_1_out_4));
  Adder adder_1 (.a(in_1), .b(in_2), .out(adder_1_out), .cin(in_3), .cout(adder_1_cout));
  Decoder #(.select(3)) decoder_1 (
    .out0(decoder_1_out0), .out1(decoder_1_out1), .out2(decoder_1_out2), .out3(decoder_1_out3),
    .out4(decoder_1_out4), .out5(decoder_1_out5), .out6(decoder_1_out6), .out7(decoder_1_out7), .sel(in_4));  // open: en
  _8bitcomparator u_8bitcomparator_1 (
    .in_1(in_1), .in_2(in_2), .out_3(n8bitcomparator_1_out_3), .out_4(out_5), .out_5(out_6));
  assign xor_1_out = in_1 ^ in_2;  // XOR_Gate xor_1, 8 bits wide
  assign or_1_out = in_1 | in_2;  // OR_Gate or_1, 8 bits wide
  assign and_1_out = in_1 & in_2;  // AND_Gate and_1, 8 bits wide
  assign out_8 = decoder_1_out0 ? adder_1_out : 8'bz;  // Controlled_Buffer controlled_buffer_1
  assign out_8 = decoder_1_out6 ? xor_1_out : 8'bz;  // Controlled_Buffer controlled_buffer_2
  assign out_8 = decoder_1_out5 ? or_1_out : 8'bz;  // Controlled_Buffer controlled_buffer_3
  assign out_8 = decoder_1_out4 ? and_1_out : 8'bz;  // Controlled_Buffer controlled_buffer_4
  assign out_8 = decoder_1_out3 ? not_1_out : 8'bz;  // Controlled_Buffer controlled_buffer_5
  and and_2 (and_2_out, undriven, decoder_1_out2);
  assign out_8 = decoder_1_out2 ? shift_left_1_out_3 : 8'bz;  // Controlled_Buffer controlled_buffer_6
  and and_3 (and_3_out, shirft_right_1_out_4, decoder_1_out1);
  assign out_8 = decoder_1_out1 ? shirft_right_1_out_3 : 8'bz;  // Controlled_Buffer controlled_buffer_7
  and and_4 (and_4_out, adder_1_cout, decoder_1_out0);
  assign out_8 = decoder_1_out7 ? n8bitcomparator_1_out_3 : 8'bz;  // Controlled_Buffer controlled_buffer_8
  or or_2 (out_9, and_2_out, and_3_out, and_4_out);
  or or_3 (or_3_out, out_8[0], out_8[1], out_8[2], out_8[3], out_8[4], out_8[5], out_8[6], out_8[7]);
  not not_2 (out_7, or_3_out);
endmodule

module E_onepin (
  input  [7:0] in_1,
  input  in_2,
  output [7:0] out_3
);

  D_Flip_Flop d_ff_1 (.clk(in_2), .D(in_1[0]), .Q(out_3[0]));  // open: Qn, preset, en, reset
  D_Flip_Flop d_ff_2 (.clk(in_2), .D(in_1[1]), .Q(out_3[1]));  // open: Qn, preset, en, reset
  D_Flip_Flop d_ff_3 (.clk(in_2), .D(in_1[2]), .Q(out_3[2]));  // open: Qn, preset, en, reset
  D_Flip_Flop d_ff_4 (.clk(in_2), .D(in_1[3]), .Q(out_3[3]));  // open: Qn, preset, en, reset
  D_Flip_Flop d_ff_5 (.clk(in_2), .D(in_1[4]), .Q(out_3[4]));  // open: Qn, preset, en, reset
  D_Flip_Flop d_ff_6 (.clk(in_2), .D(in_1[5]), .Q(out_3[5]));  // open: Qn, preset, en, reset
  D_Flip_Flop d_ff_7 (.clk(in_2), .D(in_1[6]), .Q(out_3[6]));  // open: Qn, preset, en, reset
  D_Flip_Flop d_ff_8 (.clk(in_2), .D(in_1[7]), .Q(out_3[7]));  // open: Qn, preset, en, reset
endmodule

module bus (
  input  [7:0] in_1,
  input  in_2,
  output [7:0] out_3
);

  wire not_1_out;

  and and_1 (out_3[7], in_1[7], not_1_out);
  and and_2 (out_3[6], in_1[6], not_1_out);
  and and_3 (out_3[5], in_1[5], not_1_out);
  and and_4 (out_3[4], in_1[4], not_1_out);
  and and_5 (out_3[3], in_1[3], not_1_out);
  and and_6 (out_3[2], in_1[2], not_1_out);
  and and_7 (out_3[1], in_1[1], not_1_out);
  not not_1 (not_1_out, in_2);
  or or_1 (out_3[0], in_1[0], in_2);
endmodule

module CPU1 (
);

  wire alu_1_out_5, alu_1_out_6, alu_1_out_7, alu_1_out_9, and_1_out, and_2_out, and_3_out, and_4_out,
       b_smallmemory_1_out_10, b_smallmemory_1_out_11, b_smallmemory_1_out_12, b_smallmemory_1_out_13,
       b_smallmemory_1_out_14, b_smallmemory_1_out_15, b_smallmemory_1_out_16, b_smallmemory_1_out_17,
       button_1_out, control_unit_1_acc, control_unit_1_acc_2, control_unit_1_bus1, control_unit_1_flag,
       control_unit_1_i_o_clk_s, control_unit_1_iar, control_unit_1_iar_2, control_unit_1_mar,
       control_unit_1_out_27, control_unit_1_out_36, control_unit_1_out_37, control_unit_1_out_38,
       control_unit_1_r0, control_unit_1_r0_2, control_unit_1_r1, control_unit_1_r1_2, control_unit_1_r2,
       control_unit_1_r2_2, control_unit_1_r3, control_unit_1_r3_2, control_unit_1_ram, control_unit_1_ram_2,
       control_unit_1_tmp, d_ff_1_q, flag_set_1_out_6, flag_set_1_out_7, flag_set_1_out_8, flag_set_1_out_9,
       ir_1_out_3, ir_1_out_4, ir_1_out_5, ir_1_out_6, ir_1_out_7, ir_1_out_8, ir_1_out_9, ir_1_out_10,
       not_1_out, not_2_out, not_3_out, not_4_out, not_5_out, not_6_out, undriven_2, undriven_3, undriven_4,
       undriven_5;
  wire [2:0] undriven;
  wire [7:0] alu_1_out_8, bus_1_out_3, e_onepin_1_out_3, r_1_out_4;

  R r_1 (.in_1(alu_1_out_8), .in_2(control_unit_1_acc_2), .in_3(control_unit_1_acc), .out_4(r_1_out_4));
  E_onepin e_onepin_1 (.in_2(control_unit_1_tmp), .out_3(e_onepin_1_out_3), .in_1(r_1_out_4));
  bus bus_1 (.out_3(bus_1_out_3), .in_1(e_onepin_1_out_3), .in_2(control_unit_1_bus1));
  ALU alu_1 (
    .in_1(r_1_out_4), .in_2(bus_1_out_3), .in_3(flag_set_1_out_6), .in_4(undriven), .out_5(alu_1_out_5),
    .out_6(alu_1_out_6), .out_7(alu_1_out_7), .out_8(alu_1_out_8), .out_9(alu_1_out_9));
  flag_set flag_set_1 (
    .in_1(alu_1_out_9), .in_2(alu_1_out_5), .in_3(alu_1_out_6), .in_4(alu_1_out_7), .out_6(flag_set_1_out_6),
    .out_7(flag_set_1_out_7), .out_8(flag_set_1_out_8), .out_9(flag_set_1_out_9), .in_5(control_unit_1_flag));
  R r_2 (.in_1(r_1_out_4), .in_2(control_unit_1_r0_2), .in_3(control_unit_1_r0), .out_4(r_1_out_4));
  IAR iar_1 (.in_1(r_1_out_4), .in_2(control_unit_1_iar_2), .in_3(control_unit_1_iar), .out_4(r_1_out_4));
  R r_3 (.in_1(r_1_out_4), .in_2(control_unit_1_r1_2), .in_3(control_unit_1_r1), .out_4(r_1_out_4));
  IR ir_1 (
    .out_3(ir_1_out_3), .out_4(ir_1_out_4), .out_5(ir_1_out_5), .out_6(ir_1_out_6), .out_7(ir_1_out_7),
    .out_8(ir_1_out_8), .out_9(ir_1_out_9), .out_10(ir_1_out_10), .in_1(control_unit_1_out_36),
    .in_2(r_1_out_4));
  R r_4 (.in_1(r_1_out_4), .in_2(control_unit_1_r2_2), .in_3(control_unit_1_r2), .out_4(r_1_out_4));
  R r_5 (.in_1(r_1_out_4), .in_2(control_unit_1_r3_2), .in_3(control_unit_1_r3), .out_4(r_1_out_4));
  control_unit control_unit_1 (
    .bus1(control_unit_1_bus1), .IAR(control_unit_1_iar), .RAM(control_unit_1_ram), .ACC(control_unit_1_acc),
    .R0(control_unit_1_r0), .R1(control_unit_1_r1), .R2(control_unit_1_r2), .R3(control_unit_1_r3),
    .in_1(flag_set_1_out_6), .in_2(flag_set_1_out_7), .in_3(flag_set_1_out_8), .in_4(flag_set_1_out_9),
    .MAR(control_unit_1_mar), .IAR_2(control_unit_1_iar_2), .ACC_2(control_unit_1_acc_2),
    .RAM_2(control_unit_1_ram_2), .TMP(control_unit_1_tmp), .FLAG(control_unit_1_flag),
    .i_o_clk_s(control_unit_1_i_o_clk_s), .out_27(control_unit_1_out_27), .R0_2(control_unit_1_r0_2),
    .R1_2(control_unit_1_r1_2), .R2_2(control_unit_1_r2_2), .R3_2(control_unit_1_r3_2),
    .out_36(control_unit_1_out_36), .in_9(ir_1_out_10), .in_8(ir_1_out_9), .in_15(ir_1_out_8),
    .in_14(ir_1_out_7), .in_12(ir_1_out_3), .in_10(ir_1_out_4), .in_13(ir_1_out_5), .in_11(ir_1_out_6),
    .out_37(control_unit_1_out_37), .out_38(control_unit_1_out_38), .in_5(undriven[0]), .in_6(undriven[1]),
    .in_7(undriven[2]));
  RAM ram_1 (
    .in_1(r_1_out_4), .in_2(r_1_out_4), .in_3(control_unit_1_mar), .S(control_unit_1_ram_2),
    .R(control_unit_1_ram), .out_6(r_1_out_4));
  not not_1 (not_1_out, r_1_out_4[7]);
  not not_2 (not_2_out, r_1_out_4[6]);
  not not_3 (not_3_out, r_1_out_4[5]);
  not not_4 (not_4_out, r_1_out_4[4]);
  not not_5 (not_5_out, control_unit_1_out_38);
  not not_6 (not_6_out, control_unit_1_out_37);
  and and_1 (and_1_out, control_unit_1_i_o_clk_s, control_unit_1_out_38, control_unit_1_out_37);
  and and_2 (and_2_out, control_unit_1_out_27, not_5_out, not_6_out);
  and and_3 (and_3_out, not_1_out, not_2_out, not_3_out, not_4_out, r_1_out_4[3], r_1_out_4[2], r_1_out_4[1], r_1_out_4[0]);
  E_andgroub e_andgroub_1 (
    .in_1(b_smallmemory_1_out_10), .in_2(b_smallmemory_1_out_11), .in_3(b_smallmemory_1_out_12),
    .in_4(b_smallmemory_1_out_13), .in_5(b_smallmemory_1_out_14), .in_6(b_smallmemory_1_out_15),
    .in_7(b_smallmemory_1_out_16), .in_8(b_smallmemory_1_out_17), .in_9(and_4_out), .out_10(r_1_out_4[0]),
    .out_11(r_1_out_4[1]), .out_12(r_1_out_4[2]), .out_13(r_1_out_4[3]), .out_14(r_1_out_4[4]),
    .out_15(r_1_out_4[5]), .out_16(r_1_out_4[6]), .out_17(r_1_out_4[7]));
  D_Flip_Flop d_ff_1 (.clk(and_1_out), .D(and_3_out), .Q(d_ff_1_q));  // open: Qn, preset, en, reset
  B_smallmemory b_smallmemory_1 (
    .in_1(button_1_out), .in_2(button_1_out), .in_3(button_1_out), .in_4(button_1_out), .in_5(undriven_5),
    .in_6(undriven_4), .in_7(button_1_out), .in_8(undriven_3), .S(undriven_2),
    .out_10(b_smallmemory_1_out_10), .out_11(b_smallmemory_1_out_11), .out_12(b_smallmemory_1_out_12),
    .out_13(b_smallmemory_1_out_13), .out_14(b_smallmemory_1_out_14), .out_15(b_smallmemory_1_out_15),
    .out_16(b_smallmemory_1_out_16), .out_17(b_smallmemory_1_out_17));
  control_of_kebord control_of_kebord_1 ();
  and and_4 (and_4_out, d_ff_1_q, and_2_out);
  Button button_1 (.out(button_1_out));
  Button button_2 (.out(button_1_out));
  Button button_3 (.out(button_1_out));
  Button button_4 (.out(button_1_out));

  // Notes on the sheet:
  //   TMP
  //   ACC
  //   S
  //   clks
  //   clke
  //   i/o
  //   d/a
  //   b
  //   a
  //   c
  //   d
endmodule

module click (
  output out_1,
  output out_2,
  output out_3,
  output out_4
);

  not not_1 (out_1, out_1);
  or or_1 (out_2, out_1, out_1);
  and and_1 (out_4, out_1, out_1);

  assign out_3 = out_1;
endmodule

module stepper1 (
  input  in_1,
  input  in_2,
  output out_3,
  output out_4,
  output out_5,
  output out_6,
  output out_7,
  output out_8,
  output out_9
);

  wire d_ff_1_q, d_ff_2_q, d_ff_3_q, d_ff_4_q, d_ff_5_q, d_ff_6_q, d_ff_7_q, d_ff_8_q, d_ff_9_q, d_ff_10_q,
       d_ff_11_q, not_1_out, not_2_out, not_3_out, not_4_out, not_5_out, not_6_out, not_7_out, not_8_out,
       or_1_out, or_2_out;

  not not_1 (not_1_out, in_2);
  not not_2 (not_2_out, in_1);
  or or_1 (or_1_out, in_1, not_1_out);
  or or_2 (or_2_out, in_1, in_2);
  or or_3 (out_3, in_1, not_3_out);
  not not_3 (not_3_out, d_ff_2_q);
  D_Flip_Flop d_ff_1 (.clk(or_1_out), .D(not_2_out), .Q(d_ff_1_q));  // open: Qn, preset, en, reset
  and and_1 (out_4, d_ff_2_q, not_4_out);
  D_Flip_Flop d_ff_2 (.clk(or_2_out), .D(d_ff_1_q), .Q(d_ff_2_q));  // open: Qn, preset, en, reset
  D_Flip_Flop d_ff_3 (.clk(or_1_out), .D(d_ff_2_q), .Q(d_ff_3_q));  // open: Qn, preset, en, reset
  not not_4 (not_4_out, d_ff_4_q);
  D_Flip_Flop d_ff_4 (.clk(or_2_out), .D(d_ff_3_q), .Q(d_ff_4_q));  // open: Qn, preset, en, reset
  and and_2 (out_5, d_ff_4_q, not_5_out);
  D_Flip_Flop d_ff_5 (.clk(or_1_out), .D(d_ff_4_q), .Q(d_ff_5_q));  // open: Qn, preset, en, reset
  not not_5 (not_5_out, d_ff_6_q);
  D_Flip_Flop d_ff_6 (.clk(or_2_out), .D(d_ff_5_q), .Q(d_ff_6_q));  // open: Qn, preset, en, reset
  and and_3 (out_6, d_ff_6_q, not_6_out);
  not not_6 (not_6_out, d_ff_8_q);
  D_Flip_Flop d_ff_7 (.clk(or_1_out), .D(d_ff_6_q), .Q(d_ff_7_q));  // open: Qn, preset, en, reset
  D_Flip_Flop d_ff_8 (.clk(or_2_out), .D(d_ff_7_q), .Q(d_ff_8_q));  // open: Qn, preset, en, reset
  and and_4 (out_7, d_ff_8_q, not_7_out);
  not not_7 (not_7_out, d_ff_10_q);
  D_Flip_Flop d_ff_9 (.clk(or_1_out), .D(d_ff_8_q), .Q(d_ff_9_q));  // open: Qn, preset, en, reset
  and and_5 (out_8, d_ff_10_q, not_8_out);
  D_Flip_Flop d_ff_10 (.clk(or_2_out), .D(d_ff_9_q), .Q(d_ff_10_q));  // open: Qn, preset, en, reset
  D_Flip_Flop d_ff_11 (.clk(or_1_out), .D(d_ff_10_q), .Q(d_ff_11_q));  // open: Qn, preset, en, reset
  not not_8 (not_8_out, out_9);
  D_Flip_Flop d_ff_12 (.clk(or_2_out), .D(d_ff_11_q), .Q(out_9));  // open: Qn, preset, en, reset
endmodule

module control1 (
);

  wire and_1_out, and_2_out, and_3_out, and_4_out, and_5_out, and_6_out, click_1_out_2, click_1_out_3,
       click_1_out_4, test_1_out_2, test_1_out_3, test_1_out_4, test_1_out_5, test_1_out_6, test_1_out_7,
       undriven, undriven_2, undriven_3, undriven_4, undriven_5, undriven_6, undriven_7, undriven_8,
       undriven_9, undriven_10, undriven_11, undriven_12, undriven_13;

  click click_1 (.out_3(click_1_out_3), .out_2(click_1_out_2), .out_4(click_1_out_4));  // open: out_1
  and and_1 (and_1_out, undriven, click_1_out_2);
  and and_2 (and_2_out, undriven_2, click_1_out_2);
  and and_3 (and_3_out, undriven_3, click_1_out_2);
  and and_4 (and_4_out, undriven_4, click_1_out_2);
  and and_5 (and_5_out, undriven_5, click_1_out_2);
  and and_6 (and_6_out, undriven_6, click_1_out_2);
  test test_1 (
    .out_2(test_1_out_2), .out_3(test_1_out_3), .out_4(test_1_out_4), .out_5(test_1_out_5),
    .out_6(test_1_out_6), .out_7(test_1_out_7), .in_1(click_1_out_3));
  // AND_Gate and_7 has open pins: in0=click_1_out_4, in1=undriven_7, out=open
  // AND_Gate and_8 has open pins: in0=click_1_out_4, in1=undriven_8, out=open
  // AND_Gate and_9 has open pins: in0=click_1_out_4, in1=undriven_9, out=open
  // AND_Gate and_10 has open pins: in0=click_1_out_4, in1=undriven_10, out=open
  // AND_Gate and_11 has open pins: in0=click_1_out_4, in1=undriven_11, out=open
  // AND_Gate and_12 has open pins: in0=click_1_out_4, in1=undriven_12, out=open
  // AND_Gate and_13 has open pins: in0=click_1_out_4, in1=undriven_13, out=open
  // AND_Gate and_14 has open pins: in0=click_1_out_4, out=open

  // Notes on the sheet:
  //   BUS1
  //   ALL ENABL
  //   RAM
  //   ACC
  //   R0
  //   R1
  //   R2
  //   R3
  //   ALL SET
  //   MAR
  //   ACC
  //   RAM
  //   TMP
  //   R0
  //   R1
  //   R2
  //   R3
endmodule

module IR (
  input  in_1,
  input  [7:0] in_2,
  output out_3,
  output out_4,
  output out_5,
  output out_6,
  output out_7,
  output out_8,
  output out_9,
  output out_10
);

  wire d_ff_1_qn, d_ff_3_qn, d_ff_5_qn, d_ff_7_qn;

  D_Flip_Flop d_ff_1 (.clk(in_1), .D(in_2[7]), .Q(out_3), .Qn(d_ff_1_qn));  // open: preset, en, reset
  D_Flip_Flop d_ff_2 (.clk(in_1), .D(in_2[6]), .Q(out_4));  // open: Qn, preset, en, reset
  D_Flip_Flop d_ff_3 (.clk(in_1), .D(in_2[5]), .Q(out_5), .Qn(d_ff_3_qn));  // open: preset, en, reset
  D_Flip_Flop d_ff_4 (.clk(in_1), .D(in_2[4]), .Q(out_6));  // open: Qn, preset, en, reset
  D_Flip_Flop d_ff_5 (.clk(in_1), .D(in_2[3]), .Q(out_7), .Qn(d_ff_5_qn));  // open: preset, en, reset
  D_Flip_Flop d_ff_6 (.clk(in_1), .D(in_2[2]), .Q(out_8));  // open: Qn, preset, en, reset
  D_Flip_Flop d_ff_7 (.clk(in_1), .D(in_2[1]), .Q(out_9), .Qn(d_ff_7_qn));  // open: preset, en, reset
  D_Flip_Flop d_ff_8 (.clk(in_1), .D(in_2[0]), .Q(out_10));  // open: Qn, preset, en, reset
endmodule

module IAR (
  input  [7:0] in_1,
  input  in_2,
  input  in_3,
  output [7:0] out_4
);

  wire b_smallmemory_1_out_10, b_smallmemory_1_out_11, b_smallmemory_1_out_12, b_smallmemory_1_out_13,
       b_smallmemory_1_out_14, b_smallmemory_1_out_15, b_smallmemory_1_out_16, b_smallmemory_1_out_17;
  wire [7:0] e_andgroub_1_out_10;

  B_smallmemory b_smallmemory_1 (
    .in_1(in_1[0]), .in_2(in_1[1]), .in_3(in_1[2]), .in_4(in_1[3]), .in_5(in_1[4]), .in_6(in_1[5]),
    .in_7(in_1[6]), .in_8(in_1[7]), .S(in_2), .out_10(b_smallmemory_1_out_10),
    .out_11(b_smallmemory_1_out_11), .out_12(b_smallmemory_1_out_12), .out_13(b_smallmemory_1_out_13),
    .out_14(b_smallmemory_1_out_14), .out_15(b_smallmemory_1_out_15), .out_16(b_smallmemory_1_out_16),
    .out_17(b_smallmemory_1_out_17));
  E_andgroub e_andgroub_1 (
    .in_1(b_smallmemory_1_out_10), .in_2(b_smallmemory_1_out_11), .in_3(b_smallmemory_1_out_12),
    .in_4(b_smallmemory_1_out_13), .in_5(b_smallmemory_1_out_14), .in_6(b_smallmemory_1_out_15),
    .in_7(b_smallmemory_1_out_16), .in_8(b_smallmemory_1_out_17), .in_9(in_3),
    .out_10(e_andgroub_1_out_10[0]), .out_11(e_andgroub_1_out_10[1]), .out_12(e_andgroub_1_out_10[2]),
    .out_13(e_andgroub_1_out_10[3]), .out_14(e_andgroub_1_out_10[4]), .out_15(e_andgroub_1_out_10[5]),
    .out_16(e_andgroub_1_out_10[6]), .out_17(e_andgroub_1_out_10[7]));
  assign out_4 = in_3 ? e_andgroub_1_out_10 : 8'bz;  // Controlled_Buffer controlled_buffer_1
endmodule

module control2 (
);

  wire and_1_out, and_2_out, and_3_out, and_4_out, and_5_out, and_6_out, and_7_out, click_1_out_2,
       click_1_out_3, click_1_out_4, test_1_out_2, test_1_out_3, test_1_out_4;

  click click_1 (.out_3(click_1_out_3), .out_2(click_1_out_2), .out_4(click_1_out_4));  // open: out_1
  and and_1 (and_1_out, click_1_out_2, test_1_out_2);
  and and_2 (and_2_out, click_1_out_2, test_1_out_3);
  and and_3 (and_3_out, click_1_out_2, test_1_out_4);
  test test_1 (
    .out_2(test_1_out_2), .out_3(test_1_out_3), .out_4(test_1_out_4), .in_1(click_1_out_3));  // open: out_5, out_6, out_7
  and and_4 (and_4_out, test_1_out_3, click_1_out_4);
  and and_5 (and_5_out, test_1_out_2, click_1_out_4);
  and and_6 (and_6_out, test_1_out_4, click_1_out_4);
  and and_7 (and_7_out, test_1_out_2, click_1_out_4);

  // Notes on the sheet:
  //   bus1
  //   LAR
  //   RAM
  //   ACC
  //   IR
  //   MAR
  //   LAR
  //   ACC
endmodule

module control3 (
  input  clk_s,
  input  clk_e,
  input  reg_b,
  input  reg_b_2,
  input  reg_a,
  input  in_6,
  input  in_7,
  input  in_8,
  input  in_9,
  output R0,
  output R1,
  output R2,
  output R3
);

  wire and_1_out, and_2_out, and_3_out, and_4_out, and_5_out, and_6_out, and_7_out, and_8_out, and_9_out,
       and_10_out, and_11_out, and_12_out, decoder_1_out0, decoder_1_out1, decoder_1_out2, decoder_1_out3,
       decoder_2_out0, decoder_2_out1, decoder_2_out2, decoder_2_out3, decoder_3_out0, decoder_3_out1,
       decoder_3_out2, decoder_3_out3;

  or or_1 (R0, and_5_out, and_1_out);
  or or_2 (R1, and_2_out, and_6_out);
  or or_3 (R2, and_3_out, and_7_out);
  or or_4 (R3, and_4_out, and_8_out);
  and and_1 (and_1_out, decoder_1_out0, clk_e, reg_b_2);
  and and_2 (and_2_out, decoder_1_out1, clk_e, reg_b_2);
  and and_3 (and_3_out, decoder_1_out2, clk_e, reg_b_2);
  and and_4 (and_4_out, decoder_1_out3, clk_e, reg_b_2);
  and and_5 (and_5_out, decoder_2_out0, clk_e, reg_a);
  and and_6 (and_6_out, decoder_2_out1, clk_e, reg_a);
  and and_7 (and_7_out, decoder_2_out2, clk_e, reg_a);
  and and_8 (and_8_out, decoder_2_out3, clk_e, reg_a);
  Decoder #(.select(2)) decoder_1 (
    .out0(decoder_1_out0), .out1(decoder_1_out1), .out2(decoder_1_out2), .out3(decoder_1_out3),
    .sel({in_8, in_9}));  // open: en
  Decoder #(.select(2)) decoder_2 (
    .out0(decoder_2_out0), .out1(decoder_2_out1), .out2(decoder_2_out2), .out3(decoder_2_out3),
    .sel({in_6, in_7}));  // open: en
  Decoder #(.select(2)) decoder_3 (
    .out0(decoder_3_out0), .out1(decoder_3_out1), .out2(decoder_3_out2), .out3(decoder_3_out3),
    .sel({in_8, in_9}));  // open: en
  and and_9 (and_9_out, decoder_3_out0, clk_s, reg_b);
  and and_10 (and_10_out, decoder_3_out1, clk_s, reg_b);
  and and_11 (and_11_out, decoder_3_out2, clk_s, reg_b);
  and and_12 (and_12_out, decoder_3_out3, clk_s, reg_b);

  // Notes on the sheet:
  //   R0
  //   R1
  //   R2
  //   R3
endmodule

module control4 (
);

  wire and_1_out, and_2_out, and_3_out, and_4_out, and_5_out, and_6_out, and_7_out, and_8_out, and_9_out,
       and_10_out, and_11_out, and_12_out, and_13_out, click_1_out_2, click_1_out_3, click_1_out_4,
       ir_1_out_3, ir_1_out_4, ir_1_out_5, ir_1_out_6, not_1_out, test_1_out_5, test_1_out_7;

  click click_1 (.out_3(click_1_out_3), .out_2(click_1_out_2), .out_4(click_1_out_4));  // open: out_1
  and and_1 (and_1_out, and_7_out, click_1_out_2);
  and and_2 (and_2_out, and_8_out, click_1_out_2);
  and and_3 (and_3_out, and_10_out, click_1_out_2);
  and and_4 (and_4_out, ir_1_out_3, ir_1_out_3, ir_1_out_6);
  and and_5 (and_5_out, ir_1_out_3, ir_1_out_3, ir_1_out_5);
  and and_6 (and_6_out, ir_1_out_3, ir_1_out_3, ir_1_out_4);
  IR ir_1 (
    .out_3(ir_1_out_3), .out_4(ir_1_out_4), .out_5(ir_1_out_5), .out_6(ir_1_out_6));  // open: out_7, out_8, out_9, out_10, in_1, in_2
  test test_1 (
    .out_5(test_1_out_5), .out_6(ir_1_out_3), .out_7(test_1_out_7), .in_1(click_1_out_3));  // open: out_2, out_3, out_4
  and and_7 (and_7_out, test_1_out_5, ir_1_out_3);
  and and_8 (and_8_out, ir_1_out_3, ir_1_out_3);
  and and_9 (and_9_out, ir_1_out_6, ir_1_out_5, ir_1_out_4);
  not not_1 (not_1_out, and_9_out);
  and and_10 (and_10_out, test_1_out_7, ir_1_out_3, not_1_out);
  and and_11 (and_11_out, and_7_out, click_1_out_4);
  and and_12 (and_12_out, and_8_out, click_1_out_4);
  and and_13 (and_13_out, and_10_out, click_1_out_4);

  // Notes on the sheet:
  //   ALU
  //   reg b
  //   reg a
  //   ACC
  //   TMP
  //   ACC
  //   REG B
endmodule

module control5 (
);

  wire and_1_out, and_2_out, and_9_out, and_10_out, and_11_out, and_12_out, decoder_1_out0, decoder_1_out1,
       decoder_1_out2, decoder_1_out3, decoder_1_out4, decoder_1_out5, decoder_1_out6, decoder_1_out7,
       ir_1_out_3, not_1_out, test_1_out_5, test_1_out_6;
  wire [2:0] ir_1_out_6;

  not not_1 (not_1_out, ir_1_out_3);
  IR ir_1 (
    .out_3(ir_1_out_3), .out_4(ir_1_out_6[2]), .out_5(ir_1_out_6[1]), .out_6(ir_1_out_6[0]));  // open: out_7, out_8, out_9, out_10, in_1, in_2
  Decoder #(.select(3)) decoder_1 (
    .out0(decoder_1_out0), .out1(decoder_1_out1), .out2(decoder_1_out2), .out3(decoder_1_out3),
    .out4(decoder_1_out4), .out5(decoder_1_out5), .out6(decoder_1_out6), .out7(decoder_1_out7),
    .sel(ir_1_out_6));  // open: en
  and and_1 (and_1_out, decoder_1_out0, not_1_out);
  and and_2 (and_2_out, decoder_1_out1, not_1_out);
  // AND_Gate and_3 has open pins: in0=decoder_1_out2, in1=not_1_out, out=open
  // AND_Gate and_4 has open pins: in0=decoder_1_out3, in1=not_1_out, out=open
  // AND_Gate and_5 has open pins: in0=decoder_1_out4, in1=not_1_out, out=open
  // AND_Gate and_6 has open pins: in0=decoder_1_out5, in1=not_1_out, out=open
  // AND_Gate and_7 has open pins: in0=decoder_1_out6, in1=not_1_out, out=open
  // AND_Gate and_8 has open pins: in0=decoder_1_out7, in1=not_1_out, out=open
  test test_1 (.out_5(test_1_out_5), .out_6(test_1_out_6));  // open: out_2, out_3, out_4, out_7, in_1
  and and_9 (and_9_out, test_1_out_5, and_1_out);
  and and_10 (and_10_out, test_1_out_5, and_2_out);
  and and_11 (and_11_out, test_1_out_6, and_1_out);
  and and_12 (and_12_out, test_1_out_6, and_2_out);

  // Notes on the sheet:
  //   REG A
  //   RAM
  //   REG A
  //   REG B
  //   MAR
  //   REG B
  //   RAM
  //   MAR
endmodule

module control_unit (
  input  in_1,
  input  in_2,
  input  in_3,
  input  in_4,
  input  in_5,
  input  in_6,
  input  in_7,
  input  in_8,
  input  in_9,
  input  in_10,
  input  in_11,
  input  in_12,
  input  in_13,
  input  in_14,
  input  in_15,
  output bus1,
  output IAR,
  output RAM,
  output MAR,
  output ACC,
  output IAR_2,
  output ACC_2,
  output RAM_2,
  output TMP,
  output FLAG,
  output i_o_clk_s,
  output out_27,
  output R0,
  output R1,
  output R0_2,
  output R2,
  output R1_2,
  output R3,
  output R2_2,
  output R3_2,
  output out_36,
  output out_37,
  output out_38
);

  wire and_4_out, and_5_out, and_6_out, and_7_out, and_8_out, and_9_out, and_10_out, and_11_out, and_15_out,
       and_16_out, and_17_out, and_18_out, and_19_out, and_20_out, and_21_out, and_22_out, and_23_out,
       and_24_out, and_25_out, and_26_out, and_27_out, and_28_out, and_29_out, and_30_out, and_31_out,
       and_32_out, and_33_out, and_34_out, and_35_out, and_36_out, and_37_out, and_38_out, and_39_out,
       and_40_out, and_41_out, and_42_out, and_43_out, and_44_out, and_45_out, and_46_out, click_1_out_2,
       click_1_out_3, click_1_out_4, decoder_1_out0, decoder_1_out1, decoder_1_out2, decoder_1_out3,
       decoder_2_out0, decoder_2_out1, decoder_2_out2, decoder_2_out3, decoder_3_out0, decoder_3_out1,
       decoder_3_out2, decoder_3_out3, decoder_3_out4, decoder_3_out5, decoder_3_out6, decoder_3_out7,
       decoder_4_out0, decoder_4_out1, decoder_4_out2, decoder_4_out3, not_1_out, not_2_out, not_3_out,
       or_6_out, or_7_out, or_8_out, or_9_out, or_10_out, or_11_out, or_12_out, or_13_out, or_14_out,
       or_15_out, or_16_out, test_1_out_2, test_1_out_3, test_1_out_4, test_1_out_5, test_1_out_6,
       test_1_out_7, undriven;

  or or_1 (R0, and_8_out, and_4_out);
  or or_2 (R1, and_5_out, and_9_out);
  or or_3 (R2, and_6_out, and_10_out);
  or or_4 (R3, and_7_out, and_11_out);
  click click_1 (.out_3(click_1_out_3), .out_2(click_1_out_2), .out_4(click_1_out_4));  // open: out_1
  and and_1 (IAR, or_6_out, click_1_out_2);
  and and_2 (RAM, or_7_out, click_1_out_2);
  and and_3 (ACC, or_8_out, click_1_out_2);
  and and_4 (and_4_out, decoder_1_out0, click_1_out_2, or_9_out);
  and and_5 (and_5_out, decoder_1_out1, click_1_out_2, or_9_out);
  and and_6 (and_6_out, decoder_1_out2, click_1_out_2, or_9_out);
  and and_7 (and_7_out, decoder_1_out3, click_1_out_2, or_9_out);
  and and_8 (and_8_out, decoder_2_out0, click_1_out_2, or_10_out);
  and and_9 (and_9_out, decoder_2_out1, click_1_out_2, or_10_out);
  and and_10 (and_10_out, decoder_2_out2, click_1_out_2, or_10_out);
  and and_11 (and_11_out, decoder_2_out3, click_1_out_2, or_10_out);
  or or_5 (bus1, test_1_out_2, and_15_out, and_36_out, and_41_out);
  or or_6 (or_6_out, test_1_out_2, and_15_out, and_21_out, and_36_out);
  or or_7 (or_7_out, test_1_out_3, and_42_out, and_40_out, and_17_out, and_22_out);
  or or_8 (or_8_out, test_1_out_4, and_46_out, and_18_out, and_37_out);
  or or_9 (or_9_out, and_19_out, and_43_out, and_16_out, undriven);
  or or_10 (or_10_out, and_20_out, and_35_out, and_39_out, and_44_out);
  Decoder #(.select(2)) decoder_1 (
    .out0(decoder_1_out0), .out1(decoder_1_out1), .out2(decoder_1_out2), .out3(decoder_1_out3),
    .sel({in_8, in_9}));  // open: en
  Decoder #(.select(2)) decoder_2 (
    .out0(decoder_2_out0), .out1(decoder_2_out1), .out2(decoder_2_out2), .out3(decoder_2_out3),
    .sel({in_14, in_15}));  // open: en
  and and_12 (in_5, test_1_out_6, in_12, in_11);
  and and_13 (in_6, test_1_out_6, in_12, in_13);
  and and_14 (in_7, test_1_out_6, in_12, in_10);
  and and_15 (and_15_out, test_1_out_5, and_25_out);
  and and_16 (and_16_out, test_1_out_5, and_26_out);
  and and_17 (and_17_out, test_1_out_6, and_25_out);
  and and_18 (and_18_out, test_1_out_7, and_25_out);
  and and_19 (and_19_out, test_1_out_5, in_12);
  and and_20 (and_20_out, test_1_out_6, in_12);
  and and_21 (and_21_out, test_1_out_5, and_27_out);
  not not_1 (not_1_out, in_12);
  and and_22 (and_22_out, test_1_out_6, and_27_out);
  Decoder #(.select(3)) decoder_3 (
    .out0(decoder_3_out0), .out1(decoder_3_out1), .out2(decoder_3_out2), .out3(decoder_3_out3),
    .out4(decoder_3_out4), .out5(decoder_3_out5), .out6(decoder_3_out6), .out7(decoder_3_out7),
    .sel({in_10, in_13, in_11}));  // open: en
  test test_1 (
    .out_2(test_1_out_2), .out_3(test_1_out_3), .out_4(test_1_out_4), .out_5(test_1_out_5),
    .out_6(test_1_out_6), .out_7(test_1_out_7), .in_1(click_1_out_3));
  and and_23 (and_23_out, decoder_3_out0, not_1_out);
  and and_24 (and_24_out, decoder_3_out1, not_1_out);
  and and_25 (and_25_out, decoder_3_out2, not_1_out);
  and and_26 (and_26_out, decoder_3_out3, not_1_out);
  and and_27 (and_27_out, decoder_3_out4, not_1_out);
  and and_28 (and_28_out, decoder_3_out5, not_1_out);
  and and_29 (and_29_out, decoder_3_out6, not_1_out);
  and and_30 (and_30_out, decoder_3_out7, not_1_out);
  and and_31 (and_31_out, in_1, in_14);
  and and_32 (and_32_out, in_2, in_15);
  and and_33 (and_33_out, in_3, in_8);
  and and_34 (and_34_out, in_4, in_9);
  and and_35 (and_35_out, test_1_out_5, and_23_out);
  and and_36 (and_36_out, test_1_out_5, and_28_out);
  and and_37 (and_37_out, test_1_out_6, and_28_out);
  or or_11 (or_11_out, and_31_out, and_32_out, and_33_out, and_34_out);
  and and_38 (and_38_out, in_11, in_13, in_10);
  and and_39 (and_39_out, test_1_out_5, and_24_out);
  and and_40 (and_40_out, test_1_out_7, or_11_out, and_28_out);
  not not_2 (not_2_out, and_38_out);
  and and_41 (and_41_out, test_1_out_5, and_29_out);
  and and_42 (and_42_out, test_1_out_6, and_23_out);
  and and_43 (and_43_out, test_1_out_6, and_24_out);
  and and_44 (and_44_out, test_1_out_5, in_14, and_30_out);
  not not_3 (not_3_out, in_14);
  and and_45 (and_45_out, and_30_out, not_3_out, test_1_out_6);
  and and_46 (and_46_out, test_1_out_7, in_12, not_2_out);
  or or_12 (or_12_out, test_1_out_4, and_18_out, and_16_out, and_22_out, and_40_out);
  or or_13 (or_13_out, test_1_out_2, and_20_out, and_15_out, and_36_out);
  or or_14 (or_14_out, and_41_out, and_20_out);
  or or_15 (or_15_out, and_42_out, and_17_out, and_45_out, and_46_out);
  Decoder #(.select(2)) decoder_4 (
    .out0(decoder_4_out0), .out1(decoder_4_out1), .out2(decoder_4_out2), .out3(decoder_4_out3),
    .sel({in_8, in_9}));  // open: en
  or or_16 (or_16_out, test_1_out_2, and_35_out, and_21_out, and_43_out, and_15_out, and_36_out);
  and and_47 (out_36, test_1_out_3, click_1_out_4);
  and and_48 (MAR, or_16_out, click_1_out_4);
  and and_49 (IAR_2, or_12_out, click_1_out_4);
  and and_50 (ACC_2, or_13_out, click_1_out_4);
  and and_51 (RAM_2, and_39_out, click_1_out_4);
  and and_52 (TMP, and_19_out, click_1_out_4);
  and and_53 (FLAG, or_14_out, click_1_out_4);
  and and_54 (i_o_clk_s, click_1_out_4, and_44_out);
  and and_55 (out_27, click_1_out_2, and_45_out);
  and and_56 (R0_2, decoder_4_out0, click_1_out_4, or_15_out);
  and and_57 (R1_2, decoder_4_out1, click_1_out_4, or_15_out);
  and and_58 (R2_2, decoder_4_out2, click_1_out_4, or_15_out);
  and and_59 (R3_2, decoder_4_out3, click_1_out_4, or_15_out);

  assign out_37 = in_14;
  assign out_38 = in_15;

  // Notes on the sheet:
  //   ALU
  //   enables
  //   BUS1
  //   carry out
  //   a larger
  //   equal
  //   zero
  //   S 1
  //   reg b
  //   reg a
  //   s4
  //   s5
  //   s4
  //   s4
  //   s6
  //   S 1
  //   S 1
  //   s6
  //   s7
  //   s7
  //   s3
  //   s3
  //   s7
  //   S 1
  //   s7
  //   input/output
  //   s3
  //   data/ address
  //   s3
  //   S 1
  //   reg b
  //   sets
  //   IR
  //   i/o clk e
endmodule

module flag_set (
  input  in_1,
  input  in_2,
  input  in_3,
  input  in_4,
  input  in_5,
  output out_6,
  output out_7,
  output out_8,
  output out_9
);

  Pull_Resistor pull_resistor_1 (.node(in_1));
  Pull_Resistor pull_resistor_2 (.node(in_4));
  D_Flip_Flop d_ff_1 (.clk(in_5), .D(in_1), .Q(out_6));  // open: Qn, preset, en, reset
  D_Flip_Flop d_ff_2 (.clk(in_5), .D(in_2), .Q(out_7));  // open: Qn, preset, en, reset
  D_Flip_Flop d_ff_3 (.clk(in_5), .D(in_3), .Q(out_8));  // open: Qn, preset, en, reset
  D_Flip_Flop d_ff_4 (.clk(in_5), .D(in_4), .Q(out_9));  // open: Qn, preset, en, reset
endmodule
